// Logisim project cpu_attempt_1.circ as structural Verilog: 12 circuits, main circuit main
module main (
);

  wire alu_1_ra_c_1, alu_1_ra_c_2, alu_1_ra_c_3, alu_1_ra_c_4, alu_1_ra_o_1, alu_1_ra_o_2, alu_1_ra_o_3,
       alu_1_ra_o_4, alu_1_rb_c_1, alu_1_rb_c_2, alu_1_rb_c_3, alu_1_rb_c_4, alu_1_rb_o_1, alu_1_rb_o_2,
       alu_1_rb_o_3, alu_1_rb_o_4, alu_1_rd_c_1, alu_1_rd_c_2, alu_1_rd_c_3, alu_1_rd_c_4, alu_1_rd_o_1,
       alu_1_rd_o_2, alu_1_rd_o_3, alu_1_rd_o_4, and_1_out, and_2_out, and_3_out, and_4_out, and_5_out,
       and_6_out, and_7_out, and_8_out, and_9_out, and_10_out, and_11_out, and_12_out, and_13_out,
       and_14_out, and_15_out, and_16_out, and_17_out, and_18_out, and_19_out, and_20_out, and_21_out,
       and_22_out, and_23_out, and_24_out, and_25_out, and_26_out, and_27_out, and_28_out, and_29_out,
       and_30_out, and_31_out, and_32_out, and_33_out, and_34_out, button_1_out, button_2_out, button_3_out,
       button_4_out, button_5_out, button_6_out, button_7_out, button_8_out, button_9_out, button_10_out,
       button_11_out, button_12_out, button_13_out, button_14_out, button_15_out, button_16_out,
       button_17_out, button_18_out, button_19_out, button_20_out, button_21_out, button_22_out,
       button_23_out, button_24_out, button_25_out, button_26_out, button_27_out, button_28_out,
       button_29_out, button_30_out, button_31_out, clock_1_out, clock_2_out, counter_14_1_clk_a, d_ff_1_q,
       d_ff_2_q, d_ff_3_q, d_ff_4_q, d_ff_5_q, d_ff_6_q, d_ff_7_q, d_ff_8_q, d_ff_9_q, d_ff_10_q, d_ff_11_q,
       d_ff_12_q, d_ff_13_q, d_ff_14_q, d_ff_15_q, d_ff_16_q, d_ff_17_q, d_ff_18_q, d_ff_19_q, d_ff_20_q,
       d_ff_21_q, d_ff_22_q, d_ff_23_q, d_ff_24_q, d_ff_25_q, d_ff_26_q, d_ff_27_q, d_ff_28_q, d_ff_29_q,
       d_ff_30_q, d_ff_31_q, d_ff_32_q, d_ff_33_q, d_ff_34_q, d_ff_35_q, d_ff_36_q, d_ff_37_q, d_ff_38_q,
       d_ff_39_q, d_ff_40_q, d_ff_41_q, d_ff_42_q, d_ff_43_q, d_ff_44_q, d_ff_45_q, d_ff_46_q, d_ff_47_q,
       d_ff_48_q, d_ff_49_q, d_ff_50_q, d_ff_51_q, d_ff_52_q, d_ff_53_q, d_ff_54_q, d_ff_55_q, d_ff_56_q,
       d_ff_57_q, d_ff_58_q, d_ff_59_q, d_ff_60_q, d_ff_61_q, d_ff_62_q, d_ff_63_q, d_ff_64_q, d_ff_65_q,
       d_ff_66_q, d_ff_67_q, d_ff_68_q, d_ff_69_q, d_ff_70_q, d_ff_71_q, d_ff_72_q, d_ff_73_q, d_ff_74_q,
       d_ff_75_q, d_ff_76_q, d_ff_77_q, d_ff_78_q, d_ff_79_q, d_ff_80_q, d_ff_81_q, d_ff_82_q, d_ff_83_q,
       d_ff_84_q, d_ff_85_q, d_ff_86_q, d_ff_87_q, d_ff_88_q, d_ff_89_q, d_ff_90_q, d_ff_91_q, d_ff_92_q,
       d_ff_93_q, d_ff_94_q, d_ff_95_q, d_ff_96_q, d_ff_97_q, d_ff_98_q, d_ff_99_q, d_ff_100_q, d_ff_101_q,
       d_ff_102_q, d_ff_103_q, d_ff_104_q, d_ff_105_q, d_ff_106_q, d_ff_107_q, d_ff_108_q, d_ff_109_q,
       d_ff_110_q, d_ff_111_q, d_ff_112_q, d_ff_113_q, d_ff_114_q, d_ff_115_q, d_ff_116_q, d_ff_117_q,
       d_ff_118_q, d_ff_119_q, d_ff_120_q, d_ff_121_q, d_ff_122_q, d_ff_123_q, d_ff_124_q, d_ff_125_q,
       d_ff_126_q, d_ff_127_q, d_ff_128_q, d_ff_129_q, d_ff_130_q, d_ff_131_q, d_ff_132_q, d_ff_133_q,
       d_ff_134_q, d_ff_135_q, d_ff_136_q, d_ff_137_q, d_ff_138_q, d_ff_139_q, d_ff_140_q, d_ff_141_q,
       d_ff_142_q, d_ff_143_q, d_ff_144_q, d_ff_145_q, d_ff_146_q, d_ff_147_q, d_ff_148_q, d_ff_149_q,
       d_ff_150_q, d_ff_151_q, d_ff_152_q, d_ff_153_q, d_ff_154_q, d_ff_155_q, d_ff_156_q, d_ff_157_q,
       d_ff_158_q, d_ff_159_q, d_ff_160_q, d_ff_161_q, d_ff_162_q, d_ff_163_q, d_ff_164_q, d_ff_165_q,
       d_ff_166_q, d_ff_167_q, d_ff_168_q, d_ff_169_q, d_ff_170_q, d_ff_171_q, d_ff_172_q, d_ff_173_q,
       d_ff_174_q, d_ff_175_q, d_ff_176_q, d_ff_177_q, d_ff_178_q, d_ff_179_q, d_ff_180_q, d_ff_181_q,
       d_ff_182_q, d_ff_183_q, d_ff_184_q, d_ff_185_q, d_ff_186_q, d_ff_187_q, d_ff_188_q, d_ff_189_q,
       d_ff_190_q, d_ff_191_q, d_ff_192_q, d_ff_193_q, d_ff_194_q, d_ff_195_q, d_ff_196_q, d_ff_197_q,
       d_ff_198_q, d_ff_199_q, d_ff_200_q, d_ff_201_q, d_ff_202_q, d_ff_203_q, d_ff_204_q, d_ff_205_q,
       d_ff_206_q, d_ff_207_q, d_ff_208_q, d_ff_209_q, d_ff_210_q, d_ff_211_q, d_ff_212_q, d_ff_213_q,
       d_ff_214_q, d_ff_215_q, d_ff_216_q, d_ff_217_q, d_ff_218_q, d_ff_219_q, d_ff_220_q, d_ff_221_q,
       d_ff_222_q, d_ff_223_q, d_ff_224_q, d_ff_225_q, d_ff_226_q, d_ff_227_q, d_ff_228_q, d_ff_229_q,
       d_ff_230_q, d_ff_231_q, d_ff_232_q, d_ff_233_q, d_ff_234_q, d_ff_235_q, d_ff_236_q, d_ff_237_q,
       d_ff_238_q, d_ff_239_q, d_ff_240_q, d_ff_241_q, d_ff_242_q, d_ff_243_q, d_ff_244_q, d_ff_245_q,
       d_ff_246_q, d_ff_247_q, d_ff_248_q, d_ff_249_q, d_ff_250_q, d_ff_251_q, d_ff_252_q, d_ff_253_q,
       d_ff_254_q, d_ff_255_q, d_ff_256_q, d_ff_257_q, d_ff_258_q, d_ff_259_q, d_ff_260_q, d_ff_261_q,
       d_ff_262_q, d_ff_263_q, d_ff_264_q, d_ff_265_q, d_ff_266_q, d_ff_267_q, d_ff_268_q, d_ff_269_q,
       d_ff_270_q, d_ff_271_q, d_ff_272_q, d_ff_273_q, d_ff_274_q, d_ff_275_q, d_ff_276_q, d_ff_277_q,
       d_ff_278_q, d_ff_279_q, d_ff_280_q, d_ff_281_q, d_ff_282_q, d_ff_283_q, d_ff_284_q, d_ff_285_q,
       d_ff_286_q, d_ff_287_q, d_ff_288_q, d_ff_289_q, d_ff_290_q, d_ff_291_q, d_ff_292_q, d_ff_293_q,
       d_ff_294_q, d_ff_295_q, d_ff_296_q, d_ff_297_q, d_ff_298_q, d_ff_299_q, d_ff_300_q, d_ff_301_q,
       d_ff_302_q, d_ff_303_q, d_ff_304_q, d_ff_305_q, d_ff_306_q, decoder_1_out0, decoder_1_out1,
       decoder_1_out2, decoder_1_out3, decoder_1_out4, decoder_1_out5, decoder_1_out6, decoder_1_out7,
       decoder_1_out8, decoder_1_out9, decoder_1_out10, decoder_1_out11, decoder_1_out12, decoder_1_out13,
       decoder_1_out14, decoder_1_out15, dipswitch_2_sw1, instruction_register_1_add,
       instruction_register_1_bin_and, instruction_register_1_bin_equal, instruction_register_1_bin_not,
       instruction_register_1_bin_or, instruction_register_1_bin_xor, instruction_register_1_clear,
       instruction_register_1_cond_if, instruction_register_1_get, instruction_register_1_greater_than,
       instruction_register_1_mov, instruction_register_1_ra1, instruction_register_1_ra2,
       instruction_register_1_ra3, instruction_register_1_ra4, instruction_register_1_rb1,
       instruction_register_1_rb2, instruction_register_1_rb3, instruction_register_1_rb4,
       instruction_register_1_rd1, instruction_register_1_rd2, instruction_register_1_rd3,
       instruction_register_1_rd4, instruction_register_1_set, instruction_register_1_show,
       instruction_register_1_sub, memory_address_manager_1_rd_c_1, memory_address_manager_1_rd_c_2,
       memory_address_manager_1_rd_c_3, memory_address_manager_1_rd_c_4, memory_address_manager_1_rd_o_1,
       memory_address_manager_1_rd_o_2, memory_address_manager_1_rd_o_3, memory_address_manager_1_rd_o_4,
       mover_1_csr1, mover_1_rd_c_1, mover_1_rd_c_2, mover_1_rd_c_3, mover_1_rd_c_4, mover_1_rd_o_1,
       mover_1_rd_o_2, mover_1_rd_o_3, mover_1_rd_o_4, or_1_out, output_control_1_rd_c_1,
       output_control_1_rd_c_2, output_control_1_rd_c_3, output_control_1_rd_c_4, output_control_1_rd_o_1,
       output_control_1_rd_o_2, output_control_1_rd_o_3, output_control_1_rd_o_4, program_counter_1_clk_a,
       program_counter_1_clk_i_a, program_counter_1_last_bit, program_counter_1_out_1,
       program_counter_1_rd_c_1, program_counter_1_rd_c_2, program_counter_1_rd_c_3,
       program_counter_1_rd_c_4, program_counter_1_rd_o_1, program_counter_1_rd_o_2,
       program_counter_1_rd_o_3, program_counter_1_rd_o_4, program_counter_1_ri_c_1,
       program_counter_1_ri_c_2, program_counter_1_ri_c_3, program_counter_1_ri_c_4,
       program_counter_1_ri_c_5, program_counter_1_ri_c_6, program_counter_1_ri_c_7,
       program_counter_1_ri_c_8, program_counter_1_ri_c_9, program_counter_1_ri_c_10,
       program_counter_1_ri_c_11, program_counter_1_ri_c_12, program_counter_1_ri_c_13,
       program_counter_1_ri_c_14, program_counter_1_ri_c_15, program_counter_1_ri_c_16,
       program_counter_1_ri_o_1, program_counter_1_ri_o_2, program_counter_1_ri_o_3,
       program_counter_1_ri_o_4, program_counter_1_ri_o_5, program_counter_1_ri_o_6,
       program_counter_1_ri_o_7, program_counter_1_ri_o_8, program_counter_1_ri_o_9,
       program_counter_1_ri_o_10, program_counter_1_ri_o_11, program_counter_1_ri_o_12,
       program_counter_1_ri_o_13, program_counter_1_ri_o_14, program_counter_1_ri_o_15,
       program_counter_1_ri_o_16, transistor_1_out, transistor_2_out, transistor_3_out, transistor_4_out,
       transistor_5_out, transistor_6_out, transistor_7_out, transistor_8_out, transistor_9_out,
       transistor_10_out, transistor_11_out, transistor_12_out, transistor_13_out, transistor_14_out,
       transistor_15_out, transistor_16_out, transistor_17_out, transistor_18_out, transistor_19_out,
       transistor_20_out, transistor_21_out, transistor_22_out, transistor_23_out, transistor_24_out,
       transistor_25_out, transistor_26_out, transistor_27_out, transistor_28_out, transistor_29_out,
       transistor_30_out, transistor_31_out, transistor_32_out, transistor_65_out, transistor_66_out,
       transistor_67_out, transistor_68_out, transistor_69_out, transistor_70_out, transistor_71_out,
       transistor_72_out, transistor_73_out;
  wire [3:0] dipswitch_1_p4;
  wire [7:0] output_control_1_s_o_1, output_control_1_s_o_2, output_control_1_s_o_3, output_control_1_s_o_4,
       output_control_1_s_o_5, output_control_1_s_o_6, output_control_1_s_o_7, output_control_1_s_o_8;

  Button button_1 (.out(button_1_out));
  D_Flip_Flop d_ff_1 (.clk(and_1_out), .Q(d_ff_1_q), .preset(button_1_out));  // open: D, Qn, reset
  Button button_2 (.out(button_2_out));
  Clock clock_1 (.out(clock_1_out));
  Button button_3 (.out(button_3_out));
  Button button_4 (.out(button_4_out));
  Button button_5 (.out(button_5_out));
  Button button_6 (.out(button_6_out));
  D_Flip_Flop d_ff_2 (.D(d_ff_1_q), .clk(and_1_out), .Q(d_ff_2_q), .preset(button_3_out));  // open: Qn, reset
  Button button_7 (.out(button_7_out));
  Button button_8 (.out(button_8_out));
  Button button_9 (.out(button_9_out));
  Button button_10 (.out(button_10_out));
  D_Flip_Flop d_ff_3 (.D(d_ff_2_q), .clk(and_1_out), .Q(d_ff_3_q), .preset(button_4_out));  // open: Qn, reset
  // DipSwitch dipswitch_1: pin names not known; wires that end beside it: dipswitch_1_p4[3], dipswitch_1_p4[2], dipswitch_1_p4[1], dipswitch_1_p4[0]
  DipSwitch #(.number(1)) dipswitch_2 (.sw1(dipswitch_2_sw1));
  Button button_11 (.out(button_11_out));
  Button button_12 (.out(button_12_out));
  Button button_13 (.out(button_13_out));
  Button button_14 (.out(button_14_out));
  D_Flip_Flop d_ff_4 (.D(d_ff_3_q), .clk(and_1_out), .Q(d_ff_4_q), .preset(button_5_out));  // open: Qn, reset
  Button button_15 (.out(button_15_out));
  D_Flip_Flop d_ff_5 (.D(d_ff_4_q), .clk(and_1_out), .Q(d_ff_5_q), .preset(button_6_out));  // open: Qn, reset
  Decoder #(.select(4)) decoder_1 (
    .out0(decoder_1_out0), .out1(decoder_1_out1), .out2(decoder_1_out2), .out3(decoder_1_out3),
    .out4(decoder_1_out4), .out5(decoder_1_out5), .out6(decoder_1_out6), .out7(decoder_1_out7),
    .out8(decoder_1_out8), .out9(decoder_1_out9), .out10(decoder_1_out10), .out11(decoder_1_out11),
    .out12(decoder_1_out12), .out13(decoder_1_out13), .out14(decoder_1_out14), .out15(decoder_1_out15),
    .sel(dipswitch_1_p4), .en(dipswitch_2_sw1));
  counter_14 counter_14_1 (.start(button_2_out), .CLK(clock_1_out), .CLK_A(counter_14_1_clk_a));
  and and_1 (and_1_out, counter_14_1_clk_a, clock_1_out);
  D_Flip_Flop d_ff_6 (.D(d_ff_5_q), .clk(and_1_out), .Q(d_ff_6_q), .preset(button_7_out));  // open: Qn, reset
  D_Flip_Flop d_ff_7 (.D(d_ff_6_q), .clk(and_1_out), .Q(d_ff_7_q), .preset(button_8_out));  // open: Qn, reset
  D_Flip_Flop d_ff_8 (.D(d_ff_7_q), .clk(and_1_out), .Q(d_ff_8_q), .preset(button_9_out));  // open: Qn, reset
  D_Flip_Flop d_ff_9 (.D(d_ff_8_q), .clk(and_1_out), .Q(d_ff_9_q), .preset(button_10_out));  // open: Qn, reset
  D_Flip_Flop d_ff_10 (.D(d_ff_9_q), .clk(and_1_out), .Q(d_ff_10_q), .preset(button_11_out));  // open: Qn, reset
  D_Flip_Flop d_ff_11 (.D(d_ff_10_q), .clk(and_1_out), .Q(d_ff_11_q), .preset(button_12_out));  // open: Qn, reset
  D_Flip_Flop d_ff_12 (.D(d_ff_11_q), .clk(and_1_out), .Q(d_ff_12_q), .preset(button_13_out));  // open: Qn, reset
  D_Flip_Flop d_ff_13 (.D(d_ff_12_q), .clk(and_1_out), .Q(d_ff_13_q), .preset(button_14_out));  // open: Qn, reset
  D_Flip_Flop d_ff_14 (.D(d_ff_13_q), .clk(and_1_out), .Q(d_ff_14_q), .preset(button_15_out));  // open: Qn, reset
  D_Flip_Flop d_ff_15 (.D(d_ff_14_q), .clk(and_1_out), .Q(d_ff_15_q));  // open: Qn, preset, reset
  and and_2 (and_2_out, d_ff_15_q, decoder_1_out0);
  and and_3 (and_3_out, and_1_out, decoder_1_out0);
  and and_4 (and_4_out, d_ff_15_q, decoder_1_out1);
  and and_5 (and_5_out, and_1_out, decoder_1_out1);
  and and_6 (and_6_out, d_ff_15_q, decoder_1_out2);
  and and_7 (and_7_out, and_1_out, decoder_1_out2);
  and and_8 (and_8_out, d_ff_15_q, decoder_1_out3);
  and and_9 (and_9_out, and_1_out, decoder_1_out3);
  and and_10 (and_10_out, d_ff_15_q, decoder_1_out4);
  and and_11 (and_11_out, and_1_out, decoder_1_out4);
  and and_12 (and_12_out, d_ff_15_q, decoder_1_out5);
  and and_13 (and_13_out, and_1_out, decoder_1_out5);
  and and_14 (and_14_out, d_ff_15_q, decoder_1_out6);
  and and_15 (and_15_out, and_1_out, decoder_1_out6);
  and and_16 (and_16_out, d_ff_15_q, decoder_1_out7);
  and and_17 (and_17_out, and_1_out, decoder_1_out7);
  and and_18 (and_18_out, d_ff_15_q, decoder_1_out8);
  and and_19 (and_19_out, and_1_out, decoder_1_out8);
  and and_20 (and_20_out, d_ff_15_q, decoder_1_out9);
  and and_21 (and_21_out, and_1_out, decoder_1_out9);
  and and_22 (and_22_out, d_ff_15_q, decoder_1_out10);
  and and_23 (and_23_out, and_1_out, decoder_1_out10);
  and and_24 (and_24_out, d_ff_15_q, decoder_1_out11);
  and and_25 (and_25_out, and_1_out, decoder_1_out11);
  and and_26 (and_26_out, d_ff_15_q, decoder_1_out12);
  and and_27 (and_27_out, and_1_out, decoder_1_out12);
  and and_28 (and_28_out, d_ff_15_q, decoder_1_out13);
  and and_29 (and_29_out, and_1_out, decoder_1_out13);
  and and_30 (and_30_out, d_ff_15_q, decoder_1_out14);
  and and_31 (and_31_out, and_1_out, decoder_1_out14);
  and and_32 (and_32_out, d_ff_15_q, decoder_1_out15);
  and and_33 (and_33_out, and_1_out, decoder_1_out15);
  Transistor transistor_1 (.in(and_2_out), .out(transistor_1_out), .gate(1'b0));
  Transistor transistor_2 (.in(and_3_out), .out(transistor_2_out), .gate(1'b0));
  Transistor transistor_3 (.in(and_4_out), .out(transistor_3_out), .gate(1'b0));
  Transistor transistor_4 (.in(and_5_out), .out(transistor_4_out), .gate(1'b0));
  Transistor transistor_5 (.in(and_6_out), .out(transistor_5_out), .gate(1'b0));
  Transistor transistor_6 (.in(and_7_out), .out(transistor_6_out), .gate(1'b0));
  Transistor transistor_7 (.in(and_8_out), .out(transistor_7_out), .gate(1'b0));
  Transistor transistor_8 (.in(and_9_out), .out(transistor_8_out), .gate(1'b0));
  Transistor transistor_9 (.in(and_10_out), .out(transistor_9_out), .gate(1'b0));
  Transistor transistor_10 (.in(and_11_out), .out(transistor_10_out), .gate(1'b0));
  Transistor transistor_11 (.in(and_12_out), .out(transistor_11_out), .gate(1'b0));
  Transistor transistor_12 (.in(and_13_out), .out(transistor_12_out), .gate(1'b0));
  Transistor transistor_13 (.in(and_14_out), .out(transistor_13_out), .gate(1'b0));
  Transistor transistor_14 (.in(and_15_out), .out(transistor_14_out), .gate(1'b0));
  Transistor transistor_15 (.in(and_16_out), .out(transistor_15_out), .gate(1'b0));
  Transistor transistor_16 (.in(and_17_out), .out(transistor_16_out), .gate(1'b0));
  Transistor transistor_17 (.in(and_18_out), .out(transistor_17_out), .gate(1'b0));
  Transistor transistor_18 (.in(and_19_out), .out(transistor_18_out), .gate(1'b0));
  Transistor transistor_19 (.in(and_20_out), .out(transistor_19_out), .gate(1'b0));
  Transistor transistor_20 (.in(and_21_out), .out(transistor_20_out), .gate(1'b0));
  Transistor transistor_21 (.in(and_22_out), .out(transistor_21_out), .gate(1'b0));
  Transistor transistor_22 (.in(and_23_out), .out(transistor_22_out), .gate(1'b0));
  Transistor transistor_23 (.in(and_24_out), .out(transistor_23_out), .gate(1'b0));
  Transistor transistor_24 (.in(and_25_out), .out(transistor_24_out), .gate(1'b0));
  Transistor transistor_25 (.in(and_26_out), .out(transistor_25_out), .gate(1'b0));
  Transistor transistor_26 (.in(and_27_out), .out(transistor_26_out), .gate(1'b0));
  Transistor transistor_27 (.in(and_28_out), .out(transistor_27_out), .gate(1'b0));
  Transistor transistor_28 (.in(and_29_out), .out(transistor_28_out), .gate(1'b0));
  Transistor transistor_29 (.in(and_30_out), .out(transistor_29_out), .gate(1'b0));
  Transistor transistor_30 (.in(and_31_out), .out(transistor_30_out), .gate(1'b0));
  Transistor transistor_31 (.in(and_32_out), .out(transistor_31_out), .gate(1'b0));
  Transistor transistor_32 (.in(and_33_out), .out(transistor_32_out), .gate(1'b0));
  Pull_Resistor pull_resistor_1 (.node(transistor_1_out));
  Pull_Resistor pull_resistor_2 (.node(transistor_2_out));
  Pull_Resistor pull_resistor_3 (.node(transistor_3_out));
  Pull_Resistor pull_resistor_4 (.node(transistor_4_out));
  Pull_Resistor pull_resistor_5 (.node(transistor_5_out));
  Pull_Resistor pull_resistor_6 (.node(transistor_6_out));
  Pull_Resistor pull_resistor_7 (.node(transistor_7_out));
  Pull_Resistor pull_resistor_8 (.node(transistor_8_out));
  Pull_Resistor pull_resistor_9 (.node(transistor_9_out));
  Pull_Resistor pull_resistor_10 (.node(transistor_10_out));
  Pull_Resistor pull_resistor_11 (.node(transistor_11_out));
  Pull_Resistor pull_resistor_12 (.node(transistor_12_out));
  Pull_Resistor pull_resistor_13 (.node(transistor_13_out));
  Pull_Resistor pull_resistor_14 (.node(transistor_14_out));
  Pull_Resistor pull_resistor_15 (.node(transistor_15_out));
  Pull_Resistor pull_resistor_16 (.node(transistor_16_out));
  Pull_Resistor pull_resistor_17 (.node(transistor_17_out));
  Pull_Resistor pull_resistor_18 (.node(transistor_18_out));
  Pull_Resistor pull_resistor_19 (.node(transistor_19_out));
  Pull_Resistor pull_resistor_20 (.node(transistor_20_out));
  Pull_Resistor pull_resistor_21 (.node(transistor_21_out));
  Pull_Resistor pull_resistor_22 (.node(transistor_22_out));
  Pull_Resistor pull_resistor_23 (.node(transistor_23_out));
  Pull_Resistor pull_resistor_24 (.node(transistor_24_out));
  Pull_Resistor pull_resistor_25 (.node(transistor_25_out));
  Pull_Resistor pull_resistor_26 (.node(transistor_26_out));
  Pull_Resistor pull_resistor_27 (.node(transistor_27_out));
  Pull_Resistor pull_resistor_28 (.node(transistor_28_out));
  Pull_Resistor pull_resistor_29 (.node(transistor_29_out));
  Pull_Resistor pull_resistor_30 (.node(transistor_30_out));
  Pull_Resistor pull_resistor_31 (.node(transistor_31_out));
  Pull_Resistor pull_resistor_32 (.node(transistor_32_out));
  D_Flip_Flop d_ff_16 (.D(transistor_1_out), .clk(transistor_2_out), .Q(d_ff_16_q));  // open: Qn, preset, reset
  D_Flip_Flop d_ff_17 (.D(transistor_3_out), .clk(transistor_4_out), .Q(d_ff_17_q));  // open: Qn, preset, reset
  D_Flip_Flop d_ff_18 (.D(transistor_5_out), .clk(transistor_6_out), .Q(d_ff_18_q));  // open: Qn, preset, reset
  D_Flip_Flop d_ff_19 (.D(transistor_7_out), .clk(transistor_8_out), .Q(d_ff_19_q));  // open: Qn, preset, reset
  D_Flip_Flop d_ff_20 (.D(transistor_9_out), .clk(transistor_10_out), .Q(d_ff_20_q));  // open: Qn, preset, reset
  D_Flip_Flop d_ff_21 (.D(transistor_11_out), .clk(transistor_12_out), .Q(d_ff_21_q));  // open: Qn, preset, reset
  D_Flip_Flop d_ff_22 (.D(transistor_13_out), .clk(transistor_14_out), .Q(d_ff_22_q));  // open: Qn, preset, reset
  D_Flip_Flop d_ff_23 (.D(transistor_15_out), .clk(transistor_16_out), .Q(d_ff_23_q));  // open: Qn, preset, reset
  D_Flip_Flop d_ff_24 (.D(transistor_17_out), .clk(transistor_18_out), .Q(d_ff_24_q));  // open: Qn, preset, reset
  D_Flip_Flop d_ff_25 (.D(transistor_19_out), .clk(transistor_20_out), .Q(d_ff_25_q));  // open: Qn, preset, reset
  D_Flip_Flop d_ff_26 (.D(transistor_21_out), .clk(transistor_22_out), .Q(d_ff_26_q));  // open: Qn, preset, reset
  D_Flip_Flop d_ff_27 (.D(transistor_23_out), .clk(transistor_24_out), .Q(d_ff_27_q));  // open: Qn, preset, reset
  D_Flip_Flop d_ff_28 (.D(transistor_25_out), .clk(transistor_26_out), .Q(d_ff_28_q));  // open: Qn, preset, reset
  D_Flip_Flop d_ff_29 (.D(transistor_27_out), .clk(transistor_28_out), .Q(d_ff_29_q));  // open: Qn, preset, reset
  D_Flip_Flop d_ff_30 (.D(transistor_29_out), .clk(transistor_30_out), .Q(d_ff_30_q));  // open: Qn, preset, reset
  D_Flip_Flop d_ff_31 (.D(transistor_31_out), .clk(transistor_32_out), .Q(d_ff_31_q));  // open: Qn, preset, reset
  D_Flip_Flop d_ff_32 (.D(d_ff_16_q), .clk(transistor_2_out), .Q(d_ff_32_q));  // open: Qn, preset, reset
  D_Flip_Flop d_ff_33 (.D(d_ff_17_q), .clk(transistor_4_out), .Q(d_ff_33_q));  // open: Qn, preset, reset
  D_Flip_Flop d_ff_34 (.D(d_ff_18_q), .clk(transistor_6_out), .Q(d_ff_34_q));  // open: Qn, preset, reset
  D_Flip_Flop d_ff_35 (.D(d_ff_19_q), .clk(transistor_8_out), .Q(d_ff_35_q));  // open: Qn, preset, reset
  D_Flip_Flop d_ff_36 (.D(d_ff_20_q), .clk(transistor_10_out), .Q(d_ff_36_q));  // open: Qn, preset, reset
  D_Flip_Flop d_ff_37 (.D(d_ff_21_q), .clk(transistor_12_out), .Q(d_ff_37_q));  // open: Qn, preset, reset
  D_Flip_Flop d_ff_38 (.D(d_ff_22_q), .clk(transistor_14_out), .Q(d_ff_38_q));  // open: Qn, preset, reset
  D_Flip_Flop d_ff_39 (.D(d_ff_23_q), .clk(transistor_16_out), .Q(d_ff_39_q));  // open: Qn, preset, reset
  D_Flip_Flop d_ff_40 (.D(d_ff_24_q), .clk(transistor_18_out), .Q(d_ff_40_q));  // open: Qn, preset, reset
  D_Flip_Flop d_ff_41 (.D(d_ff_25_q), .clk(transistor_20_out), .Q(d_ff_41_q));  // open: Qn, preset, reset
  D_Flip_Flop d_ff_42 (.D(d_ff_26_q), .clk(transistor_22_out), .Q(d_ff_42_q));  // open: Qn, preset, reset
  D_Flip_Flop d_ff_43 (.D(d_ff_27_q), .clk(transistor_24_out), .Q(d_ff_43_q));  // open: Qn, preset, reset
  D_Flip_Flop d_ff_44 (.D(d_ff_28_q), .clk(transistor_26_out), .Q(d_ff_44_q));  // open: Qn, preset, reset
  D_Flip_Flop d_ff_45 (.D(d_ff_29_q), .clk(transistor_28_out), .Q(d_ff_45_q));  // open: Qn, preset, reset
  D_Flip_Flop d_ff_46 (.D(d_ff_30_q), .clk(transistor_30_out), .Q(d_ff_46_q));  // open: Qn, preset, reset
  D_Flip_Flop d_ff_47 (.D(d_ff_31_q), .clk(transistor_32_out), .Q(d_ff_47_q));  // open: Qn, preset, reset
  D_Flip_Flop d_ff_48 (.D(d_ff_32_q), .clk(transistor_2_out), .Q(d_ff_48_q));  // open: Qn, preset, reset
  D_Flip_Flop d_ff_49 (.D(d_ff_33_q), .clk(transistor_4_out), .Q(d_ff_49_q));  // open: Qn, preset, reset
  D_Flip_Flop d_ff_50 (.D(d_ff_34_q), .clk(transistor_6_out), .Q(d_ff_50_q));  // open: Qn, preset, reset
  D_Flip_Flop d_ff_51 (.D(d_ff_35_q), .clk(transistor_8_out), .Q(d_ff_51_q));  // open: Qn, preset, reset
  D_Flip_Flop d_ff_52 (.D(d_ff_36_q), .clk(transistor_10_out), .Q(d_ff_52_q));  // open: Qn, preset, reset
  D_Flip_Flop d_ff_53 (.D(d_ff_37_q), .clk(transistor_12_out), .Q(d_ff_53_q));  // open: Qn, preset, reset
  D_Flip_Flop d_ff_54 (.D(d_ff_38_q), .clk(transistor_14_out), .Q(d_ff_54_q));  // open: Qn, preset, reset
  D_Flip_Flop d_ff_55 (.D(d_ff_39_q), .clk(transistor_16_out), .Q(d_ff_55_q));  // open: Qn, preset, reset
  D_Flip_Flop d_ff_56 (.D(d_ff_40_q), .clk(transistor_18_out), .Q(d_ff_56_q));  // open: Qn, preset, reset
  D_Flip_Flop d_ff_57 (.D(d_ff_41_q), .clk(transistor_20_out), .Q(d_ff_57_q));  // open: Qn, preset, reset
  D_Flip_Flop d_ff_58 (.D(d_ff_42_q), .clk(transistor_22_out), .Q(d_ff_58_q));  // open: Qn, preset, reset
  D_Flip_Flop d_ff_59 (.D(d_ff_43_q), .clk(transistor_24_out), .Q(d_ff_59_q));  // open: Qn, preset, reset
  D_Flip_Flop d_ff_60 (.D(d_ff_44_q), .clk(transistor_26_out), .Q(d_ff_60_q));  // open: Qn, preset, reset
  D_Flip_Flop d_ff_61 (.D(d_ff_45_q), .clk(transistor_28_out), .Q(d_ff_61_q));  // open: Qn, preset, reset
  D_Flip_Flop d_ff_62 (.D(d_ff_46_q), .clk(transistor_30_out), .Q(d_ff_62_q));  // open: Qn, preset, reset
  D_Flip_Flop d_ff_63 (.D(d_ff_47_q), .clk(transistor_32_out), .Q(d_ff_63_q));  // open: Qn, preset, reset
  Transistor transistor_33 (.in(program_counter_1_ri_o_1), .out(transistor_1_out), .gate(1'b0));
  Transistor transistor_34 (.in(program_counter_1_ri_o_2), .out(transistor_3_out), .gate(1'b0));
  Transistor transistor_35 (.in(program_counter_1_ri_o_3), .out(transistor_5_out), .gate(1'b0));
  Transistor transistor_36 (.in(program_counter_1_ri_o_4), .out(transistor_7_out), .gate(1'b0));
  Transistor transistor_37 (.in(program_counter_1_ri_o_5), .out(transistor_9_out), .gate(1'b0));
  Transistor transistor_38 (.in(program_counter_1_ri_o_6), .out(transistor_11_out), .gate(1'b0));
  Transistor transistor_39 (.in(program_counter_1_ri_o_7), .out(transistor_13_out), .gate(1'b0));
  Transistor transistor_40 (.in(program_counter_1_ri_o_8), .out(transistor_15_out), .gate(1'b0));
  Transistor transistor_41 (.in(program_counter_1_ri_o_9), .out(transistor_17_out), .gate(1'b0));
  Transistor transistor_42 (.in(program_counter_1_ri_o_10), .out(transistor_19_out), .gate(1'b0));
  Transistor transistor_43 (.in(program_counter_1_ri_o_11), .out(transistor_21_out), .gate(1'b0));
  Transistor transistor_44 (.in(program_counter_1_ri_o_12), .out(transistor_23_out), .gate(1'b0));
  Transistor transistor_45 (.in(program_counter_1_ri_o_13), .out(transistor_25_out), .gate(1'b0));
  Transistor transistor_46 (.in(program_counter_1_ri_o_14), .out(transistor_27_out), .gate(1'b0));
  Transistor transistor_47 (.in(program_counter_1_ri_o_15), .out(transistor_29_out), .gate(1'b0));
  Transistor transistor_48 (.in(program_counter_1_ri_o_16), .out(transistor_31_out), .gate(1'b0));
  Transistor transistor_49 (.in(program_counter_1_ri_c_1), .out(transistor_2_out), .gate(1'b0));
  Transistor transistor_50 (.in(program_counter_1_ri_c_2), .out(transistor_4_out), .gate(1'b0));
  Transistor transistor_51 (.in(program_counter_1_ri_c_3), .out(transistor_6_out), .gate(1'b0));
  Transistor transistor_52 (.in(program_counter_1_ri_c_4), .out(transistor_8_out), .gate(1'b0));
  Transistor transistor_53 (.in(program_counter_1_ri_c_5), .out(transistor_10_out), .gate(1'b0));
  Transistor transistor_54 (.in(program_counter_1_ri_c_6), .out(transistor_12_out), .gate(1'b0));
  Transistor transistor_55 (.in(program_counter_1_ri_c_7), .out(transistor_14_out), .gate(1'b0));
  Transistor transistor_56 (.in(program_counter_1_ri_c_8), .out(transistor_16_out), .gate(1'b0));
  Transistor transistor_57 (.in(program_counter_1_ri_c_9), .out(transistor_18_out), .gate(1'b0));
  Transistor transistor_58 (.in(program_counter_1_ri_c_10), .out(transistor_20_out), .gate(1'b0));
  Transistor transistor_59 (.in(program_counter_1_ri_c_11), .out(transistor_22_out), .gate(1'b0));
  Transistor transistor_60 (.in(program_counter_1_ri_c_12), .out(transistor_24_out), .gate(1'b0));
  Transistor transistor_61 (.in(program_counter_1_ri_c_13), .out(transistor_26_out), .gate(1'b0));
  Transistor transistor_62 (.in(program_counter_1_ri_c_14), .out(transistor_28_out), .gate(1'b0));
  Transistor transistor_63 (.in(program_counter_1_ri_c_15), .out(transistor_30_out), .gate(1'b0));
  Transistor transistor_64 (.in(program_counter_1_ri_c_16), .out(transistor_32_out), .gate(1'b0));
  D_Flip_Flop d_ff_64 (.D(d_ff_48_q), .clk(transistor_2_out), .Q(d_ff_64_q));  // open: Qn, preset, reset
  D_Flip_Flop d_ff_65 (.D(d_ff_49_q), .clk(transistor_4_out), .Q(d_ff_65_q));  // open: Qn, preset, reset
  D_Flip_Flop d_ff_66 (.D(d_ff_50_q), .clk(transistor_6_out), .Q(d_ff_66_q));  // open: Qn, preset, reset
  D_Flip_Flop d_ff_67 (.D(d_ff_51_q), .clk(transistor_8_out), .Q(d_ff_67_q));  // open: Qn, preset, reset
  D_Flip_Flop d_ff_68 (.D(d_ff_52_q), .clk(transistor_10_out), .Q(d_ff_68_q));  // open: Qn, preset, reset
  D_Flip_Flop d_ff_69 (.D(d_ff_53_q), .clk(transistor_12_out), .Q(d_ff_69_q));  // open: Qn, preset, reset
  D_Flip_Flop d_ff_70 (.D(d_ff_54_q), .clk(transistor_14_out), .Q(d_ff_70_q));  // open: Qn, preset, reset
  D_Flip_Flop d_ff_71 (.D(d_ff_55_q), .clk(transistor_16_out), .Q(d_ff_71_q));  // open: Qn, preset, reset
  D_Flip_Flop d_ff_72 (.D(d_ff_56_q), .clk(transistor_18_out), .Q(d_ff_72_q));  // open: Qn, preset, reset
  D_Flip_Flop d_ff_73 (.D(d_ff_57_q), .clk(transistor_20_out), .Q(d_ff_73_q));  // open: Qn, preset, reset
  D_Flip_Flop d_ff_74 (.D(d_ff_58_q), .clk(transistor_22_out), .Q(d_ff_74_q));  // open: Qn, preset, reset
  D_Flip_Flop d_ff_75 (.D(d_ff_59_q), .clk(transistor_24_out), .Q(d_ff_75_q));  // open: Qn, preset, reset
  D_Flip_Flop d_ff_76 (.D(d_ff_60_q), .clk(transistor_26_out), .Q(d_ff_76_q));  // open: Qn, preset, reset
  D_Flip_Flop d_ff_77 (.D(d_ff_61_q), .clk(transistor_28_out), .Q(d_ff_77_q));  // open: Qn, preset, reset
  D_Flip_Flop d_ff_78 (.D(d_ff_62_q), .clk(transistor_30_out), .Q(d_ff_78_q));  // open: Qn, preset, reset
  D_Flip_Flop d_ff_79 (.D(d_ff_63_q), .clk(transistor_32_out), .Q(d_ff_79_q));  // open: Qn, preset, reset
  D_Flip_Flop d_ff_80 (.D(d_ff_64_q), .clk(transistor_2_out), .Q(d_ff_80_q));  // open: Qn, preset, reset
  D_Flip_Flop d_ff_81 (.D(d_ff_65_q), .clk(transistor_4_out), .Q(d_ff_81_q));  // open: Qn, preset, reset
  D_Flip_Flop d_ff_82 (.D(d_ff_66_q), .clk(transistor_6_out), .Q(d_ff_82_q));  // open: Qn, preset, reset
  D_Flip_Flop d_ff_83 (.D(d_ff_67_q), .clk(transistor_8_out), .Q(d_ff_83_q));  // open: Qn, preset, reset
  D_Flip_Flop d_ff_84 (.D(d_ff_68_q), .clk(transistor_10_out), .Q(d_ff_84_q));  // open: Qn, preset, reset
  D_Flip_Flop d_ff_85 (.D(d_ff_69_q), .clk(transistor_12_out), .Q(d_ff_85_q));  // open: Qn, preset, reset
  D_Flip_Flop d_ff_86 (.D(d_ff_70_q), .clk(transistor_14_out), .Q(d_ff_86_q));  // open: Qn, preset, reset
  D_Flip_Flop d_ff_87 (.D(d_ff_71_q), .clk(transistor_16_out), .Q(d_ff_87_q));  // open: Qn, preset, reset
  D_Flip_Flop d_ff_88 (.D(d_ff_72_q), .clk(transistor_18_out), .Q(d_ff_88_q));  // open: Qn, preset, reset
  D_Flip_Flop d_ff_89 (.D(d_ff_73_q), .clk(transistor_20_out), .Q(d_ff_89_q));  // open: Qn, preset, reset
  D_Flip_Flop d_ff_90 (.D(d_ff_74_q), .clk(transistor_22_out), .Q(d_ff_90_q));  // open: Qn, preset, reset
  D_Flip_Flop d_ff_91 (.D(d_ff_75_q), .clk(transistor_24_out), .Q(d_ff_91_q));  // open: Qn, preset, reset
  D_Flip_Flop d_ff_92 (.D(d_ff_76_q), .clk(transistor_26_out), .Q(d_ff_92_q));  // open: Qn, preset, reset
  D_Flip_Flop d_ff_93 (.D(d_ff_77_q), .clk(transistor_28_out), .Q(d_ff_93_q));  // open: Qn, preset, reset
  D_Flip_Flop d_ff_94 (.D(d_ff_78_q), .clk(transistor_30_out), .Q(d_ff_94_q));  // open: Qn, preset, reset
  D_Flip_Flop d_ff_95 (.D(d_ff_79_q), .clk(transistor_32_out), .Q(d_ff_95_q));  // open: Qn, preset, reset
  D_Flip_Flop d_ff_96 (.D(d_ff_80_q), .clk(transistor_2_out), .Q(d_ff_96_q));  // open: Qn, preset, reset
  D_Flip_Flop d_ff_97 (.D(d_ff_81_q), .clk(transistor_4_out), .Q(d_ff_97_q));  // open: Qn, preset, reset
  D_Flip_Flop d_ff_98 (.D(d_ff_82_q), .clk(transistor_6_out), .Q(d_ff_98_q));  // open: Qn, preset, reset
  D_Flip_Flop d_ff_99 (.D(d_ff_83_q), .clk(transistor_8_out), .Q(d_ff_99_q));  // open: Qn, preset, reset
  D_Flip_Flop d_ff_100 (.D(d_ff_84_q), .clk(transistor_10_out), .Q(d_ff_100_q));  // open: Qn, preset, reset
  D_Flip_Flop d_ff_101 (.D(d_ff_85_q), .clk(transistor_12_out), .Q(d_ff_101_q));  // open: Qn, preset, reset
  D_Flip_Flop d_ff_102 (.D(d_ff_86_q), .clk(transistor_14_out), .Q(d_ff_102_q));  // open: Qn, preset, reset
  D_Flip_Flop d_ff_103 (.D(d_ff_87_q), .clk(transistor_16_out), .Q(d_ff_103_q));  // open: Qn, preset, reset
  D_Flip_Flop d_ff_104 (.D(d_ff_88_q), .clk(transistor_18_out), .Q(d_ff_104_q));  // open: Qn, preset, reset
  D_Flip_Flop d_ff_105 (.D(d_ff_89_q), .clk(transistor_20_out), .Q(d_ff_105_q));  // open: Qn, preset, reset
  D_Flip_Flop d_ff_106 (.D(d_ff_90_q), .clk(transistor_22_out), .Q(d_ff_106_q));  // open: Qn, preset, reset
  D_Flip_Flop d_ff_107 (.D(d_ff_91_q), .clk(transistor_24_out), .Q(d_ff_107_q));  // open: Qn, preset, reset
  D_Flip_Flop d_ff_108 (.D(d_ff_92_q), .clk(transistor_26_out), .Q(d_ff_108_q));  // open: Qn, preset, reset
  D_Flip_Flop d_ff_109 (.D(d_ff_93_q), .clk(transistor_28_out), .Q(d_ff_109_q));  // open: Qn, preset, reset
  D_Flip_Flop d_ff_110 (.D(d_ff_94_q), .clk(transistor_30_out), .Q(d_ff_110_q));  // open: Qn, preset, reset
  D_Flip_Flop d_ff_111 (.D(d_ff_95_q), .clk(transistor_32_out), .Q(d_ff_111_q));  // open: Qn, preset, reset
  D_Flip_Flop d_ff_112 (.D(d_ff_96_q), .clk(transistor_2_out), .Q(d_ff_112_q));  // open: Qn, preset, reset
  D_Flip_Flop d_ff_113 (.D(d_ff_97_q), .clk(transistor_4_out), .Q(d_ff_113_q));  // open: Qn, preset, reset
  D_Flip_Flop d_ff_114 (.D(d_ff_98_q), .clk(transistor_6_out), .Q(d_ff_114_q));  // open: Qn, preset, reset
  D_Flip_Flop d_ff_115 (.D(d_ff_99_q), .clk(transistor_8_out), .Q(d_ff_115_q));  // open: Qn, preset, reset
  D_Flip_Flop d_ff_116 (.D(d_ff_100_q), .clk(transistor_10_out), .Q(d_ff_116_q));  // open: Qn, preset, reset
  D_Flip_Flop d_ff_117 (.D(d_ff_101_q), .clk(transistor_12_out), .Q(d_ff_117_q));  // open: Qn, preset, reset
  D_Flip_Flop d_ff_118 (.D(d_ff_102_q), .clk(transistor_14_out), .Q(d_ff_118_q));  // open: Qn, preset, reset
  D_Flip_Flop d_ff_119 (.D(d_ff_103_q), .clk(transistor_16_out), .Q(d_ff_119_q));  // open: Qn, preset, reset
  D_Flip_Flop d_ff_120 (.D(d_ff_104_q), .clk(transistor_18_out), .Q(d_ff_120_q));  // open: Qn, preset, reset
  D_Flip_Flop d_ff_121 (.D(d_ff_105_q), .clk(transistor_20_out), .Q(d_ff_121_q));  // open: Qn, preset, reset
  D_Flip_Flop d_ff_122 (.D(d_ff_106_q), .clk(transistor_22_out), .Q(d_ff_122_q));  // open: Qn, preset, reset
  D_Flip_Flop d_ff_123 (.D(d_ff_107_q), .clk(transistor_24_out), .Q(d_ff_123_q));  // open: Qn, preset, reset
  D_Flip_Flop d_ff_124 (.D(d_ff_108_q), .clk(transistor_26_out), .Q(d_ff_124_q));  // open: Qn, preset, reset
  D_Flip_Flop d_ff_125 (.D(d_ff_109_q), .clk(transistor_28_out), .Q(d_ff_125_q));  // open: Qn, preset, reset
  D_Flip_Flop d_ff_126 (.D(d_ff_110_q), .clk(transistor_30_out), .Q(d_ff_126_q));  // open: Qn, preset, reset
  D_Flip_Flop d_ff_127 (.D(d_ff_111_q), .clk(transistor_32_out), .Q(d_ff_127_q));  // open: Qn, preset, reset
  D_Flip_Flop d_ff_128 (.D(d_ff_112_q), .clk(transistor_2_out), .Q(d_ff_128_q));  // open: Qn, preset, reset
  D_Flip_Flop d_ff_129 (.D(d_ff_113_q), .clk(transistor_4_out), .Q(d_ff_129_q));  // open: Qn, preset, reset
  D_Flip_Flop d_ff_130 (.D(d_ff_114_q), .clk(transistor_6_out), .Q(d_ff_130_q));  // open: Qn, preset, reset
  D_Flip_Flop d_ff_131 (.D(d_ff_115_q), .clk(transistor_8_out), .Q(d_ff_131_q));  // open: Qn, preset, reset
  D_Flip_Flop d_ff_132 (.D(d_ff_116_q), .clk(transistor_10_out), .Q(d_ff_132_q));  // open: Qn, preset, reset
  D_Flip_Flop d_ff_133 (.D(d_ff_117_q), .clk(transistor_12_out), .Q(d_ff_133_q));  // open: Qn, preset, reset
  D_Flip_Flop d_ff_134 (.D(d_ff_118_q), .clk(transistor_14_out), .Q(d_ff_134_q));  // open: Qn, preset, reset
  D_Flip_Flop d_ff_135 (.D(d_ff_119_q), .clk(transistor_16_out), .Q(d_ff_135_q));  // open: Qn, preset, reset
  D_Flip_Flop d_ff_136 (.D(d_ff_120_q), .clk(transistor_18_out), .Q(d_ff_136_q));  // open: Qn, preset, reset
  D_Flip_Flop d_ff_137 (.D(d_ff_121_q), .clk(transistor_20_out), .Q(d_ff_137_q));  // open: Qn, preset, reset
  D_Flip_Flop d_ff_138 (.D(d_ff_122_q), .clk(transistor_22_out), .Q(d_ff_138_q));  // open: Qn, preset, reset
  D_Flip_Flop d_ff_139 (.D(d_ff_123_q), .clk(transistor_24_out), .Q(d_ff_139_q));  // open: Qn, preset, reset
  D_Flip_Flop d_ff_140 (.D(d_ff_124_q), .clk(transistor_26_out), .Q(d_ff_140_q));  // open: Qn, preset, reset
  D_Flip_Flop d_ff_141 (.D(d_ff_125_q), .clk(transistor_28_out), .Q(d_ff_141_q));  // open: Qn, preset, reset
  D_Flip_Flop d_ff_142 (.D(d_ff_126_q), .clk(transistor_30_out), .Q(d_ff_142_q));  // open: Qn, preset, reset
  D_Flip_Flop d_ff_143 (.D(d_ff_127_q), .clk(transistor_32_out), .Q(d_ff_143_q));  // open: Qn, preset, reset
  D_Flip_Flop d_ff_144 (.D(d_ff_128_q), .clk(transistor_2_out), .Q(d_ff_144_q));  // open: Qn, preset, reset
  D_Flip_Flop d_ff_145 (.D(d_ff_129_q), .clk(transistor_4_out), .Q(d_ff_145_q));  // open: Qn, preset, reset
  D_Flip_Flop d_ff_146 (.D(d_ff_130_q), .clk(transistor_6_out), .Q(d_ff_146_q));  // open: Qn, preset, reset
  D_Flip_Flop d_ff_147 (.D(d_ff_131_q), .clk(transistor_8_out), .Q(d_ff_147_q));  // open: Qn, preset, reset
  D_Flip_Flop d_ff_148 (.D(d_ff_132_q), .clk(transistor_10_out), .Q(d_ff_148_q));  // open: Qn, preset, reset
  D_Flip_Flop d_ff_149 (.D(d_ff_133_q), .clk(transistor_12_out), .Q(d_ff_149_q));  // open: Qn, preset, reset
  D_Flip_Flop d_ff_150 (.D(d_ff_134_q), .clk(transistor_14_out), .Q(d_ff_150_q));  // open: Qn, preset, reset
  D_Flip_Flop d_ff_151 (.D(d_ff_135_q), .clk(transistor_16_out), .Q(d_ff_151_q));  // open: Qn, preset, reset
  D_Flip_Flop d_ff_152 (.D(d_ff_136_q), .clk(transistor_18_out), .Q(d_ff_152_q));  // open: Qn, preset, reset
  D_Flip_Flop d_ff_153 (.D(d_ff_137_q), .clk(transistor_20_out), .Q(d_ff_153_q));  // open: Qn, preset, reset
  D_Flip_Flop d_ff_154 (.D(d_ff_138_q), .clk(transistor_22_out), .Q(d_ff_154_q));  // open: Qn, preset, reset
  D_Flip_Flop d_ff_155 (.D(d_ff_139_q), .clk(transistor_24_out), .Q(d_ff_155_q));  // open: Qn, preset, reset
  D_Flip_Flop d_ff_156 (.D(d_ff_140_q), .clk(transistor_26_out), .Q(d_ff_156_q));  // open: Qn, preset, reset
  D_Flip_Flop d_ff_157 (.D(d_ff_141_q), .clk(transistor_28_out), .Q(d_ff_157_q));  // open: Qn, preset, reset
  D_Flip_Flop d_ff_158 (.D(d_ff_142_q), .clk(transistor_30_out), .Q(d_ff_158_q));  // open: Qn, preset, reset
  D_Flip_Flop d_ff_159 (.D(d_ff_143_q), .clk(transistor_32_out), .Q(d_ff_159_q));  // open: Qn, preset, reset
  D_Flip_Flop d_ff_160 (.D(d_ff_144_q), .clk(transistor_2_out), .Q(d_ff_160_q));  // open: Qn, preset, reset
  D_Flip_Flop d_ff_161 (.D(d_ff_145_q), .clk(transistor_4_out), .Q(d_ff_161_q));  // open: Qn, preset, reset
  D_Flip_Flop d_ff_162 (.D(d_ff_146_q), .clk(transistor_6_out), .Q(d_ff_162_q));  // open: Qn, preset, reset
  D_Flip_Flop d_ff_163 (.D(d_ff_147_q), .clk(transistor_8_out), .Q(d_ff_163_q));  // open: Qn, preset, reset
  D_Flip_Flop d_ff_164 (.D(d_ff_148_q), .clk(transistor_10_out), .Q(d_ff_164_q));  // open: Qn, preset, reset
  D_Flip_Flop d_ff_165 (.D(d_ff_149_q), .clk(transistor_12_out), .Q(d_ff_165_q));  // open: Qn, preset, reset
  D_Flip_Flop d_ff_166 (.D(d_ff_150_q), .clk(transistor_14_out), .Q(d_ff_166_q));  // open: Qn, preset, reset
  D_Flip_Flop d_ff_167 (.D(d_ff_151_q), .clk(transistor_16_out), .Q(d_ff_167_q));  // open: Qn, preset, reset
  D_Flip_Flop d_ff_168 (.D(d_ff_152_q), .clk(transistor_18_out), .Q(d_ff_168_q));  // open: Qn, preset, reset
  D_Flip_Flop d_ff_169 (.D(d_ff_153_q), .clk(transistor_20_out), .Q(d_ff_169_q));  // open: Qn, preset, reset
  D_Flip_Flop d_ff_170 (.D(d_ff_154_q), .clk(transistor_22_out), .Q(d_ff_170_q));  // open: Qn, preset, reset
  D_Flip_Flop d_ff_171 (.D(d_ff_155_q), .clk(transistor_24_out), .Q(d_ff_171_q));  // open: Qn, preset, reset
  D_Flip_Flop d_ff_172 (.D(d_ff_156_q), .clk(transistor_26_out), .Q(d_ff_172_q));  // open: Qn, preset, reset
  D_Flip_Flop d_ff_173 (.D(d_ff_157_q), .clk(transistor_28_out), .Q(d_ff_173_q));  // open: Qn, preset, reset
  D_Flip_Flop d_ff_174 (.D(d_ff_158_q), .clk(transistor_30_out), .Q(d_ff_174_q));  // open: Qn, preset, reset
  D_Flip_Flop d_ff_175 (.D(d_ff_159_q), .clk(transistor_32_out), .Q(d_ff_175_q));  // open: Qn, preset, reset
  D_Flip_Flop d_ff_176 (.D(d_ff_160_q), .clk(transistor_2_out), .Q(d_ff_176_q));  // open: Qn, preset, reset
  D_Flip_Flop d_ff_177 (.D(d_ff_161_q), .clk(transistor_4_out), .Q(d_ff_177_q));  // open: Qn, preset, reset
  D_Flip_Flop d_ff_178 (.D(d_ff_162_q), .clk(transistor_6_out), .Q(d_ff_178_q));  // open: Qn, preset, reset
  D_Flip_Flop d_ff_179 (.D(d_ff_163_q), .clk(transistor_8_out), .Q(d_ff_179_q));  // open: Qn, preset, reset
  D_Flip_Flop d_ff_180 (.D(d_ff_164_q), .clk(transistor_10_out), .Q(d_ff_180_q));  // open: Qn, preset, reset
  D_Flip_Flop d_ff_181 (.D(d_ff_165_q), .clk(transistor_12_out), .Q(d_ff_181_q));  // open: Qn, preset, reset
  D_Flip_Flop d_ff_182 (.D(d_ff_166_q), .clk(transistor_14_out), .Q(d_ff_182_q));  // open: Qn, preset, reset
  D_Flip_Flop d_ff_183 (.D(d_ff_167_q), .clk(transistor_16_out), .Q(d_ff_183_q));  // open: Qn, preset, reset
  D_Flip_Flop d_ff_184 (.D(d_ff_168_q), .clk(transistor_18_out), .Q(d_ff_184_q));  // open: Qn, preset, reset
  D_Flip_Flop d_ff_185 (.D(d_ff_169_q), .clk(transistor_20_out), .Q(d_ff_185_q));  // open: Qn, preset, reset
  D_Flip_Flop d_ff_186 (.D(d_ff_170_q), .clk(transistor_22_out), .Q(d_ff_186_q));  // open: Qn, preset, reset
  D_Flip_Flop d_ff_187 (.D(d_ff_171_q), .clk(transistor_24_out), .Q(d_ff_187_q));  // open: Qn, preset, reset
  D_Flip_Flop d_ff_188 (.D(d_ff_172_q), .clk(transistor_26_out), .Q(d_ff_188_q));  // open: Qn, preset, reset
  D_Flip_Flop d_ff_189 (.D(d_ff_173_q), .clk(transistor_28_out), .Q(d_ff_189_q));  // open: Qn, preset, reset
  D_Flip_Flop d_ff_190 (.D(d_ff_174_q), .clk(transistor_30_out), .Q(d_ff_190_q));  // open: Qn, preset, reset
  D_Flip_Flop d_ff_191 (.D(d_ff_175_q), .clk(transistor_32_out), .Q(d_ff_191_q));  // open: Qn, preset, reset
  D_Flip_Flop d_ff_192 (.D(d_ff_176_q), .clk(transistor_2_out), .Q(d_ff_192_q));  // open: Qn, preset, reset
  D_Flip_Flop d_ff_193 (.D(d_ff_177_q), .clk(transistor_4_out), .Q(d_ff_193_q));  // open: Qn, preset, reset
  D_Flip_Flop d_ff_194 (.D(d_ff_178_q), .clk(transistor_6_out), .Q(d_ff_194_q));  // open: Qn, preset, reset
  D_Flip_Flop d_ff_195 (.D(d_ff_179_q), .clk(transistor_8_out), .Q(d_ff_195_q));  // open: Qn, preset, reset
  D_Flip_Flop d_ff_196 (.D(d_ff_180_q), .clk(transistor_10_out), .Q(d_ff_196_q));  // open: Qn, preset, reset
  D_Flip_Flop d_ff_197 (.D(d_ff_181_q), .clk(transistor_12_out), .Q(d_ff_197_q));  // open: Qn, preset, reset
  D_Flip_Flop d_ff_198 (.D(d_ff_182_q), .clk(transistor_14_out), .Q(d_ff_198_q));  // open: Qn, preset, reset
  D_Flip_Flop d_ff_199 (.D(d_ff_183_q), .clk(transistor_16_out), .Q(d_ff_199_q));  // open: Qn, preset, reset
  D_Flip_Flop d_ff_200 (.D(d_ff_184_q), .clk(transistor_18_out), .Q(d_ff_200_q));  // open: Qn, preset, reset
  D_Flip_Flop d_ff_201 (.D(d_ff_185_q), .clk(transistor_20_out), .Q(d_ff_201_q));  // open: Qn, preset, reset
  D_Flip_Flop d_ff_202 (.D(d_ff_186_q), .clk(transistor_22_out), .Q(d_ff_202_q));  // open: Qn, preset, reset
  D_Flip_Flop d_ff_203 (.D(d_ff_187_q), .clk(transistor_24_out), .Q(d_ff_203_q));  // open: Qn, preset, reset
  D_Flip_Flop d_ff_204 (.D(d_ff_188_q), .clk(transistor_26_out), .Q(d_ff_204_q));  // open: Qn, preset, reset
  D_Flip_Flop d_ff_205 (.D(d_ff_189_q), .clk(transistor_28_out), .Q(d_ff_205_q));  // open: Qn, preset, reset
  D_Flip_Flop d_ff_206 (.D(d_ff_190_q), .clk(transistor_30_out), .Q(d_ff_206_q));  // open: Qn, preset, reset
  D_Flip_Flop d_ff_207 (.D(d_ff_191_q), .clk(transistor_32_out), .Q(d_ff_207_q));  // open: Qn, preset, reset
  D_Flip_Flop d_ff_208 (.D(d_ff_192_q), .clk(transistor_2_out), .Q(d_ff_208_q));  // open: Qn, preset, reset
  D_Flip_Flop d_ff_209 (.D(d_ff_193_q), .clk(transistor_4_out), .Q(d_ff_209_q));  // open: Qn, preset, reset
  D_Flip_Flop d_ff_210 (.D(d_ff_194_q), .clk(transistor_6_out), .Q(d_ff_210_q));  // open: Qn, preset, reset
  D_Flip_Flop d_ff_211 (.D(d_ff_195_q), .clk(transistor_8_out), .Q(d_ff_211_q));  // open: Qn, preset, reset
  D_Flip_Flop d_ff_212 (.D(d_ff_196_q), .clk(transistor_10_out), .Q(d_ff_212_q));  // open: Qn, preset, reset
  D_Flip_Flop d_ff_213 (.D(d_ff_197_q), .clk(transistor_12_out), .Q(d_ff_213_q));  // open: Qn, preset, reset
  D_Flip_Flop d_ff_214 (.D(d_ff_198_q), .clk(transistor_14_out), .Q(d_ff_214_q));  // open: Qn, preset, reset
  D_Flip_Flop d_ff_215 (.D(d_ff_199_q), .clk(transistor_16_out), .Q(d_ff_215_q));  // open: Qn, preset, reset
  D_Flip_Flop d_ff_216 (.D(d_ff_200_q), .clk(transistor_18_out), .Q(d_ff_216_q));  // open: Qn, preset, reset
  D_Flip_Flop d_ff_217 (.D(d_ff_201_q), .clk(transistor_20_out), .Q(d_ff_217_q));  // open: Qn, preset, reset
  D_Flip_Flop d_ff_218 (.D(d_ff_202_q), .clk(transistor_22_out), .Q(d_ff_218_q));  // open: Qn, preset, reset
  D_Flip_Flop d_ff_219 (.D(d_ff_203_q), .clk(transistor_24_out), .Q(d_ff_219_q));  // open: Qn, preset, reset
  D_Flip_Flop d_ff_220 (.D(d_ff_204_q), .clk(transistor_26_out), .Q(d_ff_220_q));  // open: Qn, preset, reset
  D_Flip_Flop d_ff_221 (.D(d_ff_205_q), .clk(transistor_28_out), .Q(d_ff_221_q));  // open: Qn, preset, reset
  D_Flip_Flop d_ff_222 (.D(d_ff_206_q), .clk(transistor_30_out), .Q(d_ff_222_q));  // open: Qn, preset, reset
  D_Flip_Flop d_ff_223 (.D(d_ff_207_q), .clk(transistor_32_out), .Q(d_ff_223_q));  // open: Qn, preset, reset
  D_Flip_Flop d_ff_224 (.D(d_ff_208_q), .clk(transistor_2_out), .Q(d_ff_224_q));  // open: Qn, preset, reset
  D_Flip_Flop d_ff_225 (.D(d_ff_209_q), .clk(transistor_4_out), .Q(d_ff_225_q));  // open: Qn, preset, reset
  D_Flip_Flop d_ff_226 (.D(d_ff_210_q), .clk(transistor_6_out), .Q(d_ff_226_q));  // open: Qn, preset, reset
  D_Flip_Flop d_ff_227 (.D(d_ff_211_q), .clk(transistor_8_out), .Q(d_ff_227_q));  // open: Qn, preset, reset
  D_Flip_Flop d_ff_228 (.D(d_ff_212_q), .clk(transistor_10_out), .Q(d_ff_228_q));  // open: Qn, preset, reset
  D_Flip_Flop d_ff_229 (.D(d_ff_213_q), .clk(transistor_12_out), .Q(d_ff_229_q));  // open: Qn, preset, reset
  D_Flip_Flop d_ff_230 (.D(d_ff_214_q), .clk(transistor_14_out), .Q(d_ff_230_q));  // open: Qn, preset, reset
  D_Flip_Flop d_ff_231 (.D(d_ff_215_q), .clk(transistor_16_out), .Q(d_ff_231_q));  // open: Qn, preset, reset
  D_Flip_Flop d_ff_232 (.D(d_ff_216_q), .clk(transistor_18_out), .Q(d_ff_232_q));  // open: Qn, preset, reset
  D_Flip_Flop d_ff_233 (.D(d_ff_217_q), .clk(transistor_20_out), .Q(d_ff_233_q));  // open: Qn, preset, reset
  D_Flip_Flop d_ff_234 (.D(d_ff_218_q), .clk(transistor_22_out), .Q(d_ff_234_q));  // open: Qn, preset, reset
  D_Flip_Flop d_ff_235 (.D(d_ff_219_q), .clk(transistor_24_out), .Q(d_ff_235_q));  // open: Qn, preset, reset
  D_Flip_Flop d_ff_236 (.D(d_ff_220_q), .clk(transistor_26_out), .Q(d_ff_236_q));  // open: Qn, preset, reset
  D_Flip_Flop d_ff_237 (.D(d_ff_221_q), .clk(transistor_28_out), .Q(d_ff_237_q));  // open: Qn, preset, reset
  D_Flip_Flop d_ff_238 (.D(d_ff_222_q), .clk(transistor_30_out), .Q(d_ff_238_q));  // open: Qn, preset, reset
  D_Flip_Flop d_ff_239 (.D(d_ff_223_q), .clk(transistor_32_out), .Q(d_ff_239_q));  // open: Qn, preset, reset
  D_Flip_Flop d_ff_240 (.D(d_ff_224_q), .clk(transistor_2_out), .Q(d_ff_240_q));  // open: Qn, preset, reset
  D_Flip_Flop d_ff_241 (.D(d_ff_225_q), .clk(transistor_4_out), .Q(d_ff_241_q));  // open: Qn, preset, reset
  D_Flip_Flop d_ff_242 (.D(d_ff_226_q), .clk(transistor_6_out), .Q(d_ff_242_q));  // open: Qn, preset, reset
  D_Flip_Flop d_ff_243 (.D(d_ff_227_q), .clk(transistor_8_out), .Q(d_ff_243_q));  // open: Qn, preset, reset
  D_Flip_Flop d_ff_244 (.D(d_ff_228_q), .clk(transistor_10_out), .Q(d_ff_244_q));  // open: Qn, preset, reset
  D_Flip_Flop d_ff_245 (.D(d_ff_229_q), .clk(transistor_12_out), .Q(d_ff_245_q));  // open: Qn, preset, reset
  D_Flip_Flop d_ff_246 (.D(d_ff_230_q), .clk(transistor_14_out), .Q(d_ff_246_q));  // open: Qn, preset, reset
  D_Flip_Flop d_ff_247 (.D(d_ff_231_q), .clk(transistor_16_out), .Q(d_ff_247_q));  // open: Qn, preset, reset
  D_Flip_Flop d_ff_248 (.D(d_ff_232_q), .clk(transistor_18_out), .Q(d_ff_248_q));  // open: Qn, preset, reset
  D_Flip_Flop d_ff_249 (.D(d_ff_233_q), .clk(transistor_20_out), .Q(d_ff_249_q));  // open: Qn, preset, reset
  D_Flip_Flop d_ff_250 (.D(d_ff_234_q), .clk(transistor_22_out), .Q(d_ff_250_q));  // open: Qn, preset, reset
  D_Flip_Flop d_ff_251 (.D(d_ff_235_q), .clk(transistor_24_out), .Q(d_ff_251_q));  // open: Qn, preset, reset
  D_Flip_Flop d_ff_252 (.D(d_ff_236_q), .clk(transistor_26_out), .Q(d_ff_252_q));  // open: Qn, preset, reset
  D_Flip_Flop d_ff_253 (.D(d_ff_237_q), .clk(transistor_28_out), .Q(d_ff_253_q));  // open: Qn, preset, reset
  D_Flip_Flop d_ff_254 (.D(d_ff_238_q), .clk(transistor_30_out), .Q(d_ff_254_q));  // open: Qn, preset, reset
  D_Flip_Flop d_ff_255 (.D(d_ff_239_q), .clk(transistor_32_out), .Q(d_ff_255_q));  // open: Qn, preset, reset
  Clock clock_2 (.out(clock_2_out));
  Button button_16 (.out(button_16_out));
  program_counter program_counter_1 (
    .start(button_16_out), .CLK(clock_2_out), .ri_1(d_ff_240_q), .ri_2(d_ff_241_q), .ri_3(d_ff_242_q),
    .ri_4(d_ff_243_q), .ri_5(d_ff_244_q), .ri_6(d_ff_245_q), .ri_7(d_ff_246_q), .ri_8(d_ff_247_q),
    .ri_9(d_ff_248_q), .ri_10(d_ff_249_q), .ri_11(d_ff_250_q), .ri_12(d_ff_251_q), .ri_13(d_ff_252_q),
    .ri_14(d_ff_253_q), .ri_15(d_ff_254_q), .ri_16(d_ff_255_q), .if_cond(instruction_register_1_cond_if),
    .l1_bit_1(d_ff_265_q), .l1_bit_2(d_ff_264_q), .l1_bit_3(d_ff_263_q), .l1_bit_4(d_ff_262_q),
    .l2_bit_1(d_ff_269_q), .l2_bit_2(d_ff_268_q), .l2_bit_3(d_ff_267_q), .l2_bit_4(d_ff_266_q),
    .rd_i_1(d_ff_303_q), .rd_i_2(d_ff_304_q), .rd_i_3(d_ff_305_q), .rd_i_4(d_ff_306_q),
    .rd_1(instruction_register_1_rd1), .rd_2(instruction_register_1_rd2), .rd_3(instruction_register_1_rd3),
    .rd_4(instruction_register_1_rd4), .CLK_I_A(program_counter_1_clk_i_a), .CLK_A(program_counter_1_clk_a),
    .last_bit(program_counter_1_last_bit), .out_1(program_counter_1_out_1),
    .RI_o_1(program_counter_1_ri_o_1), .RI_o_2(program_counter_1_ri_o_2), .RI_o_3(program_counter_1_ri_o_3),
    .RI_o_4(program_counter_1_ri_o_4), .RI_o_5(program_counter_1_ri_o_5), .RI_o_6(program_counter_1_ri_o_6),
    .RI_o_7(program_counter_1_ri_o_7), .RI_o_8(program_counter_1_ri_o_8), .RI_o_9(program_counter_1_ri_o_9),
    .RI_o_10(program_counter_1_ri_o_10), .RI_o_11(program_counter_1_ri_o_11),
    .RI_o_12(program_counter_1_ri_o_12), .RI_o_13(program_counter_1_ri_o_13),
    .RI_o_14(program_counter_1_ri_o_14), .RI_o_15(program_counter_1_ri_o_15),
    .RI_o_16(program_counter_1_ri_o_16), .RI_c_1(program_counter_1_ri_c_1),
    .RI_c_2(program_counter_1_ri_c_2), .RI_c_3(program_counter_1_ri_c_3), .RI_c_4(program_counter_1_ri_c_4),
    .RI_c_5(program_counter_1_ri_c_5), .RI_c_6(program_counter_1_ri_c_6), .RI_c_7(program_counter_1_ri_c_7),
    .RI_c_8(program_counter_1_ri_c_8), .RI_c_9(program_counter_1_ri_c_9),
    .RI_c_10(program_counter_1_ri_c_10), .RI_c_11(program_counter_1_ri_c_11),
    .RI_c_12(program_counter_1_ri_c_12), .RI_c_13(program_counter_1_ri_c_13),
    .RI_c_14(program_counter_1_ri_c_14), .RI_c_15(program_counter_1_ri_c_15),
    .RI_c_16(program_counter_1_ri_c_16), .rd_o_1(program_counter_1_rd_o_1),
    .rd_o_2(program_counter_1_rd_o_2), .rd_o_3(program_counter_1_rd_o_3), .rd_o_4(program_counter_1_rd_o_4),
    .rd_c_1(program_counter_1_rd_c_1), .rd_c_2(program_counter_1_rd_c_2), .rd_c_3(program_counter_1_rd_c_3),
    .rd_c_4(program_counter_1_rd_c_4));
  and and_34 (and_34_out, clock_2_out, program_counter_1_clk_i_a);
  D_Flip_Flop d_ff_256 (
    .D(program_counter_1_out_1), .clk(and_34_out), .Q(d_ff_256_q), .preset(button_18_out),
    .reset(button_17_out));  // open: Qn
  Button button_17 (.out(button_17_out));
  Button button_18 (.out(button_18_out));
  D_Flip_Flop d_ff_257 (
    .D(d_ff_256_q), .clk(and_34_out), .Q(d_ff_257_q), .preset(button_19_out), .reset(button_17_out));  // open: Qn
  Button button_19 (.out(button_19_out));
  D_Flip_Flop d_ff_258 (
    .D(d_ff_257_q), .clk(and_34_out), .Q(d_ff_258_q), .preset(button_20_out), .reset(button_17_out));  // open: Qn
  Button button_20 (.out(button_20_out));
  D_Flip_Flop d_ff_259 (
    .D(d_ff_258_q), .clk(and_34_out), .Q(d_ff_259_q), .preset(button_21_out), .reset(button_17_out));  // open: Qn
  Button button_21 (.out(button_21_out));
  Button button_22 (.out(button_22_out));
  D_Flip_Flop d_ff_260 (
    .D(d_ff_259_q), .clk(and_34_out), .Q(d_ff_260_q), .preset(button_22_out), .reset(button_17_out));  // open: Qn
  Button button_23 (.out(button_23_out));
  D_Flip_Flop d_ff_261 (
    .D(d_ff_260_q), .clk(and_34_out), .Q(d_ff_261_q), .preset(button_23_out), .reset(button_17_out));  // open: Qn
  Transistor transistor_65 (.in(d_ff_261_q), .out(transistor_65_out), .gate(1'b0));
  Button button_24 (.out(button_24_out));
  D_Flip_Flop d_ff_262 (
    .D(transistor_65_out), .clk(or_1_out), .Q(d_ff_262_q), .preset(button_24_out), .reset(button_17_out));  // open: Qn
  Pull_Resistor pull_resistor_33 (.node(transistor_65_out));
  or or_1 (or_1_out, mover_1_csr1, and_34_out);
  Button button_25 (.out(button_25_out));
  D_Flip_Flop d_ff_263 (
    .D(d_ff_262_q), .clk(or_1_out), .Q(d_ff_263_q), .preset(button_25_out), .reset(button_17_out));  // open: Qn
  Button button_26 (.out(button_26_out));
  D_Flip_Flop d_ff_264 (
    .D(d_ff_263_q), .clk(or_1_out), .Q(d_ff_264_q), .preset(button_26_out), .reset(button_17_out));  // open: Qn
  Button button_27 (.out(button_27_out));
  D_Flip_Flop d_ff_265 (
    .D(d_ff_264_q), .clk(or_1_out), .Q(d_ff_265_q), .preset(button_27_out), .reset(button_17_out));  // open: Qn
  Button button_28 (.out(button_28_out));
  D_Flip_Flop d_ff_266 (
    .D(d_ff_265_q), .clk(or_1_out), .Q(d_ff_266_q), .preset(button_28_out), .reset(button_17_out));  // open: Qn
  Button button_29 (.out(button_29_out));
  D_Flip_Flop d_ff_267 (
    .D(d_ff_266_q), .clk(or_1_out), .Q(d_ff_267_q), .preset(button_29_out), .reset(button_17_out));  // open: Qn
  Button button_30 (.out(button_30_out));
  D_Flip_Flop d_ff_268 (
    .D(d_ff_267_q), .clk(or_1_out), .Q(d_ff_268_q), .preset(button_30_out), .reset(button_17_out));  // open: Qn
  Button button_31 (.out(button_31_out));
  D_Flip_Flop d_ff_269 (
    .D(d_ff_268_q), .clk(or_1_out), .Q(d_ff_269_q), .preset(button_31_out), .reset(button_17_out));  // open: Qn
  D_Flip_Flop d_ff_270 (.D(d_ff_269_q), .clk(or_1_out), .Q(d_ff_270_q), .reset(button_17_out));  // open: Qn, preset
  instruction_register instruction_register_1 (
    .instruction1(d_ff_259_q), .instruction2(d_ff_258_q), .instruction3(d_ff_257_q),
    .instruction4(d_ff_256_q), .rd_bit1(d_ff_261_q), .rd_bit2(d_ff_260_q), .ra_bit1(d_ff_263_q),
    .ra_bit2(d_ff_262_q), .rb_bit1(d_ff_265_q), .rb_bit2(d_ff_264_q), .mov(instruction_register_1_mov),
    .set(instruction_register_1_set), .add(instruction_register_1_add), .sub(instruction_register_1_sub),
    .bin_and(instruction_register_1_bin_and), .bin_or(instruction_register_1_bin_or),
    .get(instruction_register_1_get), .show(instruction_register_1_show),
    .bin_not(instruction_register_1_bin_not), .bin_xor(instruction_register_1_bin_xor),
    .bin_equal(instruction_register_1_bin_equal), .greater_than(instruction_register_1_greater_than),
    .cond_if(instruction_register_1_cond_if), .rd1(instruction_register_1_rd1),
    .rd2(instruction_register_1_rd2), .rd3(instruction_register_1_rd3), .rd4(instruction_register_1_rd4),
    .ra1(instruction_register_1_ra1), .ra2(instruction_register_1_ra2), .ra3(instruction_register_1_ra3),
    .ra4(instruction_register_1_ra4), .rb1(instruction_register_1_rb1), .rb2(instruction_register_1_rb2),
    .rb3(instruction_register_1_rb3), .rb4(instruction_register_1_rb4), .clear(instruction_register_1_clear));
  mover mover_1 (
    .I1(d_ff_270_q), .CLK(clock_2_out), .CLK_A(program_counter_1_clk_a),
    .is_move_on(instruction_register_1_mov), .is_seg1_on(instruction_register_1_rd1),
    .is_seg2_on(instruction_register_1_rd2), .is_seg3_on(instruction_register_1_rd3),
    .is_seg4_on(instruction_register_1_rd4), .rd_o_1(mover_1_rd_o_1), .rd_o_2(mover_1_rd_o_2),
    .rd_o_3(mover_1_rd_o_3), .rd_o_4(mover_1_rd_o_4), .rd_c_1(mover_1_rd_c_1), .rd_c_2(mover_1_rd_c_2),
    .rd_c_3(mover_1_rd_c_3), .rd_c_4(mover_1_rd_c_4), .CSR1(mover_1_csr1));
  ALU alu_1 (
    .RFI_1(d_ff_303_q), .RFI_2(d_ff_304_q), .RFI_3(d_ff_305_q), .RFI_4(d_ff_306_q), .CLK(clock_2_out),
    .CLK_A(program_counter_1_clk_a), .is_add_on(instruction_register_1_add),
    .ra_1(instruction_register_1_ra1), .ra_2(instruction_register_1_ra2), .ra_3(instruction_register_1_ra3),
    .ra_4(instruction_register_1_ra4), .rb_1(instruction_register_1_rb1), .rb_2(instruction_register_1_rb2),
    .rb_3(instruction_register_1_rb3), .rb_4(instruction_register_1_rb4), .rd_1(instruction_register_1_rd1),
    .rd_2(instruction_register_1_rd2), .rd_3(instruction_register_1_rd3), .rd_4(instruction_register_1_rd4),
    .is_sub_on(instruction_register_1_sub), .is_and_on(instruction_register_1_bin_and),
    .is_or_on(instruction_register_1_bin_or), .is_not_on(instruction_register_1_bin_not),
    .is_equal_on(instruction_register_1_bin_equal), .is_xor_on(instruction_register_1_bin_xor),
    .is_gt_on(instruction_register_1_greater_than), .is_last_on(program_counter_1_last_bit),
    .rd_o_1(alu_1_rd_o_1), .rd_o_2(alu_1_rd_o_2), .rd_o_3(alu_1_rd_o_3), .rd_o_4(alu_1_rd_o_4),
    .rd_c_1(alu_1_rd_c_1), .rd_c_2(alu_1_rd_c_2), .rd_c_3(alu_1_rd_c_3), .rd_c_4(alu_1_rd_c_4),
    .ra_o_1(alu_1_ra_o_1), .ra_o_2(alu_1_ra_o_2), .ra_o_3(alu_1_ra_o_3), .ra_o_4(alu_1_ra_o_4),
    .ra_c_1(alu_1_ra_c_1), .ra_c_2(alu_1_ra_c_2), .ra_c_3(alu_1_ra_c_3), .ra_c_4(alu_1_ra_c_4),
    .rb_o_1(alu_1_rb_o_1), .rb_o_2(alu_1_rb_o_2), .rb_o_3(alu_1_rb_o_3), .rb_o_4(alu_1_rb_o_4),
    .rb_c_1(alu_1_rb_c_1), .rb_c_2(alu_1_rb_c_2), .rb_c_3(alu_1_rb_c_3), .rb_c_4(alu_1_rb_c_4));
  memory_address_manager memory_address_manager_1 (
    .CLK(clock_2_out), .CLK_A(program_counter_1_clk_a), .is_get_on(instruction_register_1_get),
    .is_set_on(instruction_register_1_set), .rd_1(d_ff_261_q), .rd_2(d_ff_260_q), .ram_add_1(d_ff_265_q),
    .ram_add_2(d_ff_264_q), .ram_add_3(d_ff_263_q), .ram_add_4(d_ff_262_q), .rd_i_1(d_ff_303_q),
    .rd_i_2(d_ff_304_q), .rd_i_3(d_ff_305_q), .rd_i_4(d_ff_306_q), .rd_o_1(memory_address_manager_1_rd_o_1),
    .rd_o_2(memory_address_manager_1_rd_o_2), .rd_o_3(memory_address_manager_1_rd_o_3),
    .rd_o_4(memory_address_manager_1_rd_o_4), .rd_c_1(memory_address_manager_1_rd_c_1),
    .rd_c_2(memory_address_manager_1_rd_c_2), .rd_c_3(memory_address_manager_1_rd_c_3),
    .rd_c_4(memory_address_manager_1_rd_c_4));
  output_control output_control_1 (
    .CLK(clock_2_out), .CLK_A(program_counter_1_clk_a), .is_shw_on(instruction_register_1_show),
    .rd_i_1(d_ff_303_q), .rd_i_2(d_ff_304_q), .rd_i_3(d_ff_305_q), .rd_i_4(d_ff_306_q),
    .rd_1(instruction_register_1_rd1), .rd_2(instruction_register_1_rd2), .rd_3(instruction_register_1_rd3),
    .rd_4(instruction_register_1_rd4), .clear(instruction_register_1_clear), .s_o_1(output_control_1_s_o_1),
    .s_o_2(output_control_1_s_o_2), .s_o_3(output_control_1_s_o_3), .s_o_4(output_control_1_s_o_4),
    .s_o_5(output_control_1_s_o_5), .s_o_6(output_control_1_s_o_6), .s_o_7(output_control_1_s_o_7),
    .s_o_8(output_control_1_s_o_8), .rd_o_1(output_control_1_rd_o_1), .rd_o_2(output_control_1_rd_o_2),
    .rd_o_3(output_control_1_rd_o_3), .rd_o_4(output_control_1_rd_o_4), .rd_c_1(output_control_1_rd_c_1),
    .rd_c_2(output_control_1_rd_c_2), .rd_c_3(output_control_1_rd_c_3), .rd_c_4(output_control_1_rd_c_4));
  Transistor transistor_66 (.in(mover_1_rd_o_1), .out(transistor_66_out), .gate(1'b0));
  Transistor transistor_67 (.in(mover_1_rd_o_2), .out(transistor_67_out), .gate(1'b0));
  Transistor transistor_68 (.in(mover_1_rd_o_3), .out(transistor_68_out), .gate(1'b0));
  Transistor transistor_69 (.in(mover_1_rd_o_4), .out(transistor_69_out), .gate(1'b0));
  Transistor transistor_70 (.in(mover_1_rd_c_1), .out(transistor_70_out), .gate(1'b0));
  Transistor transistor_71 (.in(mover_1_rd_c_2), .out(transistor_71_out), .gate(1'b0));
  Transistor transistor_72 (.in(mover_1_rd_c_3), .out(transistor_72_out), .gate(1'b0));
  Transistor transistor_73 (.in(mover_1_rd_c_4), .out(transistor_73_out), .gate(1'b0));
  Pull_Resistor pull_resistor_34 (.node(transistor_66_out));
  Pull_Resistor pull_resistor_35 (.node(transistor_67_out));
  Pull_Resistor pull_resistor_36 (.node(transistor_68_out));
  Pull_Resistor pull_resistor_37 (.node(transistor_69_out));
  Pull_Resistor pull_resistor_38 (.node(transistor_70_out));
  Pull_Resistor pull_resistor_39 (.node(transistor_71_out));
  Pull_Resistor pull_resistor_40 (.node(transistor_72_out));
  Transistor transistor_74 (.in(alu_1_rd_o_1), .out(transistor_66_out), .gate(1'b0));
  Transistor transistor_75 (.in(alu_1_rd_o_2), .out(transistor_67_out), .gate(1'b0));
  Transistor transistor_76 (.in(alu_1_rd_o_3), .out(transistor_68_out), .gate(1'b0));
  Transistor transistor_77 (.in(alu_1_rd_o_4), .out(transistor_69_out), .gate(1'b0));
  Transistor transistor_78 (.in(alu_1_rd_c_1), .out(transistor_70_out), .gate(1'b0));
  Transistor transistor_79 (.in(alu_1_rd_c_2), .out(transistor_71_out), .gate(1'b0));
  Transistor transistor_80 (.in(alu_1_rd_c_3), .out(transistor_72_out), .gate(1'b0));
  Transistor transistor_81 (.in(alu_1_rd_c_4), .out(transistor_73_out), .gate(1'b0));
  Transistor transistor_82 (.in(alu_1_ra_o_1), .out(transistor_66_out), .gate(1'b0));
  Transistor transistor_83 (.in(alu_1_ra_o_2), .out(transistor_67_out), .gate(1'b0));
  Transistor transistor_84 (.in(alu_1_ra_o_3), .out(transistor_68_out), .gate(1'b0));
  Transistor transistor_85 (.in(alu_1_ra_o_4), .out(transistor_69_out), .gate(1'b0));
  Transistor transistor_86 (.in(alu_1_ra_c_1), .out(transistor_70_out), .gate(1'b0));
  Transistor transistor_87 (.in(alu_1_ra_c_2), .out(transistor_71_out), .gate(1'b0));
  Transistor transistor_88 (.in(alu_1_ra_c_3), .out(transistor_72_out), .gate(1'b0));
  Transistor transistor_89 (.in(alu_1_ra_c_4), .out(transistor_73_out), .gate(1'b0));
  Transistor transistor_90 (.in(alu_1_rb_o_1), .out(transistor_66_out), .gate(1'b0));
  Transistor transistor_91 (.in(alu_1_rb_o_2), .out(transistor_67_out), .gate(1'b0));
  Transistor transistor_92 (.in(alu_1_rb_o_3), .out(transistor_68_out), .gate(1'b0));
  Transistor transistor_93 (.in(alu_1_rb_o_4), .out(transistor_69_out), .gate(1'b0));
  Transistor transistor_94 (.in(alu_1_rb_c_1), .out(transistor_70_out), .gate(1'b0));
  Transistor transistor_95 (.in(alu_1_rb_c_2), .out(transistor_71_out), .gate(1'b0));
  Transistor transistor_96 (.in(alu_1_rb_c_3), .out(transistor_72_out), .gate(1'b0));
  Transistor transistor_97 (.in(alu_1_rb_c_4), .out(transistor_73_out), .gate(1'b0));
  Transistor transistor_98 (.in(memory_address_manager_1_rd_o_1), .out(transistor_66_out), .gate(1'b0));
  Transistor transistor_99 (.in(memory_address_manager_1_rd_o_2), .out(transistor_67_out), .gate(1'b0));
  Transistor transistor_100 (.in(memory_address_manager_1_rd_o_3), .out(transistor_68_out), .gate(1'b0));
  Transistor transistor_101 (.in(memory_address_manager_1_rd_o_4), .out(transistor_69_out), .gate(1'b0));
  Transistor transistor_102 (.in(memory_address_manager_1_rd_c_1), .out(transistor_70_out), .gate(1'b0));
  Transistor transistor_103 (.in(memory_address_manager_1_rd_c_2), .out(transistor_71_out), .gate(1'b0));
  Transistor transistor_104 (.in(memory_address_manager_1_rd_c_3), .out(transistor_72_out), .gate(1'b0));
  Transistor transistor_105 (.in(memory_address_manager_1_rd_c_4), .out(transistor_73_out), .gate(1'b0));
  Transistor transistor_106 (.in(program_counter_1_rd_o_1), .out(transistor_66_out), .gate(1'b0));
  Transistor transistor_107 (.in(program_counter_1_rd_o_2), .out(transistor_67_out), .gate(1'b0));
  Transistor transistor_108 (.in(program_counter_1_rd_o_3), .out(transistor_68_out), .gate(1'b0));
  Transistor transistor_109 (.in(program_counter_1_rd_o_4), .out(transistor_69_out), .gate(1'b0));
  Transistor transistor_110 (.in(program_counter_1_rd_c_1), .out(transistor_70_out), .gate(1'b0));
  Transistor transistor_111 (.in(program_counter_1_rd_c_2), .out(transistor_71_out), .gate(1'b0));
  Transistor transistor_112 (.in(program_counter_1_rd_c_3), .out(transistor_72_out), .gate(1'b0));
  Transistor transistor_113 (.in(program_counter_1_rd_c_4), .out(transistor_73_out), .gate(1'b0));
  Transistor transistor_114 (.in(output_control_1_rd_o_1), .out(transistor_66_out), .gate(1'b0));
  Transistor transistor_115 (.in(output_control_1_rd_o_2), .out(transistor_67_out), .gate(1'b0));
  Transistor transistor_116 (.in(output_control_1_rd_o_3), .out(transistor_68_out), .gate(1'b0));
  Transistor transistor_117 (.in(output_control_1_rd_o_4), .out(transistor_69_out), .gate(1'b0));
  Transistor transistor_118 (.in(output_control_1_rd_c_1), .out(transistor_70_out), .gate(1'b0));
  Transistor transistor_119 (.in(output_control_1_rd_c_2), .out(transistor_71_out), .gate(1'b0));
  Transistor transistor_120 (.in(output_control_1_rd_c_3), .out(transistor_72_out), .gate(1'b0));
  Transistor transistor_121 (.in(output_control_1_rd_c_4), .out(transistor_73_out), .gate(1'b0));
  Pull_Resistor pull_resistor_41 (.node(transistor_73_out));
  D_Flip_Flop d_ff_271 (.D(transistor_66_out), .clk(transistor_70_out), .Q(d_ff_271_q));  // open: Qn, preset, reset
  D_Flip_Flop d_ff_272 (.D(transistor_67_out), .clk(transistor_71_out), .Q(d_ff_272_q));  // open: Qn, preset, reset
  D_Flip_Flop d_ff_273 (.D(transistor_68_out), .clk(transistor_72_out), .Q(d_ff_273_q));  // open: Qn, preset, reset
  D_Flip_Flop d_ff_274 (.D(transistor_69_out), .clk(transistor_73_out), .Q(d_ff_274_q));  // open: Qn, preset, reset
  D_Flip_Flop d_ff_275 (.D(d_ff_271_q), .clk(transistor_70_out), .Q(d_ff_275_q));  // open: Qn, preset, reset
  D_Flip_Flop d_ff_276 (.D(d_ff_272_q), .clk(transistor_71_out), .Q(d_ff_276_q));  // open: Qn, preset, reset
  D_Flip_Flop d_ff_277 (.D(d_ff_273_q), .clk(transistor_72_out), .Q(d_ff_277_q));  // open: Qn, preset, reset
  D_Flip_Flop d_ff_278 (.D(d_ff_274_q), .clk(transistor_73_out), .Q(d_ff_278_q));  // open: Qn, preset, reset
  D_Flip_Flop d_ff_279 (.D(d_ff_275_q), .clk(transistor_70_out), .Q(d_ff_279_q));  // open: Qn, preset, reset
  D_Flip_Flop d_ff_280 (.D(d_ff_276_q), .clk(transistor_71_out), .Q(d_ff_280_q));  // open: Qn, preset, reset
  D_Flip_Flop d_ff_281 (.D(d_ff_277_q), .clk(transistor_72_out), .Q(d_ff_281_q));  // open: Qn, preset, reset
  D_Flip_Flop d_ff_282 (.D(d_ff_278_q), .clk(transistor_73_out), .Q(d_ff_282_q));  // open: Qn, preset, reset
  D_Flip_Flop d_ff_283 (.D(d_ff_279_q), .clk(transistor_70_out), .Q(d_ff_283_q));  // open: Qn, preset, reset
  D_Flip_Flop d_ff_284 (.D(d_ff_280_q), .clk(transistor_71_out), .Q(d_ff_284_q));  // open: Qn, preset, reset
  D_Flip_Flop d_ff_285 (.D(d_ff_281_q), .clk(transistor_72_out), .Q(d_ff_285_q));  // open: Qn, preset, reset
  D_Flip_Flop d_ff_286 (.D(d_ff_282_q), .clk(transistor_73_out), .Q(d_ff_286_q));  // open: Qn, preset, reset
  D_Flip_Flop d_ff_287 (.D(d_ff_283_q), .clk(transistor_70_out), .Q(d_ff_287_q));  // open: Qn, preset, reset
  D_Flip_Flop d_ff_288 (.D(d_ff_284_q), .clk(transistor_71_out), .Q(d_ff_288_q));  // open: Qn, preset, reset
  D_Flip_Flop d_ff_289 (.D(d_ff_285_q), .clk(transistor_72_out), .Q(d_ff_289_q));  // open: Qn, preset, reset
  D_Flip_Flop d_ff_290 (.D(d_ff_286_q), .clk(transistor_73_out), .Q(d_ff_290_q));  // open: Qn, preset, reset
  D_Flip_Flop d_ff_291 (.D(d_ff_287_q), .clk(transistor_70_out), .Q(d_ff_291_q));  // open: Qn, preset, reset
  D_Flip_Flop d_ff_292 (.D(d_ff_288_q), .clk(transistor_71_out), .Q(d_ff_292_q));  // open: Qn, preset, reset
  D_Flip_Flop d_ff_293 (.D(d_ff_289_q), .clk(transistor_72_out), .Q(d_ff_293_q));  // open: Qn, preset, reset
  D_Flip_Flop d_ff_294 (.D(d_ff_290_q), .clk(transistor_73_out), .Q(d_ff_294_q));  // open: Qn, preset, reset
  D_Flip_Flop d_ff_295 (.D(d_ff_291_q), .clk(transistor_70_out), .Q(d_ff_295_q));  // open: Qn, preset, reset
  D_Flip_Flop d_ff_296 (.D(d_ff_292_q), .clk(transistor_71_out), .Q(d_ff_296_q));  // open: Qn, preset, reset
  D_Flip_Flop d_ff_297 (.D(d_ff_293_q), .clk(transistor_72_out), .Q(d_ff_297_q));  // open: Qn, preset, reset
  D_Flip_Flop d_ff_298 (.D(d_ff_294_q), .clk(transistor_73_out), .Q(d_ff_298_q));  // open: Qn, preset, reset
  D_Flip_Flop d_ff_299 (.D(d_ff_295_q), .clk(transistor_70_out), .Q(d_ff_299_q));  // open: Qn, preset, reset
  D_Flip_Flop d_ff_300 (.D(d_ff_296_q), .clk(transistor_71_out), .Q(d_ff_300_q));  // open: Qn, preset, reset
  D_Flip_Flop d_ff_301 (.D(d_ff_297_q), .clk(transistor_72_out), .Q(d_ff_301_q));  // open: Qn, preset, reset
  D_Flip_Flop d_ff_302 (.D(d_ff_298_q), .clk(transistor_73_out), .Q(d_ff_302_q));  // open: Qn, preset, reset
  D_Flip_Flop d_ff_303 (.D(d_ff_299_q), .clk(transistor_70_out), .Q(d_ff_303_q));  // open: Qn, preset, reset
  D_Flip_Flop d_ff_304 (.D(d_ff_300_q), .clk(transistor_71_out), .Q(d_ff_304_q));  // open: Qn, preset, reset
  D_Flip_Flop d_ff_305 (.D(d_ff_301_q), .clk(transistor_72_out), .Q(d_ff_305_q));  // open: Qn, preset, reset
  D_Flip_Flop d_ff_306 (.D(d_ff_302_q), .clk(transistor_73_out), .Q(d_ff_306_q));  // open: Qn, preset, reset
  DotMatrix #(.matrixcols(8), .matrixrows(8)) dotmatrix_1 (
    .col0(output_control_1_s_o_8), .col1(output_control_1_s_o_7), .col2(output_control_1_s_o_6),
    .col3(output_control_1_s_o_5), .col4(output_control_1_s_o_4), .col5(output_control_1_s_o_3),
    .col6(output_control_1_s_o_2), .col7(output_control_1_s_o_1));
endmodule

module instruction_register (
  input  instruction1,
  input  instruction2,
  input  instruction3,
  input  instruction4,
  input  rd_bit1,
  input  rd_bit2,
  input  ra_bit1,
  input  ra_bit2,
  input  rb_bit1,
  input  rb_bit2,
  output mov,
  output set,
  output add,
  output sub,
  output bin_and,
  output bin_or,
  output get,
  output show,
  output bin_not,
  output bin_xor,
  output bin_equal,
  output greater_than,
  output cond_if,
  output rd1,
  output rd2,
  output rd3,
  output rd4,
  output ra1,
  output ra2,
  output ra3,
  output ra4,
  output rb1,
  output rb2,
  output rb3,
  output rb4,
  output clear
);

  wire not_1_out, not_2_out, not_3_out, not_4_out, not_5_out, not_6_out;

  not not_1 (not_1_out, rd_bit1);
  not not_2 (not_2_out, rd_bit2);
  not not_3 (not_3_out, ra_bit1);
  not not_4 (not_4_out, ra_bit2);
  not not_5 (not_5_out, rb_bit1);
  not not_6 (not_6_out, rb_bit2);
  Transistor #(.\type ("n")) transistor_1 (.in(not_5_out), .out(rb1), .gate(1'b1));
  Transistor #(.\type ("n")) transistor_2 (.in(not_6_out), .out(rb1), .gate(1'b1));
  Pull_Resistor #(.pull(1)) pull_resistor_1 (.node(rb1));
  Transistor #(.\type ("n")) transistor_3 (.in(rb_bit1), .out(rb2), .gate(1'b1));
  Transistor #(.\type ("n")) transistor_4 (.in(not_6_out), .out(rb2), .gate(1'b1));
  Pull_Resistor #(.pull(1)) pull_resistor_2 (.node(rb2));
  Transistor #(.\type ("n")) transistor_5 (.in(not_5_out), .out(rb3), .gate(1'b1));
  Transistor #(.\type ("n")) transistor_6 (.in(rb_bit2), .out(rb3), .gate(1'b1));
  Pull_Resistor #(.pull(1)) pull_resistor_3 (.node(rb3));
  Transistor #(.\type ("n")) transistor_7 (.in(rb_bit1), .out(rb4), .gate(1'b1));
  Transistor #(.\type ("n")) transistor_8 (.in(rb_bit2), .out(rb4), .gate(1'b1));
  Pull_Resistor #(.pull(1)) pull_resistor_4 (.node(rb4));
  Decoder #(.select(4)) decoder_1 (
    .out0(mov), .out1(set), .out2(add), .out3(sub), .out4(bin_and), .out5(bin_or), .out6(get), .out7(show),
    .out8(bin_not), .out9(bin_xor), .out10(bin_equal), .out11(greater_than), .out12(cond_if), .out13(clear),
    .sel({instruction4, instruction3, instruction2, instruction1}), .en(1'b1));  // open: out14, out15
  Transistor #(.\type ("n")) transistor_9 (.in(not_1_out), .out(rd1), .gate(1'b1));
  Transistor #(.\type ("n")) transistor_10 (.in(not_2_out), .out(rd1), .gate(1'b1));
  Pull_Resistor #(.pull(1)) pull_resistor_5 (.node(rd1));
  Transistor #(.\type ("n")) transistor_11 (.in(rd_bit1), .out(rd2), .gate(1'b1));
  Transistor #(.\type ("n")) transistor_12 (.in(not_2_out), .out(rd2), .gate(1'b1));
  Pull_Resistor #(.pull(1)) pull_resistor_6 (.node(rd2));
  Transistor #(.\type ("n")) transistor_13 (.in(not_1_out), .out(rd3), .gate(1'b1));
  Transistor #(.\type ("n")) transistor_14 (.in(rd_bit2), .out(rd3), .gate(1'b1));
  Pull_Resistor #(.pull(1)) pull_resistor_7 (.node(rd3));
  Transistor #(.\type ("n")) transistor_15 (.in(rd_bit1), .out(rd4), .gate(1'b1));
  Transistor #(.\type ("n")) transistor_16 (.in(rd_bit2), .out(rd4), .gate(1'b1));
  Pull_Resistor #(.pull(1)) pull_resistor_8 (.node(rd4));
  Transistor #(.\type ("n")) transistor_17 (.in(not_3_out), .out(ra1), .gate(1'b1));
  Transistor #(.\type ("n")) transistor_18 (.in(not_4_out), .out(ra1), .gate(1'b1));
  Pull_Resistor #(.pull(1)) pull_resistor_9 (.node(ra1));
  Transistor #(.\type ("n")) transistor_19 (.in(ra_bit1), .out(ra2), .gate(1'b1));
  Transistor #(.\type ("n")) transistor_20 (.in(not_4_out), .out(ra2), .gate(1'b1));
  Pull_Resistor #(.pull(1)) pull_resistor_10 (.node(ra2));
  Transistor #(.\type ("n")) transistor_21 (.in(not_3_out), .out(ra3), .gate(1'b1));
  Transistor #(.\type ("n")) transistor_22 (.in(ra_bit2), .out(ra3), .gate(1'b1));
  Pull_Resistor #(.pull(1)) pull_resistor_11 (.node(ra3));
  Transistor #(.\type ("n")) transistor_23 (.in(ra_bit1), .out(ra4), .gate(1'b1));
  Transistor #(.\type ("n")) transistor_24 (.in(ra_bit2), .out(ra4), .gate(1'b1));
  Pull_Resistor #(.pull(1)) pull_resistor_12 (.node(ra4));
endmodule

module counter_8 (
  input  in_1,
  input  in_2,
  output CLK_A,
  output last_bit
);

  wire and_1_out, j_k_ff_1_q, j_k_ff_1_qn, j_k_ff_2_q, j_k_ff_2_qn, j_k_ff_3_q, j_k_ff_3_qn, j_k_ff_4_q,
       j_k_ff_4_qn, j_k_ff_5_q, j_k_ff_5_qn, j_k_ff_6_q, j_k_ff_6_qn, j_k_ff_7_q, j_k_ff_7_qn, not_1_out,
       not_2_out;

  not not_1 (not_1_out, CLK_A);
  and and_1 (and_1_out, not_1_out, in_1);
  not not_2 (not_2_out, and_1_out);
  J_K_Flip_Flop j_k_ff_1 (
    .J(and_1_out), .K(not_2_out), .clk(in_2), .Q(j_k_ff_1_q), .Qn(j_k_ff_1_qn));  // open: preset, reset
  Transistor transistor_1 (.in(j_k_ff_1_q), .out(CLK_A), .gate(1'b0));
  J_K_Flip_Flop j_k_ff_2 (
    .J(j_k_ff_1_q), .K(j_k_ff_1_qn), .clk(in_2), .Q(j_k_ff_2_q), .Qn(j_k_ff_2_qn));  // open: preset, reset
  Transistor transistor_2 (.in(j_k_ff_2_q), .out(CLK_A), .gate(1'b0));
  J_K_Flip_Flop j_k_ff_3 (
    .J(j_k_ff_2_q), .K(j_k_ff_2_qn), .clk(in_2), .Q(j_k_ff_3_q), .Qn(j_k_ff_3_qn));  // open: preset, reset
  Transistor transistor_3 (.in(j_k_ff_3_q), .out(CLK_A), .gate(1'b0));
  J_K_Flip_Flop j_k_ff_4 (
    .J(j_k_ff_3_q), .K(j_k_ff_3_qn), .clk(in_2), .Q(j_k_ff_4_q), .Qn(j_k_ff_4_qn));  // open: preset, reset
  Transistor transistor_4 (.in(j_k_ff_4_q), .out(CLK_A), .gate(1'b0));
  J_K_Flip_Flop j_k_ff_5 (
    .J(j_k_ff_4_q), .K(j_k_ff_4_qn), .clk(in_2), .Q(j_k_ff_5_q), .Qn(j_k_ff_5_qn));  // open: preset, reset
  Transistor transistor_5 (.in(j_k_ff_5_q), .out(CLK_A), .gate(1'b0));
  J_K_Flip_Flop j_k_ff_6 (
    .J(j_k_ff_5_q), .K(j_k_ff_5_qn), .clk(in_2), .Q(j_k_ff_6_q), .Qn(j_k_ff_6_qn));  // open: preset, reset
  Transistor transistor_6 (.in(j_k_ff_6_q), .out(CLK_A), .gate(1'b0));
  J_K_Flip_Flop j_k_ff_7 (
    .J(j_k_ff_6_q), .K(j_k_ff_6_qn), .clk(in_2), .Q(j_k_ff_7_q), .Qn(j_k_ff_7_qn));  // open: preset, reset
  Transistor transistor_7 (.in(j_k_ff_7_q), .out(CLK_A), .gate(1'b0));
  J_K_Flip_Flop j_k_ff_8 (.J(j_k_ff_7_q), .K(j_k_ff_7_qn), .clk(in_2), .Q(last_bit));  // open: Qn, preset, reset
  Pull_Resistor pull_resistor_1 (.node(CLK_A));
  Transistor transistor_8 (.in(last_bit), .out(CLK_A), .gate(1'b0));
endmodule

module mover (
  input  I1,
  input  CLK,
  input  CLK_A,
  input  is_move_on,
  input  is_seg1_on,
  input  is_seg2_on,
  input  is_seg3_on,
  input  is_seg4_on,
  output rd_o_1,
  output rd_o_2,
  output rd_o_3,
  output rd_o_4,
  output rd_c_1,
  output rd_c_2,
  output rd_c_3,
  output rd_c_4,
  output CSR1
);

  wire and_1_out, and_2_out, and_3_out, and_4_out, and_9_out, and_10_out, and_11_out, and_12_out;

  and and_1 (and_1_out, is_move_on, is_seg1_on);
  and and_2 (and_2_out, is_move_on, is_seg2_on);
  and and_3 (and_3_out, is_move_on, is_seg3_on);
  and and_4 (and_4_out, is_move_on, is_seg4_on);
  and and_5 (rd_o_1, I1, and_1_out);
  and and_6 (rd_o_2, I1, and_2_out);
  and and_7 (rd_o_3, I1, and_3_out);
  and and_8 (rd_o_4, I1, and_4_out);
  and and_9 (and_9_out, CLK_A, and_1_out);
  and and_10 (and_10_out, CLK_A, and_2_out);
  and and_11 (and_11_out, CLK_A, and_3_out);
  and and_12 (and_12_out, CLK_A, and_4_out);
  and and_13 (rd_c_1, CLK, and_9_out);
  and and_14 (rd_c_2, CLK, and_10_out);
  and and_15 (rd_c_3, CLK, and_11_out);
  and and_16 (rd_c_4, CLK, and_12_out);
  Transistor transistor_1 (.in(rd_c_1), .out(CSR1), .gate(1'b0));
  Transistor transistor_2 (.in(rd_c_2), .out(CSR1), .gate(1'b0));
  Transistor transistor_3 (.in(rd_c_3), .out(CSR1), .gate(1'b0));
  Transistor transistor_4 (.in(rd_c_4), .out(CSR1), .gate(1'b0));
  Pull_Resistor pull_resistor_1 (.node(CSR1));
endmodule

module adder_cpu (
  input  RFI_1,
  input  RFI_2,
  input  RFI_3,
  input  RFI_4,
  input  CLK,
  input  CLK_A,
  input  is_add_on,
  input  ra_1,
  input  ra_2,
  input  ra_3,
  input  ra_4,
  input  rb_1,
  input  rb_2,
  input  rb_3,
  input  rb_4,
  input  rd_1,
  input  rd_2,
  input  rd_3,
  input  rd_4,
  input  is_sub_on,
  input  is_and_on,
  output rd_o_1,
  output rd_o_2,
  output rd_o_3,
  output rd_o_4,
  output rd_c_1,
  output rd_c_2,
  output rd_c_3,
  output rd_c_4,
  output ra_o_1,
  output ra_o_2,
  output ra_o_3,
  output ra_o_4,
  output ra_c_1,
  output ra_c_2,
  output ra_c_3,
  output ra_c_4,
  output rb_o_1,
  output rb_o_2,
  output rb_o_3,
  output rb_o_4,
  output rb_c_1,
  output rb_c_2,
  output rb_c_3,
  output rb_c_4
);

  wire and_1_out, and_2_out, and_3_out, and_4_out, and_5_out, and_6_out, and_7_out, and_8_out, and_9_out,
       and_10_out, and_11_out, and_12_out, and_13_out, and_14_out, and_15_out, and_16_out, and_17_out,
       and_18_out, and_19_out, and_20_out, and_21_out, and_22_out, and_23_out, and_24_out, and_25_out,
       and_34_out, and_35_out, and_36_out, and_37_out, and_38_out, and_39_out, and_40_out, and_41_out,
       and_42_out, and_43_out, and_44_out, and_45_out, and_46_out, and_47_out, and_48_out, and_49_out,
       and_50_out, and_51_out, and_52_out, and_53_out, and_54_out, and_55_out, and_56_out, and_57_out,
       and_58_out, and_59_out, and_60_out, and_61_out, and_62_out, and_63_out, and_64_out, and_65_out,
       and_66_out, and_67_out, and_68_out, and_69_out, and_70_out, and_71_out, and_72_out, and_73_out,
       and_74_out, and_75_out, and_76_out, and_77_out, and_78_out, and_79_out, and_80_out, and_81_out,
       and_82_out, and_83_out, and_84_out, and_85_out, and_86_out, and_87_out, and_88_out, and_89_out,
       and_90_out, and_91_out, and_92_out, and_93_out, and_94_out, and_95_out, and_96_out, and_97_out,
       and_98_out, and_99_out, and_100_out, and_101_out, and_102_out, and_103_out, and_104_out, and_105_out,
       and_106_out, and_107_out, and_108_out, and_109_out, and_110_out, and_111_out, and_112_out,
       and_113_out, and_114_out, and_115_out, and_116_out, and_117_out, and_118_out, and_119_out,
       and_120_out, and_121_out, and_122_out, and_123_out, and_124_out, and_125_out, and_126_out,
       and_127_out, d_ff_1_q, d_ff_1_qn, j_k_ff_1_q, j_k_ff_1_qn, not_1_out, not_2_out, not_3_out, not_4_out,
       not_5_out, or_1_out, or_2_out, or_3_out, or_4_out, or_5_out, or_6_out, pull_resistor_1_node,
       pull_resistor_2_node, xor_1_out, xor_2_out, xor_3_out;

  and and_1 (and_1_out, CLK, CLK_A);
  and and_2 (and_2_out, ra_1, RFI_1);
  and and_3 (and_3_out, ra_2, RFI_2);
  and and_4 (and_4_out, ra_3, RFI_3);
  and and_5 (and_5_out, ra_4, RFI_4);
  and and_6 (and_6_out, rb_1, RFI_1);
  and and_7 (and_7_out, rb_2, RFI_2);
  and and_8 (and_8_out, rb_3, RFI_3);
  and and_9 (and_9_out, rb_4, RFI_4);
  and and_10 (and_10_out, rd_1, is_add_on);
  and and_11 (and_11_out, rd_2, is_add_on);
  and and_12 (and_12_out, rd_3, is_add_on);
  and and_13 (and_13_out, rb_1, is_add_on);
  and and_14 (and_14_out, rd_1, is_sub_on);
  and and_15 (and_15_out, rd_2, is_sub_on);
  and and_16 (and_16_out, rd_3, is_sub_on);
  and and_17 (and_17_out, rb_1, is_sub_on);
  and and_18 (and_18_out, ra_1, is_sub_on);
  and and_19 (and_19_out, ra_2, is_sub_on);
  and and_20 (and_20_out, ra_3, is_sub_on);
  and and_21 (and_21_out, ra_4, is_sub_on);
  and and_22 (and_22_out, rb_1, is_sub_on);
  and and_23 (and_23_out, rb_2, is_sub_on);
  and and_24 (and_24_out, rb_3, is_sub_on);
  and and_25 (and_25_out, rb_4, is_sub_on);
  // AND_Gate and_26 has open pins: in0=ra_1, in1=is_and_on, out=open
  // AND_Gate and_27 has open pins: in0=ra_2, in1=is_and_on, out=open
  // AND_Gate and_28 has open pins: in0=ra_3, in1=is_and_on, out=open
  // AND_Gate and_29 has open pins: in0=ra_4, in1=is_and_on, out=open
  // AND_Gate and_30 has open pins: in0=rb_1, in1=is_and_on, out=open
  // AND_Gate and_31 has open pins: in0=rb_2, in1=is_and_on, out=open
  // AND_Gate and_32 has open pins: in0=rb_3, in1=is_and_on, out=open
  // AND_Gate and_33 has open pins: in0=rb_4, in1=is_and_on, out=open
  and and_34 (and_34_out, is_and_on, rd_1);
  and and_35 (and_35_out, is_and_on, rd_2);
  and and_36 (and_36_out, is_and_on, rd_3);
  and and_37 (and_37_out, is_and_on, rb_1);
  and and_38 (and_38_out, and_1_out, is_add_on);
  Pull_Resistor pull_resistor_1 (.node(pull_resistor_1_node));
  Transistor transistor_1 (.in(and_2_out), .out(pull_resistor_1_node), .gate(1'b0));
  Transistor transistor_2 (.in(and_3_out), .out(pull_resistor_1_node), .gate(1'b0));
  Transistor transistor_3 (.in(and_4_out), .out(pull_resistor_1_node), .gate(1'b0));
  Transistor transistor_4 (.in(and_5_out), .out(pull_resistor_1_node), .gate(1'b0));
  Pull_Resistor pull_resistor_2 (.node(pull_resistor_2_node));
  Transistor transistor_5 (.in(and_6_out), .out(pull_resistor_2_node), .gate(1'b0));
  Transistor transistor_6 (.in(and_7_out), .out(pull_resistor_2_node), .gate(1'b0));
  Transistor transistor_7 (.in(and_8_out), .out(pull_resistor_2_node), .gate(1'b0));
  Transistor transistor_8 (.in(and_9_out), .out(pull_resistor_2_node), .gate(1'b0));
  and and_39 (and_39_out, is_add_on, pull_resistor_1_node);
  and and_40 (and_40_out, is_add_on, pull_resistor_2_node);
  D_Flip_Flop d_ff_1 (.D(or_4_out), .clk(and_38_out), .Q(d_ff_1_q), .Qn(d_ff_1_qn));  // open: preset, reset
  and and_41 (and_41_out, is_sub_on, and_1_out);
  and and_42 (and_42_out, pull_resistor_1_node, pull_resistor_2_node);
  and and_43 (and_43_out, and_1_out, is_and_on);
  xor xor_1 (xor_1_out, and_39_out, and_40_out);
  and and_44 (and_44_out, and_39_out, and_40_out);
  or or_1 (or_1_out, and_39_out, and_40_out);
  and and_45 (and_45_out, is_sub_on, pull_resistor_1_node);
  and and_46 (and_46_out, is_sub_on, pull_resistor_2_node);
  not not_1 (not_1_out, xor_1_out);
  J_K_Flip_Flop j_k_ff_1 (
    .J(or_6_out), .K(not_2_out), .clk(and_41_out), .Q(j_k_ff_1_q), .Qn(j_k_ff_1_qn));  // open: preset, reset
  not not_2 (not_2_out, or_6_out);
  xor xor_2 (xor_2_out, and_45_out, and_46_out);
  not not_3 (not_3_out, and_45_out);
  and and_47 (and_47_out, not_3_out, and_46_out);
  xor xor_3 (xor_3_out, and_45_out, and_46_out);
  not not_4 (not_4_out, and_45_out);
  or or_2 (or_2_out, not_4_out, and_46_out);
  and and_48 (and_48_out, d_ff_1_qn, xor_1_out);
  and and_49 (and_49_out, d_ff_1_q, not_1_out);
  and and_50 (and_50_out, d_ff_1_qn, and_44_out);
  and and_51 (and_51_out, d_ff_1_q, or_1_out);
  not not_5 (not_5_out, xor_3_out);
  or or_3 (or_3_out, and_48_out, and_49_out);
  or or_4 (or_4_out, and_50_out, and_51_out);
  and and_52 (and_52_out, j_k_ff_1_qn, xor_2_out);
  and and_53 (and_53_out, not_5_out, j_k_ff_1_q);
  or or_5 (or_5_out, and_52_out, and_53_out);
  and and_54 (and_54_out, j_k_ff_1_qn, and_47_out);
  and and_55 (and_55_out, or_2_out, j_k_ff_1_q);
  or or_6 (or_6_out, and_54_out, and_55_out);
  and and_56 (and_56_out, or_3_out, and_10_out);
  and and_57 (and_57_out, or_3_out, and_11_out);
  and and_58 (and_58_out, or_3_out, and_12_out);
  and and_59 (and_59_out, or_3_out, and_13_out);
  and and_60 (and_60_out, and_38_out, and_10_out);
  and and_61 (and_61_out, and_38_out, and_11_out);
  and and_62 (and_62_out, and_38_out, and_12_out);
  and and_63 (and_63_out, and_38_out, and_13_out);
  and and_64 (and_64_out, and_2_out, is_add_on);
  and and_65 (and_65_out, and_3_out, is_add_on);
  and and_66 (and_66_out, and_4_out, is_add_on);
  and and_67 (and_67_out, and_5_out, is_add_on);
  and and_68 (and_68_out, and_38_out, ra_1);
  and and_69 (and_69_out, and_38_out, ra_2);
  and and_70 (and_70_out, and_38_out, ra_3);
  and and_71 (and_71_out, and_38_out, ra_4);
  and and_72 (and_72_out, and_6_out, is_add_on);
  and and_73 (and_73_out, and_7_out, is_add_on);
  and and_74 (and_74_out, and_8_out, is_add_on);
  and and_75 (and_75_out, and_9_out, is_add_on);
  and and_76 (and_76_out, and_38_out, rb_1);
  and and_77 (and_77_out, and_38_out, rb_2);
  and and_78 (and_78_out, and_38_out, rb_3);
  and and_79 (and_79_out, and_38_out, rb_4);
  and and_80 (and_80_out, or_5_out, and_14_out);
  and and_81 (and_81_out, or_5_out, and_15_out);
  and and_82 (and_82_out, or_5_out, and_16_out);
  and and_83 (and_83_out, or_5_out, and_17_out);
  and and_84 (and_84_out, and_41_out, and_14_out);
  and and_85 (and_85_out, and_41_out, and_15_out);
  and and_86 (and_86_out, and_41_out, and_16_out);
  and and_87 (and_87_out, and_41_out, and_17_out);
  and and_88 (and_88_out, and_2_out, is_sub_on);
  and and_89 (and_89_out, and_3_out, is_sub_on);
  and and_90 (and_90_out, and_4_out, is_sub_on);
  and and_91 (and_91_out, and_5_out, is_sub_on);
  and and_92 (and_92_out, and_41_out, and_18_out);
  and and_93 (and_93_out, and_41_out, and_19_out);
  and and_94 (and_94_out, and_41_out, and_20_out);
  and and_95 (and_95_out, and_41_out, and_21_out);
  and and_96 (and_96_out, and_6_out, is_sub_on);
  and and_97 (and_97_out, and_7_out, is_sub_on);
  and and_98 (and_98_out, and_8_out, is_sub_on);
  and and_99 (and_99_out, and_9_out, is_sub_on);
  and and_100 (and_100_out, and_41_out, and_22_out);
  and and_101 (and_101_out, and_41_out, and_23_out);
  and and_102 (and_102_out, and_41_out, and_24_out);
  and and_103 (and_103_out, and_41_out, and_25_out);
  and and_104 (and_104_out, and_42_out, and_34_out);
  and and_105 (and_105_out, and_42_out, and_35_out);
  and and_106 (and_106_out, and_42_out, and_36_out);
  and and_107 (and_107_out, and_42_out, and_37_out);
  and and_108 (and_108_out, and_34_out, and_43_out);
  and and_109 (and_109_out, and_35_out, and_43_out);
  and and_110 (and_110_out, and_36_out, and_43_out);
  and and_111 (and_111_out, and_37_out, and_43_out);
  // AND_Gate and_112 has open pins: out=and_112_out
  // AND_Gate and_113 has open pins: out=and_113_out
  // AND_Gate and_114 has open pins: out=and_114_out
  // AND_Gate and_115 has open pins: out=and_115_out
  // AND_Gate and_116 has open pins: out=and_116_out
  // AND_Gate and_117 has open pins: out=and_117_out
  // AND_Gate and_118 has open pins: out=and_118_out
  // AND_Gate and_119 has open pins: out=and_119_out
  // AND_Gate and_120 has open pins: out=and_120_out
  // AND_Gate and_121 has open pins: out=and_121_out
  // AND_Gate and_122 has open pins: out=and_122_out
  // AND_Gate and_123 has open pins: out=and_123_out
  // AND_Gate and_124 has open pins: out=and_124_out
  // AND_Gate and_125 has open pins: out=and_125_out
  // AND_Gate and_126 has open pins: out=and_126_out
  // AND_Gate and_127 has open pins: out=and_127_out
  Transistor transistor_9 (.in(and_56_out), .out(rd_o_1), .gate(1'b0));
  Pull_Resistor pull_resistor_3 (.node(rd_o_1));
  Transistor transistor_10 (.in(and_57_out), .out(rd_o_2), .gate(1'b0));
  Pull_Resistor pull_resistor_4 (.node(rd_o_2));
  Transistor transistor_11 (.in(and_58_out), .out(rd_o_3), .gate(1'b0));
  Transistor transistor_12 (.in(and_59_out), .out(rd_o_4), .gate(1'b0));
  Transistor transistor_13 (.in(and_60_out), .out(rd_c_1), .gate(1'b0));
  Transistor transistor_14 (.in(and_61_out), .out(rd_c_2), .gate(1'b0));
  Transistor transistor_15 (.in(and_62_out), .out(rd_c_3), .gate(1'b0));
  Transistor transistor_16 (.in(and_63_out), .out(rd_c_4), .gate(1'b0));
  Transistor transistor_17 (.in(and_64_out), .out(ra_o_1), .gate(1'b0));
  Transistor transistor_18 (.in(and_65_out), .out(ra_o_2), .gate(1'b0));
  Transistor transistor_19 (.in(and_66_out), .out(ra_o_3), .gate(1'b0));
  Transistor transistor_20 (.in(and_67_out), .out(ra_o_4), .gate(1'b0));
  Transistor transistor_21 (.in(and_68_out), .out(ra_c_1), .gate(1'b0));
  Transistor transistor_22 (.in(and_69_out), .out(ra_c_2), .gate(1'b0));
  Transistor transistor_23 (.in(and_70_out), .out(ra_c_3), .gate(1'b0));
  Transistor transistor_24 (.in(and_71_out), .out(ra_c_4), .gate(1'b0));
  Transistor transistor_25 (.in(and_72_out), .out(rb_o_1), .gate(1'b0));
  Transistor transistor_26 (.in(and_73_out), .out(rb_o_2), .gate(1'b0));
  Transistor transistor_27 (.in(and_74_out), .out(rb_o_3), .gate(1'b0));
  Transistor transistor_28 (.in(and_75_out), .out(rb_o_4), .gate(1'b0));
  Transistor transistor_29 (.in(and_76_out), .out(rb_c_1), .gate(1'b0));
  Transistor transistor_30 (.in(and_77_out), .out(rb_c_2), .gate(1'b0));
  Transistor transistor_31 (.in(and_78_out), .out(rb_c_3), .gate(1'b0));
  Transistor transistor_32 (.in(and_79_out), .out(rb_c_4), .gate(1'b0));
  Transistor transistor_33 (.in(and_80_out), .out(rd_o_1), .gate(1'b0));
  Transistor transistor_34 (.in(and_81_out), .out(rd_o_2), .gate(1'b0));
  Transistor transistor_35 (.in(and_82_out), .out(rd_o_3), .gate(1'b0));
  Transistor transistor_36 (.in(and_83_out), .out(rd_o_4), .gate(1'b0));
  Transistor transistor_37 (.in(and_84_out), .out(rd_c_1), .gate(1'b0));
  Transistor transistor_38 (.in(and_85_out), .out(rd_c_2), .gate(1'b0));
  Transistor transistor_39 (.in(and_86_out), .out(rd_c_3), .gate(1'b0));
  Transistor transistor_40 (.in(and_87_out), .out(rd_c_4), .gate(1'b0));
  Transistor transistor_41 (.in(and_88_out), .out(ra_o_1), .gate(1'b0));
  Transistor transistor_42 (.in(and_89_out), .out(ra_o_2), .gate(1'b0));
  Transistor transistor_43 (.in(and_90_out), .out(ra_o_3), .gate(1'b0));
  Transistor transistor_44 (.in(and_91_out), .out(ra_o_4), .gate(1'b0));
  Transistor transistor_45 (.in(and_92_out), .out(ra_c_1), .gate(1'b0));
  Transistor transistor_46 (.in(and_93_out), .out(ra_c_2), .gate(1'b0));
  Transistor transistor_47 (.in(and_94_out), .out(ra_c_3), .gate(1'b0));
  Transistor transistor_48 (.in(and_95_out), .out(ra_c_4), .gate(1'b0));
  Transistor transistor_49 (.in(and_96_out), .out(rb_o_1), .gate(1'b0));
  Transistor transistor_50 (.in(and_97_out), .out(rb_o_2), .gate(1'b0));
  Transistor transistor_51 (.in(and_98_out), .out(rb_o_3), .gate(1'b0));
  Transistor transistor_52 (.in(and_99_out), .out(rb_o_4), .gate(1'b0));
  Transistor transistor_53 (.in(and_100_out), .out(rb_c_1), .gate(1'b0));
  Transistor transistor_54 (.in(and_101_out), .out(rb_c_2), .gate(1'b0));
  Transistor transistor_55 (.in(and_102_out), .out(rb_c_3), .gate(1'b0));
  Transistor transistor_56 (.in(and_103_out), .out(rb_c_4), .gate(1'b0));
  Transistor transistor_57 (.in(and_104_out), .gate(1'b0));  // open: out
  Transistor transistor_58 (.in(and_105_out), .gate(1'b0));  // open: out
  Transistor transistor_59 (.in(and_106_out), .gate(1'b0));  // open: out
  Transistor transistor_60 (.in(and_107_out), .gate(1'b0));  // open: out
  Transistor transistor_61 (.in(and_108_out), .gate(1'b0));  // open: out
  Transistor transistor_62 (.in(and_109_out), .gate(1'b0));  // open: out
  Transistor transistor_63 (.in(and_110_out), .gate(1'b0));  // open: out
  Transistor transistor_64 (.in(and_111_out), .gate(1'b0));  // open: out
  Transistor transistor_65 (.in(and_112_out), .gate(1'b0));  // open: out
  Transistor transistor_66 (.in(and_113_out), .gate(1'b0));  // open: out
  Transistor transistor_67 (.in(and_114_out), .gate(1'b0));  // open: out
  Transistor transistor_68 (.in(and_115_out), .gate(1'b0));  // open: out
  Transistor transistor_69 (.in(and_116_out), .gate(1'b0));  // open: out
  Transistor transistor_70 (.in(and_117_out), .gate(1'b0));  // open: out
  Transistor transistor_71 (.in(and_118_out), .gate(1'b0));  // open: out
  Transistor transistor_72 (.in(and_119_out), .gate(1'b0));  // open: out
  Transistor transistor_73 (.in(and_120_out), .gate(1'b0));  // open: out
  Transistor transistor_74 (.in(and_121_out), .gate(1'b0));  // open: out
  Transistor transistor_75 (.in(and_122_out), .gate(1'b0));  // open: out
  Transistor transistor_76 (.in(and_123_out), .gate(1'b0));  // open: out
  Transistor transistor_77 (.in(and_124_out), .gate(1'b0));  // open: out
  Transistor transistor_78 (.in(and_125_out), .gate(1'b0));  // open: out
  Transistor transistor_79 (.in(and_126_out), .gate(1'b0));  // open: out
  Transistor transistor_80 (.in(and_127_out), .gate(1'b0));  // open: out
  Pull_Resistor pull_resistor_5 (.node(rd_o_3));
  Pull_Resistor pull_resistor_6 (.node(rd_o_4));
  Pull_Resistor pull_resistor_7 (.node(rd_c_1));
  Pull_Resistor pull_resistor_8 (.node(rd_c_2));
  Pull_Resistor pull_resistor_9 (.node(rd_c_3));
  Pull_Resistor pull_resistor_10 (.node(rd_c_4));
  Pull_Resistor pull_resistor_11 (.node(ra_o_1));
  Pull_Resistor pull_resistor_12 (.node(ra_o_2));
  Pull_Resistor pull_resistor_13 (.node(ra_o_3));
  Pull_Resistor pull_resistor_14 (.node(ra_o_4));
  Pull_Resistor pull_resistor_15 (.node(ra_c_1));
  Pull_Resistor pull_resistor_16 (.node(ra_c_2));
  Pull_Resistor pull_resistor_17 (.node(ra_c_3));
  Pull_Resistor pull_resistor_18 (.node(ra_c_4));
  Pull_Resistor pull_resistor_19 (.node(rb_o_1));
  Pull_Resistor pull_resistor_20 (.node(rb_o_2));
  Pull_Resistor pull_resistor_21 (.node(rb_o_3));
  Pull_Resistor pull_resistor_22 (.node(rb_o_4));
  Pull_Resistor pull_resistor_23 (.node(rb_c_1));
  Pull_Resistor pull_resistor_24 (.node(rb_c_2));
  Pull_Resistor pull_resistor_25 (.node(rb_c_3));
  Pull_Resistor pull_resistor_26 (.node(rb_c_4));

  assign rd_4 = rb_1;
endmodule
module ALU (
  input  RFI_1,
  input  RFI_2,
  input  RFI_3,
  input  RFI_4,
  input  CLK,
  input  CLK_A,
  input  is_add_on,
  input  ra_1,
  input  ra_2,
  input  ra_3,
  input  ra_4,
  input  rb_1,
  input  rb_2,
  input  rb_3,
  input  rb_4,
  input  rd_1,
  input  rd_2,
  input  rd_3,
  input  rd_4,
  input  is_sub_on,
  input  is_and_on,
  input  is_or_on,
  input  is_not_on,
  input  is_equal_on,
  input  is_xor_on,
  input  is_gt_on,
  input  is_last_on,
  output rd_o_1,
  output rd_o_2,
  output rd_o_3,
  output rd_o_4,
  output rd_c_1,
  output rd_c_2,
  output rd_c_3,
  output rd_c_4,
  output ra_o_1,
  output ra_o_2,
  output ra_o_3,
  output ra_o_4,
  output ra_c_1,
  output ra_c_2,
  output ra_c_3,
  output ra_c_4,
  output rb_o_1,
  output rb_o_2,
  output rb_o_3,
  output rb_o_4,
  output rb_c_1,
  output rb_c_2,
  output rb_c_3,
  output rb_c_4
);

  wire and_1_out, and_2_out, and_3_out, and_4_out, and_5_out, and_6_out, and_7_out, and_8_out, and_9_out,
       and_10_out, and_11_out, and_12_out, and_13_out, and_14_out, and_15_out, and_16_out, and_17_out,
       and_18_out, and_19_out, and_20_out, and_21_out, and_22_out, and_23_out, and_24_out, and_25_out,
       and_26_out, and_27_out, and_28_out, and_29_out, and_30_out, and_31_out, and_32_out, and_33_out,
       and_34_out, and_35_out, and_36_out, and_37_out, and_38_out, and_39_out, and_40_out, and_41_out,
       and_42_out, and_43_out, and_44_out, and_45_out, and_46_out, and_47_out, and_48_out, and_49_out,
       and_50_out, and_51_out, and_52_out, and_53_out, and_54_out, and_55_out, d_ff_1_q, d_ff_2_q, d_ff_2_qn,
       d_ff_3_q, d_ff_3_qn, j_k_ff_1_q, j_k_ff_1_qn, not_1_out, not_2_out, not_3_out, not_4_out, not_5_out,
       not_6_out, not_7_out, not_8_out, not_9_out, not_10_out, or_1_out, or_2_out, or_3_out, or_4_out,
       or_5_out, or_6_out, or_7_out, or_8_out, or_9_out, or_10_out, or_11_out, or_12_out, transistor_1_out,
       transistor_5_out, transistor_9_out, transistor_10_out, xor_1_out, xor_2_out, xor_3_out, xor_4_out,
       xor_5_out;

  and and_1 (and_1_out, CLK, CLK_A);
  and and_2 (and_2_out, RFI_1, ra_1);
  and and_3 (and_3_out, RFI_2, ra_2);
  and and_4 (and_4_out, RFI_3, ra_3);
  and and_5 (and_5_out, RFI_4, ra_4);
  and and_6 (and_6_out, RFI_1, rb_1);
  and and_7 (and_7_out, RFI_2, rb_2);
  and and_8 (and_8_out, RFI_3, rb_3);
  and and_9 (and_9_out, RFI_4, rb_4);
  not not_1 (not_1_out, is_last_on);
  not not_2 (not_2_out, is_last_on);
  Transistor transistor_1 (.in(and_2_out), .out(transistor_1_out), .gate(1'b0));
  Transistor transistor_2 (.in(and_3_out), .out(transistor_1_out), .gate(1'b0));
  Transistor transistor_3 (.in(and_4_out), .out(transistor_1_out), .gate(1'b0));
  Transistor transistor_4 (.in(and_5_out), .out(transistor_1_out), .gate(1'b0));
  Transistor transistor_5 (.in(and_6_out), .out(transistor_5_out), .gate(1'b0));
  Transistor transistor_6 (.in(and_7_out), .out(transistor_5_out), .gate(1'b0));
  Transistor transistor_7 (.in(and_8_out), .out(transistor_5_out), .gate(1'b0));
  Transistor transistor_8 (.in(and_9_out), .out(transistor_5_out), .gate(1'b0));
  and and_10 (and_10_out, or_4_out, not_1_out);
  and and_11 (and_11_out, not_2_out, or_9_out);
  and and_12 (and_12_out, and_1_out, is_add_on);
  Pull_Resistor pull_resistor_1 (.node(transistor_1_out));
  Pull_Resistor pull_resistor_2 (.node(transistor_5_out));
  and and_13 (and_13_out, and_1_out, is_sub_on);
  and and_14 (and_14_out, is_equal_on, and_1_out);
  D_Flip_Flop d_ff_1 (.D(and_10_out), .clk(and_14_out), .Q(d_ff_1_q));  // open: Qn, preset, reset
  not not_3 (not_3_out, transistor_5_out);
  D_Flip_Flop d_ff_2 (.D(and_11_out), .clk(and_15_out), .Q(d_ff_2_q), .Qn(d_ff_2_qn));  // open: preset, reset
  and and_15 (and_15_out, and_1_out, is_gt_on);
  xor xor_1 (xor_1_out, transistor_1_out, transistor_5_out);
  not not_4 (not_4_out, xor_1_out);
  and and_16 (and_16_out, transistor_1_out, transistor_5_out);
  or or_1 (or_1_out, transistor_1_out, transistor_5_out);
  D_Flip_Flop d_ff_3 (.D(or_7_out), .clk(and_12_out), .Q(d_ff_3_q), .Qn(d_ff_3_qn));  // open: preset, reset
  J_K_Flip_Flop j_k_ff_1 (
    .J(or_11_out), .K(not_5_out), .clk(and_13_out), .Q(j_k_ff_1_q), .Qn(j_k_ff_1_qn));  // open: preset, reset
  not not_5 (not_5_out, or_11_out);
  xor xor_2 (xor_2_out, transistor_1_out, transistor_5_out);
  xor xor_3 (xor_3_out, transistor_1_out, transistor_5_out);
  xor xor_4 (xor_4_out, transistor_1_out, transistor_5_out);
  not not_6 (not_6_out, transistor_1_out);
  and and_17 (and_17_out, not_6_out, transistor_5_out);
  xor xor_5 (xor_5_out, transistor_1_out, transistor_5_out);
  not not_7 (not_7_out, transistor_1_out);
  or or_2 (or_2_out, not_7_out, transistor_5_out);
  and and_18 (and_18_out, transistor_1_out, transistor_5_out);
  or or_3 (or_3_out, transistor_1_out, transistor_5_out);
  not not_8 (not_8_out, transistor_1_out);
  or or_4 (or_4_out, xor_2_out, d_ff_1_q);
  and and_19 (and_19_out, transistor_1_out, not_3_out);
  or or_5 (or_5_out, transistor_1_out, not_3_out);
  and and_20 (and_20_out, d_ff_3_qn, xor_1_out);
  and and_21 (and_21_out, d_ff_3_q, not_4_out);
  and and_22 (and_22_out, d_ff_3_qn, and_16_out);
  and and_23 (and_23_out, d_ff_3_q, or_1_out);
  not not_9 (not_9_out, xor_5_out);
  and and_24 (and_24_out, is_last_on, xor_2_out);
  and and_25 (and_25_out, d_ff_1_q, is_last_on);
  and and_26 (and_26_out, and_19_out, d_ff_2_qn);
  and and_27 (and_27_out, or_5_out, d_ff_2_q);
  or or_6 (or_6_out, and_20_out, and_21_out);
  or or_7 (or_7_out, and_22_out, and_23_out);
  and and_28 (and_28_out, j_k_ff_1_qn, xor_4_out);
  and and_29 (and_29_out, not_9_out, j_k_ff_1_q);
  or or_8 (or_8_out, and_24_out, and_25_out);
  or or_9 (or_9_out, and_26_out, and_27_out);
  or or_10 (or_10_out, and_28_out, and_29_out);
  and and_30 (and_30_out, j_k_ff_1_qn, and_17_out);
  and and_31 (and_31_out, or_2_out, j_k_ff_1_q);
  and and_32 (and_32_out, is_equal_on, and_41_out);
  and and_33 (and_33_out, or_8_out, is_equal_on);
  and and_34 (and_34_out, or_9_out, is_last_on);
  and and_35 (and_35_out, d_ff_2_q, is_last_on);
  and and_36 (and_36_out, is_add_on, or_6_out);
  and and_37 (and_37_out, is_sub_on, or_10_out);
  or or_11 (or_11_out, and_30_out, and_31_out);
  and and_38 (and_38_out, is_and_on, and_18_out);
  and and_39 (and_39_out, is_or_on, or_3_out);
  and and_40 (and_40_out, not_8_out, is_not_on);
  and and_41 (and_41_out, is_last_on, not_10_out);
  not not_10 (not_10_out, and_33_out);
  Transistor transistor_9 (.in(and_42_out), .out(transistor_9_out), .gate(1'b0));
  and and_42 (and_42_out, xor_3_out, is_xor_on);
  Transistor transistor_10 (.in(is_xor_on), .out(transistor_10_out), .gate(1'b0));
  or or_12 (or_12_out, and_34_out, and_35_out);
  Pull_Resistor pull_resistor_3 (.node(transistor_10_out));
  Transistor transistor_11 (.in(is_add_on), .out(transistor_10_out), .gate(1'b0));
  and and_43 (and_43_out, rd_1, and_1_out);
  and and_44 (and_44_out, rd_2, and_1_out);
  and and_45 (and_45_out, rd_3, and_1_out);
  and and_46 (and_46_out, rd_4, and_1_out);
  and and_47 (and_47_out, ra_1, and_1_out);
  and and_48 (and_48_out, ra_2, and_1_out);
  and and_49 (and_49_out, ra_3, and_1_out);
  and and_50 (and_50_out, ra_4, and_1_out);
  and and_51 (and_51_out, rb_1, and_1_out);
  and and_52 (and_52_out, rb_2, and_1_out);
  and and_53 (and_53_out, rb_3, and_1_out);
  and and_54 (and_54_out, rb_4, and_1_out);
  Transistor transistor_12 (.in(and_37_out), .out(transistor_9_out), .gate(1'b0));
  Transistor transistor_13 (.in(is_sub_on), .out(transistor_10_out), .gate(1'b0));
  Transistor transistor_14 (.in(and_38_out), .out(transistor_9_out), .gate(1'b0));
  Transistor transistor_15 (.in(is_and_on), .out(transistor_10_out), .gate(1'b0));
  Transistor transistor_16 (.in(and_39_out), .out(transistor_9_out), .gate(1'b0));
  Transistor transistor_17 (.in(is_or_on), .out(transistor_10_out), .gate(1'b0));
  Transistor transistor_18 (.in(and_40_out), .out(transistor_9_out), .gate(1'b0));
  Transistor transistor_19 (.in(is_not_on), .out(transistor_10_out), .gate(1'b0));
  Transistor transistor_20 (.in(and_32_out), .out(transistor_9_out), .gate(1'b0));
  Transistor transistor_21 (.in(is_equal_on), .out(transistor_10_out), .gate(1'b0));
  and and_55 (and_55_out, is_gt_on, or_12_out);
  Pull_Resistor pull_resistor_4 (.node(transistor_9_out));
  Transistor transistor_22 (.in(and_36_out), .out(transistor_9_out), .gate(1'b0));
  Transistor transistor_23 (.in(and_55_out), .out(transistor_9_out), .gate(1'b0));
  Transistor transistor_24 (.in(is_gt_on), .out(transistor_10_out), .gate(1'b0));
  and and_56 (rd_o_1, transistor_9_out, rd_1);
  and and_57 (rd_o_2, transistor_9_out, rd_2);
  and and_58 (rd_o_3, transistor_9_out, rd_3);
  and and_59 (rd_o_4, transistor_9_out, rd_4);
  and and_60 (rd_c_1, transistor_10_out, and_43_out);
  and and_61 (rd_c_2, transistor_10_out, and_44_out);
  and and_62 (rd_c_3, transistor_10_out, and_45_out);
  and and_63 (rd_c_4, transistor_10_out, and_46_out);
  and and_64 (ra_o_1, and_2_out, transistor_10_out);
  and and_65 (ra_o_2, and_3_out, transistor_10_out);
  and and_66 (ra_o_3, and_4_out, transistor_10_out);
  and and_67 (ra_o_4, and_5_out, transistor_10_out);
  and and_68 (ra_c_1, and_47_out, transistor_10_out);
  and and_69 (ra_c_2, and_48_out, transistor_10_out);
  and and_70 (ra_c_3, and_49_out, transistor_10_out);
  and and_71 (ra_c_4, and_50_out, transistor_10_out);
  and and_72 (rb_o_1, and_6_out, transistor_10_out);
  and and_73 (rb_o_2, and_7_out, transistor_10_out);
  and and_74 (rb_o_3, and_8_out, transistor_10_out);
  and and_75 (rb_o_4, and_9_out, transistor_10_out);
  and and_76 (rb_c_1, and_51_out, transistor_10_out);
  and and_77 (rb_c_2, and_52_out, transistor_10_out);
  and and_78 (rb_c_3, and_53_out, transistor_10_out);
  and and_79 (rb_c_4, and_54_out, transistor_10_out);
endmodule

module cpu_ram (
  input  input_storage,
  input  CLK_A,
  input  CLK,
  input  address_bit_1,
  input  address_bit_2,
  input  address_bit_3,
  input  address_bit_4,
  input  read,
  input  write,
  output output_1,
  output output_2,
  output output_3,
  output output_4,
  output output_5,
  output output_6,
  output output_7,
  output output_8,
  output output_9,
  output output_10,
  output output_11,
  output output_12,
  output output_13,
  output output_14,
  output output_15,
  output output_16
);

  wire and_1_out, and_2_out, and_3_out, and_4_out, and_5_out, and_6_out, and_7_out, and_8_out, and_9_out,
       and_10_out, and_11_out, and_12_out, and_13_out, and_14_out, and_15_out, and_16_out, and_17_out,
       and_18_out, and_19_out, and_20_out, and_21_out, and_22_out, and_23_out, and_24_out, and_25_out,
       and_26_out, and_27_out, and_28_out, and_29_out, and_30_out, and_31_out, and_32_out, and_33_out,
       and_34_out, and_35_out, and_36_out, and_37_out, and_38_out, and_39_out, and_40_out, and_41_out,
       and_42_out, and_43_out, and_44_out, and_45_out, and_46_out, and_47_out, and_48_out, and_49_out,
       and_50_out, and_51_out, d_ff_1_q, d_ff_2_q, d_ff_3_q, d_ff_4_q, d_ff_5_q, d_ff_6_q, d_ff_7_q,
       d_ff_8_q, d_ff_9_q, d_ff_10_q, d_ff_11_q, d_ff_12_q, d_ff_13_q, d_ff_14_q, d_ff_15_q, d_ff_16_q,
       d_ff_17_q, d_ff_18_q, d_ff_19_q, d_ff_20_q, d_ff_21_q, d_ff_22_q, d_ff_23_q, d_ff_24_q, d_ff_25_q,
       d_ff_26_q, d_ff_27_q, d_ff_28_q, d_ff_29_q, d_ff_30_q, d_ff_31_q, d_ff_32_q, d_ff_33_q, d_ff_34_q,
       d_ff_35_q, d_ff_36_q, d_ff_37_q, d_ff_38_q, d_ff_39_q, d_ff_40_q, d_ff_41_q, d_ff_42_q, d_ff_43_q,
       d_ff_44_q, d_ff_45_q, d_ff_46_q, d_ff_47_q, d_ff_48_q, d_ff_49_q, d_ff_50_q, d_ff_51_q, d_ff_52_q,
       d_ff_53_q, d_ff_54_q, d_ff_55_q, d_ff_56_q, d_ff_57_q, d_ff_58_q, d_ff_59_q, d_ff_60_q, d_ff_61_q,
       d_ff_62_q, d_ff_63_q, d_ff_64_q, d_ff_65_q, d_ff_66_q, d_ff_67_q, d_ff_68_q, d_ff_69_q, d_ff_70_q,
       d_ff_71_q, d_ff_72_q, d_ff_73_q, d_ff_74_q, d_ff_75_q, d_ff_76_q, d_ff_77_q, d_ff_78_q, d_ff_79_q,
       d_ff_80_q, d_ff_81_q, d_ff_82_q, d_ff_83_q, d_ff_84_q, d_ff_85_q, d_ff_86_q, d_ff_87_q, d_ff_88_q,
       d_ff_89_q, d_ff_90_q, d_ff_91_q, d_ff_92_q, d_ff_93_q, d_ff_94_q, d_ff_95_q, d_ff_96_q, d_ff_97_q,
       d_ff_98_q, d_ff_99_q, d_ff_100_q, d_ff_101_q, d_ff_102_q, d_ff_103_q, d_ff_104_q, d_ff_105_q,
       d_ff_106_q, d_ff_107_q, d_ff_108_q, d_ff_109_q, d_ff_110_q, d_ff_111_q, d_ff_112_q, d_ff_113_q,
       d_ff_114_q, d_ff_115_q, d_ff_116_q, d_ff_117_q, d_ff_118_q, d_ff_119_q, d_ff_120_q, d_ff_121_q,
       d_ff_122_q, d_ff_123_q, d_ff_124_q, d_ff_125_q, d_ff_126_q, d_ff_127_q, d_ff_128_q, d_ff_129_q,
       d_ff_130_q, d_ff_131_q, d_ff_132_q, d_ff_133_q, d_ff_134_q, d_ff_135_q, d_ff_136_q, d_ff_137_q,
       d_ff_138_q, d_ff_139_q, d_ff_140_q, d_ff_141_q, d_ff_142_q, d_ff_143_q, d_ff_144_q, decoder_1_out0,
       decoder_1_out1, decoder_1_out2, decoder_1_out3, decoder_1_out4, decoder_1_out5, decoder_1_out6,
       decoder_1_out7, decoder_1_out8, decoder_1_out9, decoder_1_out10, decoder_1_out11, decoder_1_out12,
       decoder_1_out13, decoder_1_out14, decoder_1_out15, or_1_out;

  and and_1 (and_1_out, CLK_A, CLK);
  or or_1 (or_1_out, read, write);
  Decoder #(.select(4)) decoder_1 (
    .out0(decoder_1_out0), .out1(decoder_1_out1), .out2(decoder_1_out2), .out3(decoder_1_out3),
    .out4(decoder_1_out4), .out5(decoder_1_out5), .out6(decoder_1_out6), .out7(decoder_1_out7),
    .out8(decoder_1_out8), .out9(decoder_1_out9), .out10(decoder_1_out10), .out11(decoder_1_out11),
    .out12(decoder_1_out12), .out13(decoder_1_out13), .out14(decoder_1_out14), .out15(decoder_1_out15),
    .sel({address_bit_4, address_bit_3, address_bit_2, address_bit_1}), .en(or_1_out));
  and and_2 (and_2_out, or_1_out, and_1_out);
  and and_3 (and_3_out, input_storage, write);
  and and_4 (and_4_out, decoder_1_out0, and_3_out);
  and and_5 (and_5_out, decoder_1_out0, and_2_out);
  and and_6 (and_6_out, decoder_1_out1, and_3_out);
  and and_7 (and_7_out, decoder_1_out1, and_2_out);
  and and_8 (and_8_out, decoder_1_out2, and_3_out);
  and and_9 (and_9_out, decoder_1_out2, and_2_out);
  and and_10 (and_10_out, decoder_1_out3, and_3_out);
  and and_11 (and_11_out, decoder_1_out3, and_2_out);
  and and_12 (and_12_out, decoder_1_out4, and_3_out);
  and and_13 (and_13_out, decoder_1_out4, and_2_out);
  and and_14 (and_14_out, decoder_1_out5, and_3_out);
  and and_15 (and_15_out, decoder_1_out5, and_2_out);
  and and_16 (and_16_out, decoder_1_out6, and_3_out);
  and and_17 (and_17_out, decoder_1_out6, and_2_out);
  and and_18 (and_18_out, decoder_1_out7, and_3_out);
  and and_19 (and_19_out, decoder_1_out7, and_2_out);
  and and_20 (and_20_out, decoder_1_out8, and_3_out);
  and and_21 (and_21_out, decoder_1_out8, and_2_out);
  and and_22 (and_22_out, decoder_1_out9, and_3_out);
  and and_23 (and_23_out, decoder_1_out9, and_2_out);
  and and_24 (and_24_out, decoder_1_out10, and_3_out);
  and and_25 (and_25_out, decoder_1_out10, and_2_out);
  and and_26 (and_26_out, decoder_1_out11, and_3_out);
  and and_27 (and_27_out, decoder_1_out11, and_2_out);
  and and_28 (and_28_out, decoder_1_out12, and_3_out);
  and and_29 (and_29_out, decoder_1_out12, and_2_out);
  and and_30 (and_30_out, decoder_1_out13, and_3_out);
  and and_31 (and_31_out, decoder_1_out13, and_2_out);
  and and_32 (and_32_out, decoder_1_out14, and_3_out);
  and and_33 (and_33_out, decoder_1_out14, and_2_out);
  and and_34 (and_34_out, decoder_1_out15, and_3_out);
  and and_35 (and_35_out, decoder_1_out15, and_2_out);
  and and_36 (and_36_out, decoder_1_out0, read);
  and and_37 (and_37_out, decoder_1_out1, read);
  and and_38 (and_38_out, decoder_1_out2, read);
  and and_39 (and_39_out, decoder_1_out3, read);
  and and_40 (and_40_out, decoder_1_out4, read);
  and and_41 (and_41_out, decoder_1_out5, read);
  and and_42 (and_42_out, decoder_1_out6, read);
  and and_43 (and_43_out, decoder_1_out7, read);
  and and_44 (and_44_out, decoder_1_out8, read);
  and and_45 (and_45_out, decoder_1_out9, read);
  and and_46 (and_46_out, decoder_1_out10, read);
  and and_47 (and_47_out, decoder_1_out11, read);
  and and_48 (and_48_out, decoder_1_out12, read);
  and and_49 (and_49_out, decoder_1_out13, read);
  and and_50 (and_50_out, decoder_1_out14, read);
  and and_51 (and_51_out, decoder_1_out15, read);
  D_Flip_Flop d_ff_1 (.D(and_4_out), .clk(and_5_out), .Q(d_ff_1_q));  // open: Qn, preset, reset
  D_Flip_Flop d_ff_2 (.D(and_6_out), .clk(and_7_out), .Q(d_ff_2_q));  // open: Qn, preset, reset
  D_Flip_Flop d_ff_3 (.D(and_8_out), .clk(and_9_out), .Q(d_ff_3_q));  // open: Qn, preset, reset
  D_Flip_Flop d_ff_4 (.D(and_10_out), .clk(and_11_out), .Q(d_ff_4_q));  // open: Qn, preset, reset
  D_Flip_Flop d_ff_5 (.D(and_12_out), .clk(and_13_out), .Q(d_ff_5_q));  // open: Qn, preset, reset
  D_Flip_Flop d_ff_6 (.D(and_14_out), .clk(and_15_out), .Q(d_ff_6_q));  // open: Qn, preset, reset
  D_Flip_Flop d_ff_7 (.D(and_16_out), .clk(and_17_out), .Q(d_ff_7_q));  // open: Qn, preset, reset
  D_Flip_Flop d_ff_8 (.D(and_18_out), .clk(and_19_out), .Q(d_ff_8_q));  // open: Qn, preset, reset
  D_Flip_Flop d_ff_9 (.D(and_20_out), .clk(and_21_out), .Q(d_ff_9_q));  // open: Qn, preset, reset
  D_Flip_Flop d_ff_10 (.D(and_22_out), .clk(and_23_out), .Q(d_ff_10_q));  // open: Qn, preset, reset
  D_Flip_Flop d_ff_11 (.D(and_24_out), .clk(and_25_out), .Q(d_ff_11_q));  // open: Qn, preset, reset
  D_Flip_Flop d_ff_12 (.D(and_26_out), .clk(and_27_out), .Q(d_ff_12_q));  // open: Qn, preset, reset
  D_Flip_Flop d_ff_13 (.D(and_28_out), .clk(and_29_out), .Q(d_ff_13_q));  // open: Qn, preset, reset
  D_Flip_Flop d_ff_14 (.D(and_30_out), .clk(and_31_out), .Q(d_ff_14_q));  // open: Qn, preset, reset
  D_Flip_Flop d_ff_15 (.D(and_32_out), .clk(and_33_out), .Q(d_ff_15_q));  // open: Qn, preset, reset
  D_Flip_Flop d_ff_16 (.D(and_34_out), .clk(and_35_out), .Q(d_ff_16_q));  // open: Qn, preset, reset
  D_Flip_Flop d_ff_17 (.D(d_ff_1_q), .clk(and_5_out), .Q(d_ff_17_q));  // open: Qn, preset, reset
  D_Flip_Flop d_ff_18 (.D(d_ff_2_q), .clk(and_7_out), .Q(d_ff_18_q));  // open: Qn, preset, reset
  D_Flip_Flop d_ff_19 (.D(d_ff_3_q), .clk(and_9_out), .Q(d_ff_19_q));  // open: Qn, preset, reset
  D_Flip_Flop d_ff_20 (.D(d_ff_4_q), .clk(and_11_out), .Q(d_ff_20_q));  // open: Qn, preset, reset
  D_Flip_Flop d_ff_21 (.D(d_ff_5_q), .clk(and_13_out), .Q(d_ff_21_q));  // open: Qn, preset, reset
  D_Flip_Flop d_ff_22 (.D(d_ff_6_q), .clk(and_15_out), .Q(d_ff_22_q));  // open: Qn, preset, reset
  D_Flip_Flop d_ff_23 (.D(d_ff_7_q), .clk(and_17_out), .Q(d_ff_23_q));  // open: Qn, preset, reset
  D_Flip_Flop d_ff_24 (.D(d_ff_8_q), .clk(and_19_out), .Q(d_ff_24_q));  // open: Qn, preset, reset
  D_Flip_Flop d_ff_25 (.D(d_ff_9_q), .clk(and_21_out), .Q(d_ff_25_q));  // open: Qn, preset, reset
  D_Flip_Flop d_ff_26 (.D(d_ff_10_q), .clk(and_23_out), .Q(d_ff_26_q));  // open: Qn, preset, reset
  D_Flip_Flop d_ff_27 (.D(d_ff_11_q), .clk(and_25_out), .Q(d_ff_27_q));  // open: Qn, preset, reset
  D_Flip_Flop d_ff_28 (.D(d_ff_12_q), .clk(and_27_out), .Q(d_ff_28_q));  // open: Qn, preset, reset
  D_Flip_Flop d_ff_29 (.D(d_ff_13_q), .clk(and_29_out), .Q(d_ff_29_q));  // open: Qn, preset, reset
  D_Flip_Flop d_ff_30 (.D(d_ff_14_q), .clk(and_31_out), .Q(d_ff_30_q));  // open: Qn, preset, reset
  D_Flip_Flop d_ff_31 (.D(d_ff_15_q), .clk(and_33_out), .Q(d_ff_31_q));  // open: Qn, preset, reset
  D_Flip_Flop d_ff_32 (.D(d_ff_16_q), .clk(and_35_out), .Q(d_ff_32_q));  // open: Qn, preset, reset
  D_Flip_Flop d_ff_33 (.D(d_ff_17_q), .clk(and_5_out), .Q(d_ff_33_q));  // open: Qn, preset, reset
  D_Flip_Flop d_ff_34 (.D(d_ff_18_q), .clk(and_7_out), .Q(d_ff_34_q));  // open: Qn, preset, reset
  D_Flip_Flop d_ff_35 (.D(d_ff_19_q), .clk(and_9_out), .Q(d_ff_35_q));  // open: Qn, preset, reset
  D_Flip_Flop d_ff_36 (.D(d_ff_20_q), .clk(and_11_out), .Q(d_ff_36_q));  // open: Qn, preset, reset
  D_Flip_Flop d_ff_37 (.D(d_ff_21_q), .clk(and_13_out), .Q(d_ff_37_q));  // open: Qn, preset, reset
  D_Flip_Flop d_ff_38 (.D(d_ff_22_q), .clk(and_15_out), .Q(d_ff_38_q));  // open: Qn, preset, reset
  D_Flip_Flop d_ff_39 (.D(d_ff_23_q), .clk(and_17_out), .Q(d_ff_39_q));  // open: Qn, preset, reset
  D_Flip_Flop d_ff_40 (.D(d_ff_24_q), .clk(and_19_out), .Q(d_ff_40_q));  // open: Qn, preset, reset
  D_Flip_Flop d_ff_41 (.D(d_ff_25_q), .clk(and_21_out), .Q(d_ff_41_q));  // open: Qn, preset, reset
  D_Flip_Flop d_ff_42 (.D(d_ff_26_q), .clk(and_23_out), .Q(d_ff_42_q));  // open: Qn, preset, reset
  D_Flip_Flop d_ff_43 (.D(d_ff_27_q), .clk(and_25_out), .Q(d_ff_43_q));  // open: Qn, preset, reset
  D_Flip_Flop d_ff_44 (.D(d_ff_28_q), .clk(and_27_out), .Q(d_ff_44_q));  // open: Qn, preset, reset
  D_Flip_Flop d_ff_45 (.D(d_ff_29_q), .clk(and_29_out), .Q(d_ff_45_q));  // open: Qn, preset, reset
  D_Flip_Flop d_ff_46 (.D(d_ff_30_q), .clk(and_31_out), .Q(d_ff_46_q));  // open: Qn, preset, reset
  D_Flip_Flop d_ff_47 (.D(d_ff_31_q), .clk(and_33_out), .Q(d_ff_47_q));  // open: Qn, preset, reset
  D_Flip_Flop d_ff_48 (.D(d_ff_32_q), .clk(and_35_out), .Q(d_ff_48_q));  // open: Qn, preset, reset
  D_Flip_Flop d_ff_49 (.D(d_ff_33_q), .clk(and_5_out), .Q(d_ff_49_q));  // open: Qn, preset, reset
  D_Flip_Flop d_ff_50 (.D(d_ff_34_q), .clk(and_7_out), .Q(d_ff_50_q));  // open: Qn, preset, reset
  D_Flip_Flop d_ff_51 (.D(d_ff_35_q), .clk(and_9_out), .Q(d_ff_51_q));  // open: Qn, preset, reset
  D_Flip_Flop d_ff_52 (.D(d_ff_36_q), .clk(and_11_out), .Q(d_ff_52_q));  // open: Qn, preset, reset
  D_Flip_Flop d_ff_53 (.D(d_ff_37_q), .clk(and_13_out), .Q(d_ff_53_q));  // open: Qn, preset, reset
  D_Flip_Flop d_ff_54 (.D(d_ff_38_q), .clk(and_15_out), .Q(d_ff_54_q));  // open: Qn, preset, reset
  D_Flip_Flop d_ff_55 (.D(d_ff_39_q), .clk(and_17_out), .Q(d_ff_55_q));  // open: Qn, preset, reset
  D_Flip_Flop d_ff_56 (.D(d_ff_40_q), .clk(and_19_out), .Q(d_ff_56_q));  // open: Qn, preset, reset
  D_Flip_Flop d_ff_57 (.D(d_ff_41_q), .clk(and_21_out), .Q(d_ff_57_q));  // open: Qn, preset, reset
  D_Flip_Flop d_ff_58 (.D(d_ff_42_q), .clk(and_23_out), .Q(d_ff_58_q));  // open: Qn, preset, reset
  D_Flip_Flop d_ff_59 (.D(d_ff_43_q), .clk(and_25_out), .Q(d_ff_59_q));  // open: Qn, preset, reset
  D_Flip_Flop d_ff_60 (.D(d_ff_44_q), .clk(and_27_out), .Q(d_ff_60_q));  // open: Qn, preset, reset
  D_Flip_Flop d_ff_61 (.D(d_ff_45_q), .clk(and_29_out), .Q(d_ff_61_q));  // open: Qn, preset, reset
  D_Flip_Flop d_ff_62 (.D(d_ff_46_q), .clk(and_31_out), .Q(d_ff_62_q));  // open: Qn, preset, reset
  D_Flip_Flop d_ff_63 (.D(d_ff_47_q), .clk(and_33_out), .Q(d_ff_63_q));  // open: Qn, preset, reset
  D_Flip_Flop d_ff_64 (.D(d_ff_48_q), .clk(and_35_out), .Q(d_ff_64_q));  // open: Qn, preset, reset
  D_Flip_Flop d_ff_65 (.D(d_ff_49_q), .clk(and_5_out), .Q(d_ff_65_q));  // open: Qn, preset, reset
  D_Flip_Flop d_ff_66 (.D(d_ff_50_q), .clk(and_7_out), .Q(d_ff_66_q));  // open: Qn, preset, reset
  D_Flip_Flop d_ff_67 (.D(d_ff_51_q), .clk(and_9_out), .Q(d_ff_67_q));  // open: Qn, preset, reset
  D_Flip_Flop d_ff_68 (.D(d_ff_52_q), .clk(and_11_out), .Q(d_ff_68_q));  // open: Qn, preset, reset
  D_Flip_Flop d_ff_69 (.D(d_ff_53_q), .clk(and_13_out), .Q(d_ff_69_q));  // open: Qn, preset, reset
  D_Flip_Flop d_ff_70 (.D(d_ff_54_q), .clk(and_15_out), .Q(d_ff_70_q));  // open: Qn, preset, reset
  D_Flip_Flop d_ff_71 (.D(d_ff_55_q), .clk(and_17_out), .Q(d_ff_71_q));  // open: Qn, preset, reset
  D_Flip_Flop d_ff_72 (.D(d_ff_56_q), .clk(and_19_out), .Q(d_ff_72_q));  // open: Qn, preset, reset
  D_Flip_Flop d_ff_73 (.D(d_ff_57_q), .clk(and_21_out), .Q(d_ff_73_q));  // open: Qn, preset, reset
  D_Flip_Flop d_ff_74 (.D(d_ff_58_q), .clk(and_23_out), .Q(d_ff_74_q));  // open: Qn, preset, reset
  D_Flip_Flop d_ff_75 (.D(d_ff_59_q), .clk(and_25_out), .Q(d_ff_75_q));  // open: Qn, preset, reset
  D_Flip_Flop d_ff_76 (.D(d_ff_60_q), .clk(and_27_out), .Q(d_ff_76_q));  // open: Qn, preset, reset
  D_Flip_Flop d_ff_77 (.D(d_ff_61_q), .clk(and_29_out), .Q(d_ff_77_q));  // open: Qn, preset, reset
  D_Flip_Flop d_ff_78 (.D(d_ff_62_q), .clk(and_31_out), .Q(d_ff_78_q));  // open: Qn, preset, reset
  D_Flip_Flop d_ff_79 (.D(d_ff_63_q), .clk(and_33_out), .Q(d_ff_79_q));  // open: Qn, preset, reset
  D_Flip_Flop d_ff_80 (.D(d_ff_64_q), .clk(and_35_out), .Q(d_ff_80_q));  // open: Qn, preset, reset
  D_Flip_Flop d_ff_81 (.D(d_ff_65_q), .clk(and_5_out), .Q(d_ff_81_q));  // open: Qn, preset, reset
  D_Flip_Flop d_ff_82 (.D(d_ff_66_q), .clk(and_7_out), .Q(d_ff_82_q));  // open: Qn, preset, reset
  D_Flip_Flop d_ff_83 (.D(d_ff_67_q), .clk(and_9_out), .Q(d_ff_83_q));  // open: Qn, preset, reset
  D_Flip_Flop d_ff_84 (.D(d_ff_68_q), .clk(and_11_out), .Q(d_ff_84_q));  // open: Qn, preset, reset
  D_Flip_Flop d_ff_85 (.D(d_ff_69_q), .clk(and_13_out), .Q(d_ff_85_q));  // open: Qn, preset, reset
  D_Flip_Flop d_ff_86 (.D(d_ff_70_q), .clk(and_15_out), .Q(d_ff_86_q));  // open: Qn, preset, reset
  D_Flip_Flop d_ff_87 (.D(d_ff_71_q), .clk(and_17_out), .Q(d_ff_87_q));  // open: Qn, preset, reset
  D_Flip_Flop d_ff_88 (.D(d_ff_72_q), .clk(and_19_out), .Q(d_ff_88_q));  // open: Qn, preset, reset
  D_Flip_Flop d_ff_89 (.D(d_ff_73_q), .clk(and_21_out), .Q(d_ff_89_q));  // open: Qn, preset, reset
  D_Flip_Flop d_ff_90 (.D(d_ff_74_q), .clk(and_23_out), .Q(d_ff_90_q));  // open: Qn, preset, reset
  D_Flip_Flop d_ff_91 (.D(d_ff_75_q), .clk(and_25_out), .Q(d_ff_91_q));  // open: Qn, preset, reset
  D_Flip_Flop d_ff_92 (.D(d_ff_76_q), .clk(and_27_out), .Q(d_ff_92_q));  // open: Qn, preset, reset
  D_Flip_Flop d_ff_93 (.D(d_ff_77_q), .clk(and_29_out), .Q(d_ff_93_q));  // open: Qn, preset, reset
  D_Flip_Flop d_ff_94 (.D(d_ff_78_q), .clk(and_31_out), .Q(d_ff_94_q));  // open: Qn, preset, reset
  D_Flip_Flop d_ff_95 (.D(d_ff_79_q), .clk(and_33_out), .Q(d_ff_95_q));  // open: Qn, preset, reset
  D_Flip_Flop d_ff_96 (.D(d_ff_80_q), .clk(and_35_out), .Q(d_ff_96_q));  // open: Qn, preset, reset
  D_Flip_Flop d_ff_97 (.D(d_ff_81_q), .clk(and_5_out), .Q(d_ff_97_q));  // open: Qn, preset, reset
  D_Flip_Flop d_ff_98 (.D(d_ff_82_q), .clk(and_7_out), .Q(d_ff_98_q));  // open: Qn, preset, reset
  D_Flip_Flop d_ff_99 (.D(d_ff_83_q), .clk(and_9_out), .Q(d_ff_99_q));  // open: Qn, preset, reset
  D_Flip_Flop d_ff_100 (.D(d_ff_84_q), .clk(and_11_out), .Q(d_ff_100_q));  // open: Qn, preset, reset
  D_Flip_Flop d_ff_101 (.D(d_ff_85_q), .clk(and_13_out), .Q(d_ff_101_q));  // open: Qn, preset, reset
  D_Flip_Flop d_ff_102 (.D(d_ff_86_q), .clk(and_15_out), .Q(d_ff_102_q));  // open: Qn, preset, reset
  D_Flip_Flop d_ff_103 (.D(d_ff_87_q), .clk(and_17_out), .Q(d_ff_103_q));  // open: Qn, preset, reset
  D_Flip_Flop d_ff_104 (.D(d_ff_88_q), .clk(and_19_out), .Q(d_ff_104_q));  // open: Qn, preset, reset
  D_Flip_Flop d_ff_105 (.D(d_ff_89_q), .clk(and_21_out), .Q(d_ff_105_q));  // open: Qn, preset, reset
  D_Flip_Flop d_ff_106 (.D(d_ff_90_q), .clk(and_23_out), .Q(d_ff_106_q));  // open: Qn, preset, reset
  D_Flip_Flop d_ff_107 (.D(d_ff_91_q), .clk(and_25_out), .Q(d_ff_107_q));  // open: Qn, preset, reset
  D_Flip_Flop d_ff_108 (.D(d_ff_92_q), .clk(and_27_out), .Q(d_ff_108_q));  // open: Qn, preset, reset
  D_Flip_Flop d_ff_109 (.D(d_ff_93_q), .clk(and_29_out), .Q(d_ff_109_q));  // open: Qn, preset, reset
  D_Flip_Flop d_ff_110 (.D(d_ff_94_q), .clk(and_31_out), .Q(d_ff_110_q));  // open: Qn, preset, reset
  D_Flip_Flop d_ff_111 (.D(d_ff_95_q), .clk(and_33_out), .Q(d_ff_111_q));  // open: Qn, preset, reset
  D_Flip_Flop d_ff_112 (.D(d_ff_96_q), .clk(and_35_out), .Q(d_ff_112_q));  // open: Qn, preset, reset
  D_Flip_Flop d_ff_113 (.D(d_ff_97_q), .clk(and_5_out), .Q(d_ff_113_q));  // open: Qn, preset, reset
  D_Flip_Flop d_ff_114 (.D(d_ff_98_q), .clk(and_7_out), .Q(d_ff_114_q));  // open: Qn, preset, reset
  D_Flip_Flop d_ff_115 (.D(d_ff_99_q), .clk(and_9_out), .Q(d_ff_115_q));  // open: Qn, preset, reset
  D_Flip_Flop d_ff_116 (.D(d_ff_100_q), .clk(and_11_out), .Q(d_ff_116_q));  // open: Qn, preset, reset
  D_Flip_Flop d_ff_117 (.D(d_ff_101_q), .clk(and_13_out), .Q(d_ff_117_q));  // open: Qn, preset, reset
  D_Flip_Flop d_ff_118 (.D(d_ff_102_q), .clk(and_15_out), .Q(d_ff_118_q));  // open: Qn, preset, reset
  D_Flip_Flop d_ff_119 (.D(d_ff_103_q), .clk(and_17_out), .Q(d_ff_119_q));  // open: Qn, preset, reset
  D_Flip_Flop d_ff_120 (.D(d_ff_104_q), .clk(and_19_out), .Q(d_ff_120_q));  // open: Qn, preset, reset
  D_Flip_Flop d_ff_121 (.D(d_ff_105_q), .clk(and_21_out), .Q(d_ff_121_q));  // open: Qn, preset, reset
  D_Flip_Flop d_ff_122 (.D(d_ff_106_q), .clk(and_23_out), .Q(d_ff_122_q));  // open: Qn, preset, reset
  D_Flip_Flop d_ff_123 (.D(d_ff_107_q), .clk(and_25_out), .Q(d_ff_123_q));  // open: Qn, preset, reset
  D_Flip_Flop d_ff_124 (.D(d_ff_108_q), .clk(and_27_out), .Q(d_ff_124_q));  // open: Qn, preset, reset
  D_Flip_Flop d_ff_125 (.D(d_ff_109_q), .clk(and_29_out), .Q(d_ff_125_q));  // open: Qn, preset, reset
  D_Flip_Flop d_ff_126 (.D(d_ff_110_q), .clk(and_31_out), .Q(d_ff_126_q));  // open: Qn, preset, reset
  D_Flip_Flop d_ff_127 (.D(d_ff_111_q), .clk(and_33_out), .Q(d_ff_127_q));  // open: Qn, preset, reset
  D_Flip_Flop d_ff_128 (.D(d_ff_112_q), .clk(and_35_out), .Q(d_ff_128_q));  // open: Qn, preset, reset
  D_Flip_Flop d_ff_129 (.D(d_ff_113_q), .clk(and_5_out), .Q(d_ff_129_q));  // open: Qn, preset, reset
  D_Flip_Flop d_ff_130 (.D(d_ff_114_q), .clk(and_7_out), .Q(d_ff_130_q));  // open: Qn, preset, reset
  D_Flip_Flop d_ff_131 (.D(d_ff_115_q), .clk(and_9_out), .Q(d_ff_131_q));  // open: Qn, preset, reset
  D_Flip_Flop d_ff_132 (.D(d_ff_116_q), .clk(and_11_out), .Q(d_ff_132_q));  // open: Qn, preset, reset
  D_Flip_Flop d_ff_133 (.D(d_ff_117_q), .clk(and_13_out), .Q(d_ff_133_q));  // open: Qn, preset, reset
  D_Flip_Flop d_ff_134 (.D(d_ff_118_q), .clk(and_15_out), .Q(d_ff_134_q));  // open: Qn, preset, reset
  D_Flip_Flop d_ff_135 (.D(d_ff_119_q), .clk(and_17_out), .Q(d_ff_135_q));  // open: Qn, preset, reset
  D_Flip_Flop d_ff_136 (.D(d_ff_120_q), .clk(and_19_out), .Q(d_ff_136_q));  // open: Qn, preset, reset
  D_Flip_Flop d_ff_137 (.D(d_ff_121_q), .clk(and_21_out), .Q(d_ff_137_q));  // open: Qn, preset, reset
  D_Flip_Flop d_ff_138 (.D(d_ff_122_q), .clk(and_23_out), .Q(d_ff_138_q));  // open: Qn, preset, reset
  D_Flip_Flop d_ff_139 (.D(d_ff_123_q), .clk(and_25_out), .Q(d_ff_139_q));  // open: Qn, preset, reset
  D_Flip_Flop d_ff_140 (.D(d_ff_124_q), .clk(and_27_out), .Q(d_ff_140_q));  // open: Qn, preset, reset
  D_Flip_Flop d_ff_141 (.D(d_ff_125_q), .clk(and_29_out), .Q(d_ff_141_q));  // open: Qn, preset, reset
  D_Flip_Flop d_ff_142 (.D(d_ff_126_q), .clk(and_31_out), .Q(d_ff_142_q));  // open: Qn, preset, reset
  D_Flip_Flop d_ff_143 (.D(d_ff_127_q), .clk(and_33_out), .Q(d_ff_143_q));  // open: Qn, preset, reset
  D_Flip_Flop d_ff_144 (.D(d_ff_128_q), .clk(and_35_out), .Q(d_ff_144_q));  // open: Qn, preset, reset
  and and_52 (output_1, d_ff_129_q, and_36_out);
  and and_53 (output_2, d_ff_130_q, and_37_out);
  and and_54 (output_3, d_ff_131_q, and_38_out);
  and and_55 (output_4, d_ff_132_q, and_39_out);
  and and_56 (output_5, d_ff_133_q, and_40_out);
  and and_57 (output_6, d_ff_134_q, and_41_out);
  and and_58 (output_7, d_ff_135_q, and_42_out);
  and and_59 (output_8, d_ff_136_q, and_43_out);
  and and_60 (output_9, d_ff_137_q, and_44_out);
  and and_61 (output_10, d_ff_138_q, and_45_out);
  and and_62 (output_11, d_ff_139_q, and_46_out);
  and and_63 (output_12, d_ff_140_q, and_47_out);
  and and_64 (output_13, d_ff_141_q, and_48_out);
  and and_65 (output_14, d_ff_142_q, and_49_out);
  and and_66 (output_15, d_ff_143_q, and_50_out);
  and and_67 (output_16, d_ff_144_q, and_51_out);
endmodule

module memory_address_manager (
  input  CLK,
  input  CLK_A,
  input  is_get_on,
  input  is_set_on,
  input  rd_1,
  input  rd_2,
  input  ram_add_1,
  input  ram_add_2,
  input  ram_add_3,
  input  ram_add_4,
  input  rd_i_1,
  input  rd_i_2,
  input  rd_i_3,
  input  rd_i_4,
  output rd_o_1,
  output rd_o_2,
  output rd_o_3,
  output rd_o_4,
  output rd_c_1,
  output rd_c_2,
  output rd_c_3,
  output rd_c_4
);

  wire and_1_out, and_2_out, and_3_out, and_4_out, and_5_out, and_6_out, and_7_out, and_8_out,
       cpu_ram_1_output_1, cpu_ram_1_output_2, cpu_ram_1_output_3, cpu_ram_1_output_4, cpu_ram_1_output_5,
       cpu_ram_1_output_6, cpu_ram_1_output_7, cpu_ram_1_output_8, cpu_ram_1_output_9, cpu_ram_1_output_10,
       cpu_ram_1_output_11, cpu_ram_1_output_12, cpu_ram_1_output_13, cpu_ram_1_output_14,
       cpu_ram_1_output_15, cpu_ram_1_output_16, decoder_1_out0, decoder_1_out1, decoder_1_out2,
       decoder_1_out3, or_1_out, pull_resistor_2_node, transistor_1_out;

  Decoder #(.select(2)) decoder_1 (
    .out0(decoder_1_out0), .out1(decoder_1_out1), .out2(decoder_1_out2), .out3(decoder_1_out3),
    .sel({rd_2, rd_1}), .en(or_1_out));
  and and_1 (and_1_out, CLK, CLK_A);
  or or_1 (or_1_out, is_set_on, is_get_on);
  and and_2 (and_2_out, rd_i_1, decoder_1_out0);
  and and_3 (and_3_out, rd_i_2, decoder_1_out1);
  and and_4 (and_4_out, rd_i_3, decoder_1_out2);
  and and_5 (and_5_out, rd_i_4, decoder_1_out3);
  and and_6 (and_6_out, and_1_out, or_1_out);
  Transistor transistor_1 (.in(and_2_out), .out(transistor_1_out), .gate(1'b0));
  Transistor transistor_2 (.in(and_3_out), .out(transistor_1_out), .gate(1'b0));
  Transistor transistor_3 (.in(and_4_out), .out(transistor_1_out), .gate(1'b0));
  Transistor transistor_4 (.in(and_5_out), .out(transistor_1_out), .gate(1'b0));
  Pull_Resistor pull_resistor_1 (.node(transistor_1_out));
  and and_7 (and_7_out, is_set_on, transistor_1_out);
  cpu_ram cpu_ram_1 (
    .input_storage(and_7_out), .CLK_A(CLK_A), .CLK(CLK), .address_bit_1(ram_add_1),
    .address_bit_2(ram_add_2), .address_bit_3(ram_add_3), .address_bit_4(ram_add_4), .read(is_get_on),
    .write(is_set_on), .output_1(cpu_ram_1_output_1), .output_2(cpu_ram_1_output_2),
    .output_3(cpu_ram_1_output_3), .output_4(cpu_ram_1_output_4), .output_5(cpu_ram_1_output_5),
    .output_6(cpu_ram_1_output_6), .output_7(cpu_ram_1_output_7), .output_8(cpu_ram_1_output_8),
    .output_9(cpu_ram_1_output_9), .output_10(cpu_ram_1_output_10), .output_11(cpu_ram_1_output_11),
    .output_12(cpu_ram_1_output_12), .output_13(cpu_ram_1_output_13), .output_14(cpu_ram_1_output_14),
    .output_15(cpu_ram_1_output_15), .output_16(cpu_ram_1_output_16));
  Pull_Resistor pull_resistor_2 (.node(pull_resistor_2_node));
  Transistor transistor_5 (.in(cpu_ram_1_output_1), .out(pull_resistor_2_node), .gate(1'b0));
  Transistor transistor_6 (.in(cpu_ram_1_output_2), .out(pull_resistor_2_node), .gate(1'b0));
  Transistor transistor_7 (.in(cpu_ram_1_output_3), .out(pull_resistor_2_node), .gate(1'b0));
  Transistor transistor_8 (.in(cpu_ram_1_output_4), .out(pull_resistor_2_node), .gate(1'b0));
  Transistor transistor_9 (.in(cpu_ram_1_output_5), .out(pull_resistor_2_node), .gate(1'b0));
  Transistor transistor_10 (.in(cpu_ram_1_output_6), .out(pull_resistor_2_node), .gate(1'b0));
  Transistor transistor_11 (.in(cpu_ram_1_output_7), .out(pull_resistor_2_node), .gate(1'b0));
  Transistor transistor_12 (.in(cpu_ram_1_output_8), .out(pull_resistor_2_node), .gate(1'b0));
  Transistor transistor_13 (.in(cpu_ram_1_output_9), .out(pull_resistor_2_node), .gate(1'b0));
  Transistor transistor_14 (.in(cpu_ram_1_output_10), .out(pull_resistor_2_node), .gate(1'b0));
  Transistor transistor_15 (.in(cpu_ram_1_output_11), .out(pull_resistor_2_node), .gate(1'b0));
  Transistor transistor_16 (.in(cpu_ram_1_output_12), .out(pull_resistor_2_node), .gate(1'b0));
  Transistor transistor_17 (.in(cpu_ram_1_output_13), .out(pull_resistor_2_node), .gate(1'b0));
  Transistor transistor_18 (.in(cpu_ram_1_output_14), .out(pull_resistor_2_node), .gate(1'b0));
  Transistor transistor_19 (.in(cpu_ram_1_output_15), .out(pull_resistor_2_node), .gate(1'b0));
  Transistor transistor_20 (.in(cpu_ram_1_output_16), .out(pull_resistor_2_node), .gate(1'b0));
  Transistor transistor_21 (.in(and_7_out), .out(pull_resistor_2_node), .gate(1'b0));
  and and_8 (and_8_out, or_1_out, pull_resistor_2_node);
  and and_9 (rd_c_1, and_6_out, decoder_1_out0);
  and and_10 (rd_c_2, and_6_out, decoder_1_out1);
  and and_11 (rd_c_3, and_6_out, decoder_1_out2);
  and and_12 (rd_c_4, and_6_out, decoder_1_out3);
  and and_13 (rd_o_1, and_8_out, decoder_1_out0);
  and and_14 (rd_o_2, and_8_out, decoder_1_out1);
  and and_15 (rd_o_3, and_8_out, decoder_1_out2);
  and and_16 (rd_o_4, and_8_out, decoder_1_out3);
endmodule

module program_counter (
  input  start,
  input  CLK,
  input  ri_1,
  input  ri_2,
  input  ri_3,
  input  ri_4,
  input  ri_5,
  input  ri_6,
  input  ri_7,
  input  ri_8,
  input  ri_9,
  input  ri_10,
  input  ri_11,
  input  ri_12,
  input  ri_13,
  input  ri_14,
  input  ri_15,
  input  ri_16,
  input  if_cond,
  input  l1_bit_1,
  input  l1_bit_2,
  input  l1_bit_3,
  input  l1_bit_4,
  input  l2_bit_1,
  input  l2_bit_2,
  input  l2_bit_3,
  input  l2_bit_4,
  input  rd_i_1,
  input  rd_i_2,
  input  rd_i_3,
  input  rd_i_4,
  input  rd_1,
  input  rd_2,
  input  rd_3,
  input  rd_4,
  output CLK_I_A,
  output CLK_A,
  output last_bit,
  output out_1,
  output RI_o_1,
  output RI_o_2,
  output RI_o_3,
  output RI_o_4,
  output RI_o_5,
  output RI_o_6,
  output RI_o_7,
  output RI_o_8,
  output RI_o_9,
  output RI_o_10,
  output RI_o_11,
  output RI_o_12,
  output RI_o_13,
  output RI_o_14,
  output RI_o_15,
  output RI_o_16,
  output RI_c_1,
  output RI_c_2,
  output RI_c_3,
  output RI_c_4,
  output RI_c_5,
  output RI_c_6,
  output RI_c_7,
  output RI_c_8,
  output RI_c_9,
  output RI_c_10,
  output RI_c_11,
  output RI_c_12,
  output RI_c_13,
  output RI_c_14,
  output RI_c_15,
  output RI_c_16,
  output rd_o_1,
  output rd_o_2,
  output rd_o_3,
  output rd_o_4,
  output rd_c_1,
  output rd_c_2,
  output rd_c_3,
  output rd_c_4
);

  wire and_1_out, and_2_out, and_3_out, and_4_out, and_5_out, and_6_out, and_7_out, and_8_out, and_9_out,
       and_10_out, and_11_out, and_12_out, and_13_out, and_14_out, and_15_out, and_16_out, and_17_out,
       and_18_out, and_51_out, and_52_out, and_53_out, and_54_out, and_55_out, and_56_out, and_57_out,
       and_58_out, and_59_out, and_60_out, and_61_out, and_62_out, and_63_out, and_64_out, and_65_out,
       and_66_out, and_67_out, and_68_out, and_69_out, and_70_out, and_71_out, and_72_out, and_73_out,
       and_74_out, and_75_out, and_76_out, and_77_out, and_78_out, and_79_out, and_80_out, and_81_out,
       and_82_out, and_91_out, and_92_out, and_93_out, and_94_out, and_95_out, and_96_out, and_97_out,
       and_98_out, and_99_out, and_100_out, and_101_out, and_102_out, and_103_out, and_104_out, and_105_out,
       and_106_out, d_ff_1_q, decoder_1_out0, decoder_1_out1, decoder_1_out2, decoder_1_out3, decoder_1_out4,
       decoder_1_out5, decoder_1_out6, decoder_1_out7, decoder_1_out8, decoder_1_out9, decoder_1_out10,
       decoder_1_out11, decoder_1_out12, decoder_1_out13, decoder_1_out14, decoder_1_out15, decoder_2_out0,
       decoder_2_out1, decoder_2_out2, decoder_2_out3, decoder_2_out4, decoder_2_out5, decoder_2_out6,
       decoder_2_out7, decoder_2_out8, decoder_2_out9, decoder_2_out10, decoder_2_out11, decoder_2_out12,
       decoder_2_out13, decoder_2_out14, decoder_2_out15, j_k_ff_1_q, j_k_ff_1_qn, j_k_ff_2_q, j_k_ff_2_qn,
       j_k_ff_3_q, j_k_ff_3_qn, j_k_ff_4_q, j_k_ff_4_qn, j_k_ff_5_q, j_k_ff_5_qn, j_k_ff_6_q, j_k_ff_6_qn,
       j_k_ff_7_q, j_k_ff_7_qn, j_k_ff_8_q, j_k_ff_8_qn, j_k_ff_9_q, j_k_ff_9_qn, j_k_ff_10_q, j_k_ff_10_qn,
       j_k_ff_11_q, j_k_ff_11_qn, j_k_ff_12_q, j_k_ff_12_qn, j_k_ff_13_q, j_k_ff_13_qn, j_k_ff_14_q,
       j_k_ff_14_qn, j_k_ff_15_q, j_k_ff_15_qn, j_k_ff_16_q, j_k_ff_17_q, j_k_ff_17_qn, j_k_ff_18_q,
       j_k_ff_18_qn, j_k_ff_19_q, j_k_ff_19_qn, j_k_ff_20_q, j_k_ff_20_qn, j_k_ff_21_q, j_k_ff_21_qn,
       j_k_ff_22_q, j_k_ff_22_qn, j_k_ff_23_q, j_k_ff_23_qn, j_k_ff_24_q, j_k_ff_24_qn, j_k_ff_25_q,
       j_k_ff_25_qn, j_k_ff_26_q, j_k_ff_26_qn, j_k_ff_27_q, j_k_ff_27_qn, j_k_ff_28_q, j_k_ff_28_qn,
       j_k_ff_29_q, j_k_ff_29_qn, j_k_ff_30_q, j_k_ff_30_qn, j_k_ff_31_q, j_k_ff_31_qn, j_k_ff_32_q,
       j_k_ff_32_qn, j_k_ff_33_q, j_k_ff_33_qn, j_k_ff_34_q, j_k_ff_34_qn, j_k_ff_35_q, j_k_ff_35_qn,
       j_k_ff_36_q, j_k_ff_36_qn, j_k_ff_37_q, j_k_ff_37_qn, j_k_ff_38_q, j_k_ff_38_qn, not_1_out, not_2_out,
       not_3_out, not_4_out, not_5_out, not_6_out, not_7_out, not_8_out, not_9_out, not_10_out, not_11_out,
       not_12_out, not_13_out, not_14_out, not_15_out, not_16_out, not_17_out, not_18_out, not_19_out,
       not_20_out, not_21_out, not_22_out, not_23_out, or_1_out, or_2_out, or_3_out, or_4_out, or_5_out,
       or_6_out, or_7_out, or_8_out, or_9_out, or_10_out, or_11_out, or_12_out, or_13_out, or_14_out,
       or_15_out, or_16_out, or_17_out, or_18_out, or_19_out, or_20_out, or_21_out, pull_resistor_1_node,
       transistor_5_out, transistor_42_out;

  not not_1 (not_1_out, or_3_out);
  not not_2 (not_2_out, transistor_5_out);
  and and_1 (and_1_out, CLK, not_2_out);
  and and_2 (and_2_out, last_bit, if_cond);
  and and_3 (and_3_out, CLK, CLK_A);
  and and_4 (and_4_out, if_cond, CLK_A);
  and and_5 (and_5_out, start, and_1_out);
  not not_3 (not_3_out, if_cond);
  and and_6 (and_6_out, and_2_out, or_3_out);
  Decoder #(.select(4)) decoder_1 (
    .out0(decoder_1_out0), .out1(decoder_1_out1), .out2(decoder_1_out2), .out3(decoder_1_out3),
    .out4(decoder_1_out4), .out5(decoder_1_out5), .out6(decoder_1_out6), .out7(decoder_1_out7),
    .out8(decoder_1_out8), .out9(decoder_1_out9), .out10(decoder_1_out10), .out11(decoder_1_out11),
    .out12(decoder_1_out12), .out13(decoder_1_out13), .out14(decoder_1_out14), .out15(decoder_1_out15),
    .sel({l1_bit_4, l1_bit_3, l1_bit_2, l1_bit_1}), .en(and_2_out));
  and and_7 (and_7_out, not_1_out, and_2_out);
  Decoder #(.select(4)) decoder_2 (
    .out0(decoder_2_out0), .out1(decoder_2_out1), .out2(decoder_2_out2), .out3(decoder_2_out3),
    .out4(decoder_2_out4), .out5(decoder_2_out5), .out6(decoder_2_out6), .out7(decoder_2_out7),
    .out8(decoder_2_out8), .out9(decoder_2_out9), .out10(decoder_2_out10), .out11(decoder_2_out11),
    .out12(decoder_2_out12), .out13(decoder_2_out13), .out14(decoder_2_out14), .out15(decoder_2_out15),
    .sel({l2_bit_4, l2_bit_3, l2_bit_2, l2_bit_1}), .en(and_2_out));
  and and_8 (and_8_out, rd_i_1, rd_1);
  and and_9 (and_9_out, rd_i_2, rd_2);
  and and_10 (and_10_out, rd_i_3, rd_3);
  and and_11 (and_11_out, rd_i_4, rd_4);
  not not_4 (not_4_out, last_bit);
  and and_12 (and_12_out, CLK, and_4_out);
  and and_13 (and_13_out, not_2_out, start);
  not not_5 (not_5_out, and_13_out);
  or or_1 (or_1_out, and_5_out, and_14_out);
  and and_14 (and_14_out, not_3_out, last_bit);
  Pull_Resistor pull_resistor_1 (.node(pull_resistor_1_node));
  Transistor transistor_1 (.in(and_8_out), .out(pull_resistor_1_node), .gate(1'b0));
  Transistor transistor_2 (.in(and_9_out), .out(pull_resistor_1_node), .gate(1'b0));
  Transistor transistor_3 (.in(and_10_out), .out(pull_resistor_1_node), .gate(1'b0));
  Transistor transistor_4 (.in(and_11_out), .out(pull_resistor_1_node), .gate(1'b0));
  D_Flip_Flop d_ff_1 (.D(and_15_out), .clk(and_3_out), .Q(d_ff_1_q));  // open: Qn, preset, reset
  and and_15 (and_15_out, not_4_out, or_2_out);
  J_K_Flip_Flop j_k_ff_1 (
    .J(and_13_out), .K(not_5_out), .clk(or_1_out), .Q(j_k_ff_1_q), .Qn(j_k_ff_1_qn), .preset(or_4_out),
    .reset(and_91_out));
  Transistor transistor_5 (.in(j_k_ff_1_q), .out(transistor_5_out), .gate(1'b0));
  J_K_Flip_Flop j_k_ff_2 (
    .J(j_k_ff_1_q), .K(j_k_ff_1_qn), .clk(or_1_out), .Q(j_k_ff_2_q), .Qn(j_k_ff_2_qn), .preset(or_5_out),
    .reset(and_92_out));
  or or_2 (or_2_out, pull_resistor_1_node, d_ff_1_q);
  and and_16 (and_16_out, pull_resistor_1_node, and_4_out);
  Transistor transistor_6 (.in(j_k_ff_2_q), .out(transistor_5_out), .gate(1'b0));
  J_K_Flip_Flop j_k_ff_3 (
    .J(j_k_ff_2_q), .K(j_k_ff_2_qn), .clk(or_1_out), .Q(j_k_ff_3_q), .Qn(j_k_ff_3_qn), .preset(or_6_out),
    .reset(and_93_out));
  Transistor transistor_7 (.in(j_k_ff_3_q), .out(transistor_5_out), .gate(1'b0));
  J_K_Flip_Flop j_k_ff_4 (
    .J(j_k_ff_3_q), .K(j_k_ff_3_qn), .clk(or_1_out), .Q(j_k_ff_4_q), .Qn(j_k_ff_4_qn), .preset(or_7_out),
    .reset(and_94_out));
  or or_3 (or_3_out, or_2_out, d_ff_1_q);
  Transistor transistor_8 (.in(j_k_ff_4_q), .out(transistor_5_out), .gate(1'b0));
  J_K_Flip_Flop j_k_ff_5 (
    .J(j_k_ff_4_q), .K(j_k_ff_4_qn), .clk(or_1_out), .Q(j_k_ff_5_q), .Qn(j_k_ff_5_qn), .preset(or_8_out),
    .reset(and_95_out));
  not not_6 (not_6_out, or_21_out);
  Transistor transistor_9 (.in(j_k_ff_5_q), .out(transistor_5_out), .gate(1'b0));
  J_K_Flip_Flop j_k_ff_6 (
    .J(j_k_ff_5_q), .K(j_k_ff_5_qn), .clk(or_1_out), .Q(j_k_ff_6_q), .Qn(j_k_ff_6_qn), .preset(or_9_out),
    .reset(and_96_out));
  and and_17 (and_17_out, not_6_out, transistor_5_out);
  Transistor transistor_10 (.in(j_k_ff_6_q), .out(transistor_5_out), .gate(1'b0));
  J_K_Flip_Flop j_k_ff_7 (
    .J(j_k_ff_6_q), .K(j_k_ff_6_qn), .clk(or_1_out), .Q(j_k_ff_7_q), .Qn(j_k_ff_7_qn), .preset(or_10_out),
    .reset(and_97_out));
  not not_7 (not_7_out, and_17_out);
  Transistor transistor_11 (.in(j_k_ff_7_q), .out(transistor_5_out), .gate(1'b0));
  J_K_Flip_Flop j_k_ff_8 (
    .J(j_k_ff_7_q), .K(j_k_ff_7_qn), .clk(or_1_out), .Q(j_k_ff_8_q), .Qn(j_k_ff_8_qn), .preset(or_11_out),
    .reset(and_98_out));
  Transistor transistor_12 (.in(j_k_ff_8_q), .out(transistor_5_out), .gate(1'b0));
  J_K_Flip_Flop j_k_ff_9 (
    .J(j_k_ff_8_q), .K(j_k_ff_8_qn), .clk(or_1_out), .Q(j_k_ff_9_q), .Qn(j_k_ff_9_qn), .preset(or_12_out),
    .reset(and_99_out));
  Transistor transistor_13 (.in(j_k_ff_9_q), .out(transistor_5_out), .gate(1'b0));
  J_K_Flip_Flop j_k_ff_10 (
    .J(j_k_ff_9_q), .K(j_k_ff_9_qn), .clk(or_1_out), .Q(j_k_ff_10_q), .Qn(j_k_ff_10_qn), .preset(or_13_out),
    .reset(and_100_out));
  Transistor transistor_14 (.in(j_k_ff_10_q), .out(transistor_5_out), .gate(1'b0));
  J_K_Flip_Flop j_k_ff_11 (
    .J(j_k_ff_10_q), .K(j_k_ff_10_qn), .clk(or_1_out), .Q(j_k_ff_11_q), .Qn(j_k_ff_11_qn),
    .preset(or_14_out), .reset(and_101_out));
  Transistor transistor_15 (.in(j_k_ff_11_q), .out(transistor_5_out), .gate(1'b0));
  J_K_Flip_Flop j_k_ff_12 (
    .J(j_k_ff_11_q), .K(j_k_ff_11_qn), .clk(or_1_out), .Q(j_k_ff_12_q), .Qn(j_k_ff_12_qn),
    .preset(or_15_out), .reset(and_102_out));
  Transistor transistor_16 (.in(j_k_ff_12_q), .out(transistor_5_out), .gate(1'b0));
  J_K_Flip_Flop j_k_ff_13 (
    .J(j_k_ff_12_q), .K(j_k_ff_12_qn), .clk(or_1_out), .Q(j_k_ff_13_q), .Qn(j_k_ff_13_qn),
    .preset(or_16_out), .reset(and_103_out));
  Transistor transistor_17 (.in(j_k_ff_13_q), .out(transistor_5_out), .gate(1'b0));
  J_K_Flip_Flop j_k_ff_14 (
    .J(j_k_ff_13_q), .K(j_k_ff_13_qn), .clk(or_1_out), .Q(j_k_ff_14_q), .Qn(j_k_ff_14_qn),
    .preset(or_17_out), .reset(and_104_out));
  Transistor transistor_18 (.in(j_k_ff_14_q), .out(transistor_5_out), .gate(1'b0));
  J_K_Flip_Flop j_k_ff_15 (
    .J(j_k_ff_14_q), .K(j_k_ff_14_qn), .clk(or_1_out), .Q(j_k_ff_15_q), .Qn(j_k_ff_15_qn),
    .preset(or_18_out), .reset(and_105_out));
  Pull_Resistor pull_resistor_2 (.node(transistor_5_out));
  Transistor transistor_19 (.in(j_k_ff_15_q), .out(transistor_5_out), .gate(1'b0));
  J_K_Flip_Flop j_k_ff_16 (
    .J(j_k_ff_15_q), .K(j_k_ff_15_qn), .clk(or_1_out), .Q(j_k_ff_16_q), .preset(or_19_out),
    .reset(and_106_out));  // open: Qn
  Transistor transistor_20 (.in(j_k_ff_16_q), .out(transistor_5_out), .gate(1'b0));
  J_K_Flip_Flop j_k_ff_17 (
    .J(and_17_out), .K(not_7_out), .clk(CLK), .Q(j_k_ff_17_q), .Qn(j_k_ff_17_qn));  // open: preset, reset
  Transistor transistor_21 (.in(j_k_ff_17_q), .out(CLK_I_A), .gate(1'b0));
  J_K_Flip_Flop j_k_ff_18 (
    .J(j_k_ff_17_q), .K(j_k_ff_17_qn), .clk(CLK), .Q(j_k_ff_18_q), .Qn(j_k_ff_18_qn));  // open: preset, reset
  and and_18 (and_18_out, CLK_I_A, CLK);
  Transistor transistor_22 (.in(j_k_ff_18_q), .out(CLK_I_A), .gate(1'b0));
  J_K_Flip_Flop j_k_ff_19 (
    .J(j_k_ff_18_q), .K(j_k_ff_18_qn), .clk(CLK), .Q(j_k_ff_19_q), .Qn(j_k_ff_19_qn));  // open: preset, reset
  Transistor transistor_23 (.in(j_k_ff_19_q), .out(CLK_I_A), .gate(1'b0));
  J_K_Flip_Flop j_k_ff_20 (
    .J(j_k_ff_19_q), .K(j_k_ff_19_qn), .clk(CLK), .Q(j_k_ff_20_q), .Qn(j_k_ff_20_qn));  // open: preset, reset
  and and_19 (RI_o_1, j_k_ff_1_q, ri_1);
  and and_20 (RI_o_2, j_k_ff_2_q, ri_2);
  and and_21 (RI_o_3, j_k_ff_3_q, ri_3);
  and and_22 (RI_o_4, j_k_ff_4_q, ri_4);
  and and_23 (RI_o_5, j_k_ff_5_q, ri_5);
  and and_24 (RI_o_6, j_k_ff_6_q, ri_6);
  and and_25 (RI_o_7, j_k_ff_7_q, ri_7);
  and and_26 (RI_o_8, j_k_ff_8_q, ri_8);
  and and_27 (RI_o_9, j_k_ff_9_q, ri_9);
  and and_28 (RI_o_10, j_k_ff_10_q, ri_10);
  and and_29 (RI_o_11, j_k_ff_11_q, ri_11);
  and and_30 (RI_o_12, j_k_ff_12_q, ri_12);
  and and_31 (RI_o_13, j_k_ff_13_q, ri_13);
  and and_32 (RI_o_14, j_k_ff_14_q, ri_14);
  and and_33 (RI_o_15, j_k_ff_15_q, ri_15);
  and and_34 (RI_o_16, j_k_ff_16_q, ri_16);
  and and_35 (RI_c_1, j_k_ff_1_q, and_18_out);
  and and_36 (RI_c_2, j_k_ff_2_q, and_18_out);
  and and_37 (RI_c_3, j_k_ff_3_q, and_18_out);
  and and_38 (RI_c_4, j_k_ff_4_q, and_18_out);
  and and_39 (RI_c_5, j_k_ff_5_q, and_18_out);
  and and_40 (RI_c_6, j_k_ff_6_q, and_18_out);
  and and_41 (RI_c_7, j_k_ff_7_q, and_18_out);
  and and_42 (RI_c_8, j_k_ff_8_q, and_18_out);
  and and_43 (RI_c_9, j_k_ff_9_q, and_18_out);
  and and_44 (RI_c_10, j_k_ff_10_q, and_18_out);
  and and_45 (RI_c_11, j_k_ff_11_q, and_18_out);
  and and_46 (RI_c_12, j_k_ff_12_q, and_18_out);
  and and_47 (RI_c_13, j_k_ff_13_q, and_18_out);
  and and_48 (RI_c_14, j_k_ff_14_q, and_18_out);
  and and_49 (RI_c_15, j_k_ff_15_q, and_18_out);
  and and_50 (RI_c_16, j_k_ff_16_q, and_18_out);
  and and_51 (and_51_out, and_6_out, decoder_1_out0);
  and and_52 (and_52_out, and_6_out, decoder_1_out1);
  and and_53 (and_53_out, and_6_out, decoder_1_out2);
  and and_54 (and_54_out, and_6_out, decoder_1_out3);
  and and_55 (and_55_out, and_6_out, decoder_1_out4);
  and and_56 (and_56_out, and_6_out, decoder_1_out5);
  and and_57 (and_57_out, and_6_out, decoder_1_out6);
  and and_58 (and_58_out, and_6_out, decoder_1_out7);
  and and_59 (and_59_out, and_6_out, decoder_1_out8);
  and and_60 (and_60_out, and_6_out, decoder_1_out9);
  and and_61 (and_61_out, and_6_out, decoder_1_out10);
  and and_62 (and_62_out, and_6_out, decoder_1_out11);
  and and_63 (and_63_out, and_6_out, decoder_1_out12);
  and and_64 (and_64_out, and_6_out, decoder_1_out13);
  and and_65 (and_65_out, and_6_out, decoder_1_out14);
  and and_66 (and_66_out, and_6_out, decoder_1_out15);
  and and_67 (and_67_out, and_7_out, decoder_2_out0);
  and and_68 (and_68_out, and_7_out, decoder_2_out1);
  and and_69 (and_69_out, and_7_out, decoder_2_out2);
  and and_70 (and_70_out, and_7_out, decoder_2_out3);
  and and_71 (and_71_out, and_7_out, decoder_2_out4);
  and and_72 (and_72_out, and_7_out, decoder_2_out5);
  and and_73 (and_73_out, and_7_out, decoder_2_out6);
  and and_74 (and_74_out, and_7_out, decoder_2_out7);
  and and_75 (and_75_out, and_7_out, decoder_2_out8);
  and and_76 (and_76_out, and_7_out, decoder_2_out9);
  and and_77 (and_77_out, and_7_out, decoder_2_out10);
  and and_78 (and_78_out, and_7_out, decoder_2_out11);
  and and_79 (and_79_out, and_7_out, decoder_2_out12);
  and and_80 (and_80_out, and_7_out, decoder_2_out13);
  and and_81 (and_81_out, and_7_out, decoder_2_out14);
  and and_82 (and_82_out, and_7_out, decoder_2_out15);
  Transistor transistor_24 (.in(j_k_ff_20_q), .out(CLK_I_A), .gate(1'b0));
  J_K_Flip_Flop j_k_ff_21 (
    .J(j_k_ff_20_q), .K(j_k_ff_20_qn), .clk(CLK), .Q(j_k_ff_21_q), .Qn(j_k_ff_21_qn));  // open: preset, reset
  Transistor transistor_25 (.in(j_k_ff_21_q), .out(CLK_I_A), .gate(1'b0));
  J_K_Flip_Flop j_k_ff_22 (
    .J(j_k_ff_21_q), .K(j_k_ff_21_qn), .clk(CLK), .Q(j_k_ff_22_q), .Qn(j_k_ff_22_qn));  // open: preset, reset
  Transistor transistor_26 (.in(RI_o_1), .out(out_1), .gate(1'b0));
  Transistor transistor_27 (.in(RI_o_2), .out(out_1), .gate(1'b0));
  Transistor transistor_28 (.in(RI_o_3), .out(out_1), .gate(1'b0));
  Transistor transistor_29 (.in(RI_o_4), .out(out_1), .gate(1'b0));
  Transistor transistor_30 (.in(RI_o_5), .out(out_1), .gate(1'b0));
  Transistor transistor_31 (.in(RI_o_6), .out(out_1), .gate(1'b0));
  Transistor transistor_32 (.in(RI_o_7), .out(out_1), .gate(1'b0));
  Transistor transistor_33 (.in(RI_o_8), .out(out_1), .gate(1'b0));
  Transistor transistor_34 (.in(RI_o_9), .out(out_1), .gate(1'b0));
  Transistor transistor_35 (.in(RI_o_10), .out(out_1), .gate(1'b0));
  Transistor transistor_36 (.in(RI_o_11), .out(out_1), .gate(1'b0));
  Transistor transistor_37 (.in(RI_o_12), .out(out_1), .gate(1'b0));
  Transistor transistor_38 (.in(RI_o_13), .out(out_1), .gate(1'b0));
  Transistor transistor_39 (.in(RI_o_14), .out(out_1), .gate(1'b0));
  Transistor transistor_40 (.in(RI_o_15), .out(out_1), .gate(1'b0));
  Transistor transistor_41 (.in(RI_o_16), .out(out_1), .gate(1'b0));
  Pull_Resistor pull_resistor_3 (.node(out_1));
  Transistor transistor_42 (.in(RI_c_1), .out(transistor_42_out), .gate(1'b0));
  Transistor transistor_43 (.in(RI_c_2), .out(transistor_42_out), .gate(1'b0));
  Transistor transistor_44 (.in(RI_c_3), .out(transistor_42_out), .gate(1'b0));
  Transistor transistor_45 (.in(RI_c_4), .out(transistor_42_out), .gate(1'b0));
  Transistor transistor_46 (.in(RI_c_5), .out(transistor_42_out), .gate(1'b0));
  Transistor transistor_47 (.in(RI_c_6), .out(transistor_42_out), .gate(1'b0));
  Transistor transistor_48 (.in(RI_c_7), .out(transistor_42_out), .gate(1'b0));
  Transistor transistor_49 (.in(RI_c_8), .out(transistor_42_out), .gate(1'b0));
  Transistor transistor_50 (.in(RI_c_9), .out(transistor_42_out), .gate(1'b0));
  Transistor transistor_51 (.in(RI_c_10), .out(transistor_42_out), .gate(1'b0));
  Transistor transistor_52 (.in(RI_c_11), .out(transistor_42_out), .gate(1'b0));
  Transistor transistor_53 (.in(RI_c_12), .out(transistor_42_out), .gate(1'b0));
  Transistor transistor_54 (.in(RI_c_13), .out(transistor_42_out), .gate(1'b0));
  Transistor transistor_55 (.in(RI_c_14), .out(transistor_42_out), .gate(1'b0));
  Transistor transistor_56 (.in(RI_c_15), .out(transistor_42_out), .gate(1'b0));
  Transistor transistor_57 (.in(RI_c_16), .out(transistor_42_out), .gate(1'b0));
  Pull_Resistor pull_resistor_4 (.node(transistor_42_out));
  Transistor transistor_58 (.in(j_k_ff_22_q), .out(CLK_I_A), .gate(1'b0));
  J_K_Flip_Flop j_k_ff_23 (
    .J(j_k_ff_22_q), .K(j_k_ff_22_qn), .clk(CLK), .Q(j_k_ff_23_q), .Qn(j_k_ff_23_qn));  // open: preset, reset
  or or_4 (or_4_out, and_51_out, and_67_out);
  or or_5 (or_5_out, and_52_out, and_68_out);
  or or_6 (or_6_out, and_53_out, and_69_out);
  or or_7 (or_7_out, and_54_out, and_70_out);
  or or_8 (or_8_out, and_55_out, and_71_out);
  or or_9 (or_9_out, and_56_out, and_72_out);
  or or_10 (or_10_out, and_57_out, and_73_out);
  or or_11 (or_11_out, and_58_out, and_74_out);
  or or_12 (or_12_out, and_59_out, and_75_out);
  or or_13 (or_13_out, and_60_out, and_76_out);
  or or_14 (or_14_out, and_61_out, and_77_out);
  or or_15 (or_15_out, and_62_out, and_78_out);
  or or_16 (or_16_out, and_63_out, and_79_out);
  or or_17 (or_17_out, and_64_out, and_80_out);
  or or_18 (or_18_out, and_65_out, and_81_out);
  or or_19 (or_19_out, and_66_out, and_82_out);
  Transistor transistor_59 (.in(j_k_ff_23_q), .out(CLK_I_A), .gate(1'b0));
  J_K_Flip_Flop j_k_ff_24 (
    .J(j_k_ff_23_q), .K(j_k_ff_23_qn), .clk(CLK), .Q(j_k_ff_24_q), .Qn(j_k_ff_24_qn));  // open: preset, reset
  Transistor transistor_60 (.in(j_k_ff_24_q), .out(CLK_I_A), .gate(1'b0));
  Pull_Resistor pull_resistor_5 (.node(CLK_I_A));
  J_K_Flip_Flop j_k_ff_25 (
    .J(j_k_ff_24_q), .K(j_k_ff_24_qn), .clk(CLK), .Q(j_k_ff_25_q), .Qn(j_k_ff_25_qn));  // open: preset, reset
  Transistor transistor_61 (.in(j_k_ff_25_q), .out(CLK_I_A), .gate(1'b0));
  J_K_Flip_Flop j_k_ff_26 (
    .J(j_k_ff_25_q), .K(j_k_ff_25_qn), .clk(CLK), .Q(j_k_ff_26_q), .Qn(j_k_ff_26_qn));  // open: preset, reset
  Transistor transistor_62 (.in(j_k_ff_26_q), .out(CLK_I_A), .gate(1'b0));
  J_K_Flip_Flop j_k_ff_27 (
    .J(j_k_ff_26_q), .K(j_k_ff_26_qn), .clk(CLK), .Q(j_k_ff_27_q), .Qn(j_k_ff_27_qn));  // open: preset, reset
  and and_83 (rd_o_1, rd_1, and_16_out);
  and and_84 (rd_o_2, rd_2, and_16_out);
  and and_85 (rd_o_3, rd_3, and_16_out);
  and and_86 (rd_o_4, rd_4, and_16_out);
  and and_87 (rd_c_1, rd_1, and_12_out);
  and and_88 (rd_c_2, rd_2, and_12_out);
  and and_89 (rd_c_3, rd_3, and_12_out);
  and and_90 (rd_c_4, rd_4, and_12_out);
  Transistor transistor_63 (.in(j_k_ff_27_q), .out(CLK_I_A), .gate(1'b0));
  J_K_Flip_Flop j_k_ff_28 (
    .J(j_k_ff_27_q), .K(j_k_ff_27_qn), .clk(CLK), .Q(j_k_ff_28_q), .Qn(j_k_ff_28_qn));  // open: preset, reset
  Transistor transistor_64 (.in(j_k_ff_28_q), .out(CLK_I_A), .gate(1'b0));
  J_K_Flip_Flop j_k_ff_29 (
    .J(j_k_ff_28_q), .K(j_k_ff_28_qn), .clk(CLK), .Q(j_k_ff_29_q), .Qn(j_k_ff_29_qn));  // open: preset, reset
  not not_8 (not_8_out, or_4_out);
  not not_9 (not_9_out, or_5_out);
  not not_10 (not_10_out, or_6_out);
  not not_11 (not_11_out, or_7_out);
  not not_12 (not_12_out, or_8_out);
  not not_13 (not_13_out, or_9_out);
  not not_14 (not_14_out, or_10_out);
  not not_15 (not_15_out, or_11_out);
  not not_16 (not_16_out, or_12_out);
  not not_17 (not_17_out, or_13_out);
  not not_18 (not_18_out, or_14_out);
  not not_19 (not_19_out, or_15_out);
  not not_20 (not_20_out, or_16_out);
  not not_21 (not_21_out, or_17_out);
  not not_22 (not_22_out, or_18_out);
  not not_23 (not_23_out, or_19_out);
  Transistor transistor_65 (.in(j_k_ff_29_q), .out(CLK_I_A), .gate(1'b0));
  J_K_Flip_Flop j_k_ff_30 (
    .J(j_k_ff_29_q), .K(j_k_ff_29_qn), .clk(CLK), .Q(j_k_ff_30_q), .Qn(j_k_ff_30_qn));  // open: preset, reset
  and and_91 (and_91_out, not_8_out, and_2_out);
  and and_92 (and_92_out, not_9_out, and_2_out);
  and and_93 (and_93_out, not_10_out, and_2_out);
  and and_94 (and_94_out, not_11_out, and_2_out);
  and and_95 (and_95_out, not_12_out, and_2_out);
  and and_96 (and_96_out, not_13_out, and_2_out);
  and and_97 (and_97_out, not_14_out, and_2_out);
  and and_98 (and_98_out, not_15_out, and_2_out);
  and and_99 (and_99_out, not_16_out, and_2_out);
  and and_100 (and_100_out, not_17_out, and_2_out);
  and and_101 (and_101_out, not_18_out, and_2_out);
  and and_102 (and_102_out, not_19_out, and_2_out);
  and and_103 (and_103_out, not_20_out, and_2_out);
  and and_104 (and_104_out, not_21_out, and_2_out);
  and and_105 (and_105_out, not_22_out, and_2_out);
  and and_106 (and_106_out, not_23_out, and_2_out);
  Transistor transistor_66 (.in(j_k_ff_30_q), .out(CLK_I_A), .gate(1'b0));
  J_K_Flip_Flop j_k_ff_31 (
    .J(j_k_ff_30_q), .K(j_k_ff_30_qn), .clk(CLK), .Q(j_k_ff_31_q), .Qn(j_k_ff_31_qn));  // open: preset, reset
  or or_20 (or_20_out, CLK_A, j_k_ff_31_q);
  J_K_Flip_Flop j_k_ff_32 (
    .J(j_k_ff_31_q), .K(j_k_ff_31_qn), .clk(CLK), .Q(j_k_ff_32_q), .Qn(j_k_ff_32_qn));  // open: preset, reset
  Transistor transistor_67 (.in(j_k_ff_32_q), .out(CLK_A), .gate(1'b0));
  J_K_Flip_Flop j_k_ff_33 (
    .J(j_k_ff_32_q), .K(j_k_ff_32_qn), .clk(CLK), .Q(j_k_ff_33_q), .Qn(j_k_ff_33_qn));  // open: preset, reset
  or or_21 (or_21_out, CLK_I_A, or_20_out);
  Transistor transistor_68 (.in(j_k_ff_33_q), .out(CLK_A), .gate(1'b0));
  Pull_Resistor pull_resistor_6 (.node(CLK_A));
  J_K_Flip_Flop j_k_ff_34 (
    .J(j_k_ff_33_q), .K(j_k_ff_33_qn), .clk(CLK), .Q(j_k_ff_34_q), .Qn(j_k_ff_34_qn));  // open: preset, reset
  Transistor transistor_69 (.in(j_k_ff_34_q), .out(CLK_A), .gate(1'b0));
  J_K_Flip_Flop j_k_ff_35 (
    .J(j_k_ff_34_q), .K(j_k_ff_34_qn), .clk(CLK), .Q(j_k_ff_35_q), .Qn(j_k_ff_35_qn));  // open: preset, reset
  Transistor transistor_70 (.in(j_k_ff_35_q), .out(CLK_A), .gate(1'b0));
  J_K_Flip_Flop j_k_ff_36 (
    .J(j_k_ff_35_q), .K(j_k_ff_35_qn), .clk(CLK), .Q(j_k_ff_36_q), .Qn(j_k_ff_36_qn));  // open: preset, reset
  Transistor transistor_71 (.in(j_k_ff_36_q), .out(CLK_A), .gate(1'b0));
  J_K_Flip_Flop j_k_ff_37 (
    .J(j_k_ff_36_q), .K(j_k_ff_36_qn), .clk(CLK), .Q(j_k_ff_37_q), .Qn(j_k_ff_37_qn));  // open: preset, reset
  Transistor transistor_72 (.in(j_k_ff_37_q), .out(CLK_A), .gate(1'b0));
  J_K_Flip_Flop j_k_ff_38 (
    .J(j_k_ff_37_q), .K(j_k_ff_37_qn), .clk(CLK), .Q(j_k_ff_38_q), .Qn(j_k_ff_38_qn));  // open: preset, reset
  Transistor transistor_73 (.in(j_k_ff_38_q), .out(CLK_A), .gate(1'b0));
  J_K_Flip_Flop j_k_ff_39 (.J(j_k_ff_38_q), .K(j_k_ff_38_qn), .clk(CLK), .Q(last_bit));  // open: Qn, preset, reset
  Transistor transistor_74 (.in(last_bit), .out(CLK_A), .gate(1'b0));
endmodule

module output_control (
  input  CLK,
  input  CLK_A,
  input  is_shw_on,
  input  rd_i_1,
  input  rd_i_2,
  input  rd_i_3,
  input  rd_i_4,
  input  rd_1,
  input  rd_2,
  input  rd_3,
  input  rd_4,
  input  clear,
  output [7:0] s_o_1,
  output [7:0] s_o_2,
  output [7:0] s_o_3,
  output [7:0] s_o_4,
  output [7:0] s_o_5,
  output [7:0] s_o_6,
  output [7:0] s_o_7,
  output [7:0] s_o_8,
  output rd_o_1,
  output rd_o_2,
  output rd_o_3,
  output rd_o_4,
  output rd_c_1,
  output rd_c_2,
  output rd_c_3,
  output rd_c_4
);

  wire and_1_out, and_2_out, and_3_out, and_4_out, and_5_out, and_6_out, and_7_out, and_8_out, and_9_out,
       and_14_out, and_15_out, and_16_out, and_17_out, and_18_out, and_19_out, and_20_out, and_21_out,
       and_22_out, and_23_out, and_24_out, and_25_out, and_26_out, and_27_out, and_28_out, and_29_out,
       d_ff_1_q, d_ff_2_q, d_ff_3_q, d_ff_4_q, d_ff_5_q, d_ff_6_q, d_ff_7_q, d_ff_8_q, not_1_out,
       pull_resistor_1_node, transistor_1_out;

  and and_1 (and_1_out, CLK, CLK_A);
  and and_2 (and_2_out, clear, CLK_A);
  and and_3 (and_3_out, is_shw_on, CLK_A);
  and and_4 (and_4_out, and_1_out, is_shw_on);
  D_Flip_Flop d_ff_1 (.D(d_ff_8_q), .clk(not_1_out), .Q(d_ff_1_q), .preset(and_2_out));  // open: Qn, reset
  not not_1 (not_1_out, and_3_out);
  and and_5 (and_5_out, pull_resistor_1_node, and_3_out);
  and and_6 (and_6_out, rd_i_1, rd_1);
  and and_7 (and_7_out, rd_i_2, rd_2);
  and and_8 (and_8_out, rd_i_3, rd_3);
  and and_9 (and_9_out, rd_i_4, rd_4);
  and and_10 (rd_c_1, rd_1, and_4_out);
  and and_11 (rd_c_2, rd_2, and_4_out);
  and and_12 (rd_c_3, rd_3, and_4_out);
  and and_13 (rd_c_4, rd_4, and_4_out);
  Transistor transistor_1 (.in(d_ff_1_q), .out(transistor_1_out), .gate(1'b0));
  D_Flip_Flop d_ff_2 (.D(d_ff_1_q), .clk(not_1_out), .Q(d_ff_2_q), .reset(and_2_out));  // open: Qn, preset
  Pull_Resistor pull_resistor_1 (.node(pull_resistor_1_node));
  Transistor transistor_2 (.in(and_6_out), .out(pull_resistor_1_node), .gate(1'b0));
  Transistor transistor_3 (.in(and_7_out), .out(pull_resistor_1_node), .gate(1'b0));
  Transistor transistor_4 (.in(and_8_out), .out(pull_resistor_1_node), .gate(1'b0));
  Transistor transistor_5 (.in(and_9_out), .out(pull_resistor_1_node), .gate(1'b0));
  Transistor transistor_6 (.in(d_ff_2_q), .out(transistor_1_out), .gate(1'b0));
  D_Flip_Flop d_ff_3 (.D(d_ff_2_q), .clk(not_1_out), .Q(d_ff_3_q), .reset(and_2_out));  // open: Qn, preset
  Transistor transistor_7 (.in(d_ff_3_q), .out(transistor_1_out), .gate(1'b0));
  D_Flip_Flop d_ff_4 (.D(d_ff_3_q), .clk(not_1_out), .Q(d_ff_4_q), .reset(and_2_out));  // open: Qn, preset
  Transistor transistor_8 (.in(d_ff_4_q), .out(transistor_1_out), .gate(1'b0));
  D_Flip_Flop d_ff_5 (.D(d_ff_4_q), .clk(not_1_out), .Q(d_ff_5_q), .reset(and_2_out));  // open: Qn, preset
  Transistor transistor_9 (.in(d_ff_5_q), .out(transistor_1_out), .gate(1'b0));
  D_Flip_Flop d_ff_6 (.D(d_ff_5_q), .clk(not_1_out), .Q(d_ff_6_q), .reset(and_2_out));  // open: Qn, preset
  Transistor transistor_10 (.in(d_ff_6_q), .out(transistor_1_out), .gate(1'b0));
  D_Flip_Flop d_ff_7 (.D(d_ff_6_q), .clk(not_1_out), .Q(d_ff_7_q), .reset(and_2_out));  // open: Qn, preset
  Transistor transistor_11 (.in(d_ff_7_q), .out(transistor_1_out), .gate(1'b0));
  D_Flip_Flop d_ff_8 (.D(d_ff_7_q), .clk(not_1_out), .Q(d_ff_8_q), .reset(and_2_out));  // open: Qn, preset
  Transistor transistor_12 (.in(d_ff_8_q), .out(transistor_1_out), .gate(1'b0));
  Pull_Resistor pull_resistor_2 (.node(transistor_1_out));
  and and_14 (and_14_out, and_5_out, d_ff_1_q);
  and and_15 (and_15_out, and_5_out, d_ff_2_q);
  and and_16 (and_16_out, and_5_out, d_ff_3_q);
  and and_17 (and_17_out, and_5_out, d_ff_4_q);
  and and_18 (and_18_out, and_5_out, d_ff_5_q);
  and and_19 (and_19_out, and_5_out, d_ff_6_q);
  and and_20 (and_20_out, and_5_out, d_ff_7_q);
  and and_21 (and_21_out, and_5_out, d_ff_8_q);
  and and_22 (and_22_out, and_4_out, d_ff_1_q);
  and and_23 (and_23_out, and_4_out, d_ff_2_q);
  and and_24 (and_24_out, and_4_out, d_ff_3_q);
  and and_25 (and_25_out, and_4_out, d_ff_4_q);
  and and_26 (and_26_out, and_4_out, d_ff_5_q);
  and and_27 (and_27_out, and_4_out, d_ff_6_q);
  and and_28 (and_28_out, and_4_out, d_ff_7_q);
  and and_29 (and_29_out, and_4_out, d_ff_8_q);
  and and_30 (rd_o_1, and_5_out, rd_1);
  and and_31 (rd_o_2, and_5_out, rd_2);
  and and_32 (rd_o_3, and_5_out, rd_3);
  and and_33 (rd_o_4, and_5_out, rd_4);
  D_Flip_Flop d_ff_9 (.D(and_14_out), .clk(and_22_out), .Q(s_o_8[7]), .reset(and_2_out));  // open: Qn, preset
  D_Flip_Flop d_ff_10 (.D(and_15_out), .clk(and_23_out), .Q(s_o_8[6]), .reset(and_2_out));  // open: Qn, preset
  D_Flip_Flop d_ff_11 (.D(and_16_out), .clk(and_24_out), .Q(s_o_8[5]), .reset(and_2_out));  // open: Qn, preset
  D_Flip_Flop d_ff_12 (.D(and_17_out), .clk(and_25_out), .Q(s_o_8[4]), .reset(and_2_out));  // open: Qn, preset
  D_Flip_Flop d_ff_13 (.D(and_18_out), .clk(and_26_out), .Q(s_o_8[3]), .reset(and_2_out));  // open: Qn, preset
  D_Flip_Flop d_ff_14 (.D(and_19_out), .clk(and_27_out), .Q(s_o_8[2]), .reset(and_2_out));  // open: Qn, preset
  D_Flip_Flop d_ff_15 (.D(and_20_out), .clk(and_28_out), .Q(s_o_8[1]), .reset(and_2_out));  // open: Qn, preset
  D_Flip_Flop d_ff_16 (.D(and_21_out), .clk(and_29_out), .Q(s_o_8[0]), .reset(and_2_out));  // open: Qn, preset
  D_Flip_Flop d_ff_17 (.D(s_o_8[7]), .clk(and_22_out), .Q(s_o_7[7]), .reset(and_2_out));  // open: Qn, preset
  D_Flip_Flop d_ff_18 (.D(s_o_8[6]), .clk(and_23_out), .Q(s_o_7[6]), .reset(and_2_out));  // open: Qn, preset
  D_Flip_Flop d_ff_19 (.D(s_o_8[5]), .clk(and_24_out), .Q(s_o_7[5]), .reset(and_2_out));  // open: Qn, preset
  D_Flip_Flop d_ff_20 (.D(s_o_8[4]), .clk(and_25_out), .Q(s_o_7[4]), .reset(and_2_out));  // open: Qn, preset
  D_Flip_Flop d_ff_21 (.D(s_o_8[3]), .clk(and_26_out), .Q(s_o_7[3]), .reset(and_2_out));  // open: Qn, preset
  D_Flip_Flop d_ff_22 (.D(s_o_8[2]), .clk(and_27_out), .Q(s_o_7[2]), .reset(and_2_out));  // open: Qn, preset
  D_Flip_Flop d_ff_23 (.D(s_o_8[1]), .clk(and_28_out), .Q(s_o_7[1]), .reset(and_2_out));  // open: Qn, preset
  D_Flip_Flop d_ff_24 (.D(s_o_8[0]), .clk(and_29_out), .Q(s_o_7[0]), .reset(and_2_out));  // open: Qn, preset
  D_Flip_Flop d_ff_25 (.D(s_o_7[7]), .clk(and_22_out), .Q(s_o_6[7]), .reset(and_2_out));  // open: Qn, preset
  D_Flip_Flop d_ff_26 (.D(s_o_7[6]), .clk(and_23_out), .Q(s_o_6[6]), .reset(and_2_out));  // open: Qn, preset
  D_Flip_Flop d_ff_27 (.D(s_o_7[5]), .clk(and_24_out), .Q(s_o_6[5]), .reset(and_2_out));  // open: Qn, preset
  D_Flip_Flop d_ff_28 (.D(s_o_7[4]), .clk(and_25_out), .Q(s_o_6[4]), .reset(and_2_out));  // open: Qn, preset
  D_Flip_Flop d_ff_29 (.D(s_o_7[3]), .clk(and_26_out), .Q(s_o_6[3]), .reset(and_2_out));  // open: Qn, preset
  D_Flip_Flop d_ff_30 (.D(s_o_7[2]), .clk(and_27_out), .Q(s_o_6[2]), .reset(and_2_out));  // open: Qn, preset
  D_Flip_Flop d_ff_31 (.D(s_o_7[1]), .clk(and_28_out), .Q(s_o_6[1]), .reset(and_2_out));  // open: Qn, preset
  D_Flip_Flop d_ff_32 (.D(s_o_7[0]), .clk(and_29_out), .Q(s_o_6[0]), .reset(and_2_out));  // open: Qn, preset
  D_Flip_Flop d_ff_33 (.D(s_o_6[7]), .clk(and_22_out), .Q(s_o_5[7]), .reset(and_2_out));  // open: Qn, preset
  D_Flip_Flop d_ff_34 (.D(s_o_6[6]), .clk(and_23_out), .Q(s_o_5[6]), .reset(and_2_out));  // open: Qn, preset
  D_Flip_Flop d_ff_35 (.D(s_o_6[5]), .clk(and_24_out), .Q(s_o_5[5]), .reset(and_2_out));  // open: Qn, preset
  D_Flip_Flop d_ff_36 (.D(s_o_6[4]), .clk(and_25_out), .Q(s_o_5[4]), .reset(and_2_out));  // open: Qn, preset
  D_Flip_Flop d_ff_37 (.D(s_o_6[3]), .clk(and_26_out), .Q(s_o_5[3]), .reset(and_2_out));  // open: Qn, preset
  D_Flip_Flop d_ff_38 (.D(s_o_6[2]), .clk(and_27_out), .Q(s_o_5[2]), .reset(and_2_out));  // open: Qn, preset
  D_Flip_Flop d_ff_39 (.D(s_o_6[1]), .clk(and_28_out), .Q(s_o_5[1]), .reset(and_2_out));  // open: Qn, preset
  D_Flip_Flop d_ff_40 (.D(s_o_6[0]), .clk(and_29_out), .Q(s_o_5[0]), .reset(and_2_out));  // open: Qn, preset
  D_Flip_Flop d_ff_41 (.D(s_o_5[7]), .clk(and_22_out), .Q(s_o_4[7]), .reset(and_2_out));  // open: Qn, preset
  D_Flip_Flop d_ff_42 (.D(s_o_5[6]), .clk(and_23_out), .Q(s_o_4[6]), .reset(and_2_out));  // open: Qn, preset
  D_Flip_Flop d_ff_43 (.D(s_o_5[5]), .clk(and_24_out), .Q(s_o_4[5]), .reset(and_2_out));  // open: Qn, preset
  D_Flip_Flop d_ff_44 (.D(s_o_5[4]), .clk(and_25_out), .Q(s_o_4[4]), .reset(and_2_out));  // open: Qn, preset
  D_Flip_Flop d_ff_45 (.D(s_o_5[3]), .clk(and_26_out), .Q(s_o_4[3]), .reset(and_2_out));  // open: Qn, preset
  D_Flip_Flop d_ff_46 (.D(s_o_5[2]), .clk(and_27_out), .Q(s_o_4[2]), .reset(and_2_out));  // open: Qn, preset
  D_Flip_Flop d_ff_47 (.D(s_o_5[1]), .clk(and_28_out), .Q(s_o_4[1]), .reset(and_2_out));  // open: Qn, preset
  D_Flip_Flop d_ff_48 (.D(s_o_5[0]), .clk(and_29_out), .Q(s_o_4[0]), .reset(and_2_out));  // open: Qn, preset
  D_Flip_Flop d_ff_49 (.D(s_o_4[7]), .clk(and_22_out), .Q(s_o_3[7]), .reset(and_2_out));  // open: Qn, preset
  D_Flip_Flop d_ff_50 (.D(s_o_4[6]), .clk(and_23_out), .Q(s_o_3[6]), .reset(and_2_out));  // open: Qn, preset
  D_Flip_Flop d_ff_51 (.D(s_o_4[5]), .clk(and_24_out), .Q(s_o_3[5]), .reset(and_2_out));  // open: Qn, preset
  D_Flip_Flop d_ff_52 (.D(s_o_4[4]), .clk(and_25_out), .Q(s_o_3[4]), .reset(and_2_out));  // open: Qn, preset
  D_Flip_Flop d_ff_53 (.D(s_o_4[3]), .clk(and_26_out), .Q(s_o_3[3]), .reset(and_2_out));  // open: Qn, preset
  D_Flip_Flop d_ff_54 (.D(s_o_4[2]), .clk(and_27_out), .Q(s_o_3[2]), .reset(and_2_out));  // open: Qn, preset
  D_Flip_Flop d_ff_55 (.D(s_o_4[1]), .clk(and_28_out), .Q(s_o_3[1]), .reset(and_2_out));  // open: Qn, preset
  D_Flip_Flop d_ff_56 (.D(s_o_4[0]), .clk(and_29_out), .Q(s_o_3[0]), .reset(and_2_out));  // open: Qn, preset
  D_Flip_Flop d_ff_57 (.D(s_o_3[7]), .clk(and_22_out), .Q(s_o_2[7]), .reset(and_2_out));  // open: Qn, preset
  D_Flip_Flop d_ff_58 (.D(s_o_3[6]), .clk(and_23_out), .Q(s_o_2[6]), .reset(and_2_out));  // open: Qn, preset
  D_Flip_Flop d_ff_59 (.D(s_o_3[5]), .clk(and_24_out), .Q(s_o_2[5]), .reset(and_2_out));  // open: Qn, preset
  D_Flip_Flop d_ff_60 (.D(s_o_3[4]), .clk(and_25_out), .Q(s_o_2[4]), .reset(and_2_out));  // open: Qn, preset
  D_Flip_Flop d_ff_61 (.D(s_o_3[3]), .clk(and_26_out), .Q(s_o_2[3]), .reset(and_2_out));  // open: Qn, preset
  D_Flip_Flop d_ff_62 (.D(s_o_3[2]), .clk(and_27_out), .Q(s_o_2[2]), .reset(and_2_out));  // open: Qn, preset
  D_Flip_Flop d_ff_63 (.D(s_o_3[1]), .clk(and_28_out), .Q(s_o_2[1]), .reset(and_2_out));  // open: Qn, preset
  D_Flip_Flop d_ff_64 (.D(s_o_3[0]), .clk(and_29_out), .Q(s_o_2[0]), .reset(and_2_out));  // open: Qn, preset
  D_Flip_Flop d_ff_65 (.D(s_o_2[7]), .clk(and_22_out), .Q(s_o_1[7]), .reset(and_2_out));  // open: Qn, preset
  D_Flip_Flop d_ff_66 (.D(s_o_2[6]), .clk(and_23_out), .Q(s_o_1[6]), .reset(and_2_out));  // open: Qn, preset
  D_Flip_Flop d_ff_67 (.D(s_o_2[5]), .clk(and_24_out), .Q(s_o_1[5]), .reset(and_2_out));  // open: Qn, preset
  D_Flip_Flop d_ff_68 (.D(s_o_2[4]), .clk(and_25_out), .Q(s_o_1[4]), .reset(and_2_out));  // open: Qn, preset
  D_Flip_Flop d_ff_69 (.D(s_o_2[3]), .clk(and_26_out), .Q(s_o_1[3]), .reset(and_2_out));  // open: Qn, preset
  D_Flip_Flop d_ff_70 (.D(s_o_2[2]), .clk(and_27_out), .Q(s_o_1[2]), .reset(and_2_out));  // open: Qn, preset
  D_Flip_Flop d_ff_71 (.D(s_o_2[1]), .clk(and_28_out), .Q(s_o_1[1]), .reset(and_2_out));  // open: Qn, preset
  D_Flip_Flop d_ff_72 (.D(s_o_2[0]), .clk(and_29_out), .Q(s_o_1[0]), .reset(and_2_out));  // open: Qn, preset
  D_Flip_Flop d_ff_73 (.D(s_o_1[7]), .clk(and_22_out), .reset(and_2_out));  // open: Q, Qn, preset
  D_Flip_Flop d_ff_74 (.D(s_o_1[6]), .clk(and_23_out), .reset(and_2_out));  // open: Q, Qn, preset
  D_Flip_Flop d_ff_75 (.D(s_o_1[5]), .clk(and_24_out), .reset(and_2_out));  // open: Q, Qn, preset
  D_Flip_Flop d_ff_76 (.D(s_o_1[4]), .clk(and_25_out), .reset(and_2_out));  // open: Q, Qn, preset
  D_Flip_Flop d_ff_77 (.D(s_o_1[3]), .clk(and_26_out), .reset(and_2_out));  // open: Q, Qn, preset
  D_Flip_Flop d_ff_78 (.D(s_o_1[2]), .clk(and_27_out), .reset(and_2_out));  // open: Q, Qn, preset
  D_Flip_Flop d_ff_79 (.D(s_o_1[1]), .clk(and_28_out), .reset(and_2_out));  // open: Q, Qn, preset
  D_Flip_Flop d_ff_80 (.D(s_o_1[0]), .clk(and_29_out), .reset(and_2_out));  // open: Q, Qn, preset
endmodule
module input_control (
);

  wire and_1_out, and_2_out, and_3_out, and_4_out, and_5_out, and_6_out, and_7_out, and_8_out, and_9_out,
       and_10_out, and_11_out, and_12_out, and_13_out, and_14_out, and_15_out, and_16_out, and_17_out,
       and_18_out, and_19_out, and_20_out, and_21_out, and_22_out, and_23_out, and_24_out, and_25_out,
       and_26_out, and_27_out, and_28_out, and_29_out, and_30_out, and_31_out, and_32_out, and_33_out,
       button_1_out, button_2_out, button_3_out, button_4_out, button_5_out, button_6_out, button_7_out,
       button_8_out, button_9_out, button_10_out, button_11_out, button_12_out, button_13_out, button_14_out,
       button_15_out, clock_1_out, counter_14_1_clk_a, d_ff_1_q, d_ff_2_q, d_ff_3_q, d_ff_4_q, d_ff_5_q,
       d_ff_6_q, d_ff_7_q, d_ff_8_q, d_ff_9_q, d_ff_10_q, d_ff_11_q, d_ff_12_q, d_ff_13_q, d_ff_14_q,
       d_ff_15_q, d_ff_16_q, d_ff_17_q, d_ff_18_q, d_ff_19_q, d_ff_20_q, d_ff_21_q, d_ff_22_q, d_ff_23_q,
       d_ff_24_q, d_ff_25_q, d_ff_26_q, d_ff_27_q, d_ff_28_q, d_ff_29_q, d_ff_30_q, d_ff_31_q, d_ff_32_q,
       d_ff_33_q, d_ff_34_q, d_ff_35_q, d_ff_36_q, d_ff_37_q, d_ff_38_q, d_ff_39_q, d_ff_40_q, d_ff_41_q,
       d_ff_42_q, d_ff_43_q, d_ff_44_q, d_ff_45_q, d_ff_46_q, d_ff_47_q, d_ff_48_q, d_ff_49_q, d_ff_50_q,
       d_ff_51_q, d_ff_52_q, d_ff_53_q, d_ff_54_q, d_ff_55_q, d_ff_56_q, d_ff_57_q, d_ff_58_q, d_ff_59_q,
       d_ff_60_q, d_ff_61_q, d_ff_62_q, d_ff_63_q, d_ff_64_q, d_ff_65_q, d_ff_66_q, d_ff_67_q, d_ff_68_q,
       d_ff_69_q, d_ff_70_q, d_ff_71_q, d_ff_72_q, d_ff_73_q, d_ff_74_q, d_ff_75_q, d_ff_76_q, d_ff_77_q,
       d_ff_78_q, d_ff_79_q, d_ff_80_q, d_ff_81_q, d_ff_82_q, d_ff_83_q, d_ff_84_q, d_ff_85_q, d_ff_86_q,
       d_ff_87_q, d_ff_88_q, d_ff_89_q, d_ff_90_q, d_ff_91_q, d_ff_92_q, d_ff_93_q, d_ff_94_q, d_ff_95_q,
       d_ff_96_q, d_ff_97_q, d_ff_98_q, d_ff_99_q, d_ff_100_q, d_ff_101_q, d_ff_102_q, d_ff_103_q,
       d_ff_104_q, d_ff_105_q, d_ff_106_q, d_ff_107_q, d_ff_108_q, d_ff_109_q, d_ff_110_q, d_ff_111_q,
       d_ff_112_q, d_ff_113_q, d_ff_114_q, d_ff_115_q, d_ff_116_q, d_ff_117_q, d_ff_118_q, d_ff_119_q,
       d_ff_120_q, d_ff_121_q, d_ff_122_q, d_ff_123_q, d_ff_124_q, d_ff_125_q, d_ff_126_q, d_ff_127_q,
       d_ff_128_q, d_ff_129_q, d_ff_130_q, d_ff_131_q, d_ff_132_q, d_ff_133_q, d_ff_134_q, d_ff_135_q,
       d_ff_136_q, d_ff_137_q, d_ff_138_q, d_ff_139_q, d_ff_140_q, d_ff_141_q, d_ff_142_q, d_ff_143_q,
       d_ff_144_q, d_ff_145_q, d_ff_146_q, d_ff_147_q, d_ff_148_q, d_ff_149_q, d_ff_150_q, d_ff_151_q,
       d_ff_152_q, d_ff_153_q, d_ff_154_q, d_ff_155_q, d_ff_156_q, d_ff_157_q, d_ff_158_q, d_ff_159_q,
       d_ff_160_q, d_ff_161_q, d_ff_162_q, d_ff_163_q, d_ff_164_q, d_ff_165_q, d_ff_166_q, d_ff_167_q,
       d_ff_168_q, d_ff_169_q, d_ff_170_q, d_ff_171_q, d_ff_172_q, d_ff_173_q, d_ff_174_q, d_ff_175_q,
       d_ff_176_q, d_ff_177_q, d_ff_178_q, d_ff_179_q, d_ff_180_q, d_ff_181_q, d_ff_182_q, d_ff_183_q,
       d_ff_184_q, d_ff_185_q, d_ff_186_q, d_ff_187_q, d_ff_188_q, d_ff_189_q, d_ff_190_q, d_ff_191_q,
       d_ff_192_q, d_ff_193_q, d_ff_194_q, d_ff_195_q, d_ff_196_q, d_ff_197_q, d_ff_198_q, d_ff_199_q,
       d_ff_200_q, d_ff_201_q, d_ff_202_q, d_ff_203_q, d_ff_204_q, d_ff_205_q, d_ff_206_q, d_ff_207_q,
       d_ff_208_q, d_ff_209_q, d_ff_210_q, d_ff_211_q, d_ff_212_q, d_ff_213_q, d_ff_214_q, d_ff_215_q,
       d_ff_216_q, d_ff_217_q, d_ff_218_q, d_ff_219_q, d_ff_220_q, d_ff_221_q, d_ff_222_q, d_ff_223_q,
       d_ff_224_q, d_ff_225_q, d_ff_226_q, d_ff_227_q, d_ff_228_q, d_ff_229_q, d_ff_230_q, d_ff_231_q,
       d_ff_232_q, d_ff_233_q, d_ff_234_q, d_ff_235_q, d_ff_236_q, d_ff_237_q, d_ff_238_q, d_ff_239_q,
       decoder_1_out0, decoder_1_out1, decoder_1_out2, decoder_1_out3, decoder_1_out4, decoder_1_out5,
       decoder_1_out6, decoder_1_out7, decoder_1_out8, decoder_1_out9, decoder_1_out10, decoder_1_out11,
       decoder_1_out12, decoder_1_out13, decoder_1_out14, decoder_1_out15, dipswitch_2_sw1;
  wire [3:0] dipswitch_1_p4;

  Button button_1 (.out(button_1_out));
  D_Flip_Flop d_ff_1 (.clk(and_1_out), .Q(d_ff_1_q), .preset(button_1_out));  // open: D, Qn, reset
  Button button_2 (.out(button_2_out));
  Clock clock_1 (.out(clock_1_out));
  Button button_3 (.out(button_3_out));
  Button button_4 (.out(button_4_out));
  Button button_5 (.out(button_5_out));
  Button button_6 (.out(button_6_out));
  D_Flip_Flop d_ff_2 (.D(d_ff_1_q), .clk(and_1_out), .Q(d_ff_2_q), .preset(button_3_out));  // open: Qn, reset
  Button button_7 (.out(button_7_out));
  Button button_8 (.out(button_8_out));
  Button button_9 (.out(button_9_out));
  Button button_10 (.out(button_10_out));
  D_Flip_Flop d_ff_3 (.D(d_ff_2_q), .clk(and_1_out), .Q(d_ff_3_q), .preset(button_4_out));  // open: Qn, reset
  // DipSwitch dipswitch_1: pin names not known; wires that end beside it: dipswitch_1_p4[3], dipswitch_1_p4[2], dipswitch_1_p4[1], dipswitch_1_p4[0]
  DipSwitch #(.number(1)) dipswitch_2 (.sw1(dipswitch_2_sw1));
  Button button_11 (.out(button_11_out));
  Button button_12 (.out(button_12_out));
  Button button_13 (.out(button_13_out));
  Button button_14 (.out(button_14_out));
  D_Flip_Flop d_ff_4 (.D(d_ff_3_q), .clk(and_1_out), .Q(d_ff_4_q), .preset(button_5_out));  // open: Qn, reset
  Button button_15 (.out(button_15_out));
  D_Flip_Flop d_ff_5 (.D(d_ff_4_q), .clk(and_1_out), .Q(d_ff_5_q), .preset(button_6_out));  // open: Qn, reset
  Decoder #(.select(4)) decoder_1 (
    .out0(decoder_1_out0), .out1(decoder_1_out1), .out2(decoder_1_out2), .out3(decoder_1_out3),
    .out4(decoder_1_out4), .out5(decoder_1_out5), .out6(decoder_1_out6), .out7(decoder_1_out7),
    .out8(decoder_1_out8), .out9(decoder_1_out9), .out10(decoder_1_out10), .out11(decoder_1_out11),
    .out12(decoder_1_out12), .out13(decoder_1_out13), .out14(decoder_1_out14), .out15(decoder_1_out15),
    .sel(dipswitch_1_p4), .en(dipswitch_2_sw1));
  counter_14 counter_14_1 (.start(button_2_out), .CLK(clock_1_out), .CLK_A(counter_14_1_clk_a));
  and and_1 (and_1_out, counter_14_1_clk_a, clock_1_out);
  D_Flip_Flop d_ff_6 (.D(d_ff_5_q), .clk(and_1_out), .Q(d_ff_6_q), .preset(button_7_out));  // open: Qn, reset
  D_Flip_Flop d_ff_7 (.D(d_ff_6_q), .clk(and_1_out), .Q(d_ff_7_q), .preset(button_8_out));  // open: Qn, reset
  D_Flip_Flop d_ff_8 (.D(d_ff_7_q), .clk(and_1_out), .Q(d_ff_8_q), .preset(button_9_out));  // open: Qn, reset
  D_Flip_Flop d_ff_9 (.D(d_ff_8_q), .clk(and_1_out), .Q(d_ff_9_q), .preset(button_10_out));  // open: Qn, reset
  D_Flip_Flop d_ff_10 (.D(d_ff_9_q), .clk(and_1_out), .Q(d_ff_10_q), .preset(button_11_out));  // open: Qn, reset
  D_Flip_Flop d_ff_11 (.D(d_ff_10_q), .clk(and_1_out), .Q(d_ff_11_q), .preset(button_12_out));  // open: Qn, reset
  D_Flip_Flop d_ff_12 (.D(d_ff_11_q), .clk(and_1_out), .Q(d_ff_12_q), .preset(button_13_out));  // open: Qn, reset
  D_Flip_Flop d_ff_13 (.D(d_ff_12_q), .clk(and_1_out), .Q(d_ff_13_q), .preset(button_14_out));  // open: Qn, reset
  D_Flip_Flop d_ff_14 (.D(d_ff_13_q), .clk(and_1_out), .Q(d_ff_14_q), .preset(button_15_out));  // open: Qn, reset
  D_Flip_Flop d_ff_15 (.D(d_ff_14_q), .clk(and_1_out), .Q(d_ff_15_q));  // open: Qn, preset, reset
  and and_2 (and_2_out, d_ff_15_q, decoder_1_out0);
  and and_3 (and_3_out, and_1_out, decoder_1_out0);
  and and_4 (and_4_out, d_ff_15_q, decoder_1_out1);
  and and_5 (and_5_out, and_1_out, decoder_1_out1);
  and and_6 (and_6_out, d_ff_15_q, decoder_1_out2);
  and and_7 (and_7_out, and_1_out, decoder_1_out2);
  and and_8 (and_8_out, d_ff_15_q, decoder_1_out3);
  and and_9 (and_9_out, and_1_out, decoder_1_out3);
  and and_10 (and_10_out, d_ff_15_q, decoder_1_out4);
  and and_11 (and_11_out, and_1_out, decoder_1_out4);
  and and_12 (and_12_out, d_ff_15_q, decoder_1_out5);
  and and_13 (and_13_out, and_1_out, decoder_1_out5);
  and and_14 (and_14_out, d_ff_15_q, decoder_1_out6);
  and and_15 (and_15_out, and_1_out, decoder_1_out6);
  and and_16 (and_16_out, d_ff_15_q, decoder_1_out7);
  and and_17 (and_17_out, and_1_out, decoder_1_out7);
  and and_18 (and_18_out, d_ff_15_q, decoder_1_out8);
  and and_19 (and_19_out, and_1_out, decoder_1_out8);
  and and_20 (and_20_out, d_ff_15_q, decoder_1_out9);
  and and_21 (and_21_out, and_1_out, decoder_1_out9);
  and and_22 (and_22_out, d_ff_15_q, decoder_1_out10);
  and and_23 (and_23_out, and_1_out, decoder_1_out10);
  and and_24 (and_24_out, d_ff_15_q, decoder_1_out11);
  and and_25 (and_25_out, and_1_out, decoder_1_out11);
  and and_26 (and_26_out, d_ff_15_q, decoder_1_out12);
  and and_27 (and_27_out, and_1_out, decoder_1_out12);
  and and_28 (and_28_out, d_ff_15_q, decoder_1_out13);
  and and_29 (and_29_out, and_1_out, decoder_1_out13);
  and and_30 (and_30_out, d_ff_15_q, decoder_1_out14);
  and and_31 (and_31_out, and_1_out, decoder_1_out14);
  and and_32 (and_32_out, d_ff_15_q, decoder_1_out15);
  and and_33 (and_33_out, and_1_out, decoder_1_out15);
  D_Flip_Flop d_ff_16 (.D(and_2_out), .clk(and_3_out), .Q(d_ff_16_q));  // open: Qn, preset, reset
  D_Flip_Flop d_ff_17 (.D(and_4_out), .clk(and_5_out), .Q(d_ff_17_q));  // open: Qn, preset, reset
  D_Flip_Flop d_ff_18 (.D(and_6_out), .clk(and_7_out), .Q(d_ff_18_q));  // open: Qn, preset, reset
  D_Flip_Flop d_ff_19 (.D(and_8_out), .clk(and_9_out), .Q(d_ff_19_q));  // open: Qn, preset, reset
  D_Flip_Flop d_ff_20 (.D(and_10_out), .clk(and_11_out), .Q(d_ff_20_q));  // open: Qn, preset, reset
  D_Flip_Flop d_ff_21 (.D(and_12_out), .clk(and_13_out), .Q(d_ff_21_q));  // open: Qn, preset, reset
  D_Flip_Flop d_ff_22 (.D(and_14_out), .clk(and_15_out), .Q(d_ff_22_q));  // open: Qn, preset, reset
  D_Flip_Flop d_ff_23 (.D(and_16_out), .clk(and_17_out), .Q(d_ff_23_q));  // open: Qn, preset, reset
  D_Flip_Flop d_ff_24 (.D(and_18_out), .clk(and_19_out), .Q(d_ff_24_q));  // open: Qn, preset, reset
  D_Flip_Flop d_ff_25 (.D(and_20_out), .clk(and_21_out), .Q(d_ff_25_q));  // open: Qn, preset, reset
  D_Flip_Flop d_ff_26 (.D(and_22_out), .clk(and_23_out), .Q(d_ff_26_q));  // open: Qn, preset, reset
  D_Flip_Flop d_ff_27 (.D(and_24_out), .clk(and_25_out), .Q(d_ff_27_q));  // open: Qn, preset, reset
  D_Flip_Flop d_ff_28 (.D(and_26_out), .clk(and_27_out), .Q(d_ff_28_q));  // open: Qn, preset, reset
  D_Flip_Flop d_ff_29 (.D(and_28_out), .clk(and_29_out), .Q(d_ff_29_q));  // open: Qn, preset, reset
  D_Flip_Flop d_ff_30 (.D(and_30_out), .clk(and_31_out), .Q(d_ff_30_q));  // open: Qn, preset, reset
  D_Flip_Flop d_ff_31 (.D(and_32_out), .clk(and_33_out), .Q(d_ff_31_q));  // open: Qn, preset, reset
  D_Flip_Flop d_ff_32 (.D(d_ff_16_q), .clk(and_3_out), .Q(d_ff_32_q));  // open: Qn, preset, reset
  D_Flip_Flop d_ff_33 (.D(d_ff_17_q), .clk(and_5_out), .Q(d_ff_33_q));  // open: Qn, preset, reset
  D_Flip_Flop d_ff_34 (.D(d_ff_18_q), .clk(and_7_out), .Q(d_ff_34_q));  // open: Qn, preset, reset
  D_Flip_Flop d_ff_35 (.D(d_ff_19_q), .clk(and_9_out), .Q(d_ff_35_q));  // open: Qn, preset, reset
  D_Flip_Flop d_ff_36 (.D(d_ff_20_q), .clk(and_11_out), .Q(d_ff_36_q));  // open: Qn, preset, reset
  D_Flip_Flop d_ff_37 (.D(d_ff_21_q), .clk(and_13_out), .Q(d_ff_37_q));  // open: Qn, preset, reset
  D_Flip_Flop d_ff_38 (.D(d_ff_22_q), .clk(and_15_out), .Q(d_ff_38_q));  // open: Qn, preset, reset
  D_Flip_Flop d_ff_39 (.D(d_ff_23_q), .clk(and_17_out), .Q(d_ff_39_q));  // open: Qn, preset, reset
  D_Flip_Flop d_ff_40 (.D(d_ff_24_q), .clk(and_19_out), .Q(d_ff_40_q));  // open: Qn, preset, reset
  D_Flip_Flop d_ff_41 (.D(d_ff_25_q), .clk(and_21_out), .Q(d_ff_41_q));  // open: Qn, preset, reset
  D_Flip_Flop d_ff_42 (.D(d_ff_26_q), .clk(and_23_out), .Q(d_ff_42_q));  // open: Qn, preset, reset
  D_Flip_Flop d_ff_43 (.D(d_ff_27_q), .clk(and_25_out), .Q(d_ff_43_q));  // open: Qn, preset, reset
  D_Flip_Flop d_ff_44 (.D(d_ff_28_q), .clk(and_27_out), .Q(d_ff_44_q));  // open: Qn, preset, reset
  D_Flip_Flop d_ff_45 (.D(d_ff_29_q), .clk(and_29_out), .Q(d_ff_45_q));  // open: Qn, preset, reset
  D_Flip_Flop d_ff_46 (.D(d_ff_30_q), .clk(and_31_out), .Q(d_ff_46_q));  // open: Qn, preset, reset
  D_Flip_Flop d_ff_47 (.D(d_ff_31_q), .clk(and_33_out), .Q(d_ff_47_q));  // open: Qn, preset, reset
  D_Flip_Flop d_ff_48 (.D(d_ff_32_q), .clk(and_3_out), .Q(d_ff_48_q));  // open: Qn, preset, reset
  D_Flip_Flop d_ff_49 (.D(d_ff_33_q), .clk(and_5_out), .Q(d_ff_49_q));  // open: Qn, preset, reset
  D_Flip_Flop d_ff_50 (.D(d_ff_34_q), .clk(and_7_out), .Q(d_ff_50_q));  // open: Qn, preset, reset
  D_Flip_Flop d_ff_51 (.D(d_ff_35_q), .clk(and_9_out), .Q(d_ff_51_q));  // open: Qn, preset, reset
  D_Flip_Flop d_ff_52 (.D(d_ff_36_q), .clk(and_11_out), .Q(d_ff_52_q));  // open: Qn, preset, reset
  D_Flip_Flop d_ff_53 (.D(d_ff_37_q), .clk(and_13_out), .Q(d_ff_53_q));  // open: Qn, preset, reset
  D_Flip_Flop d_ff_54 (.D(d_ff_38_q), .clk(and_15_out), .Q(d_ff_54_q));  // open: Qn, preset, reset
  D_Flip_Flop d_ff_55 (.D(d_ff_39_q), .clk(and_17_out), .Q(d_ff_55_q));  // open: Qn, preset, reset
  D_Flip_Flop d_ff_56 (.D(d_ff_40_q), .clk(and_19_out), .Q(d_ff_56_q));  // open: Qn, preset, reset
  D_Flip_Flop d_ff_57 (.D(d_ff_41_q), .clk(and_21_out), .Q(d_ff_57_q));  // open: Qn, preset, reset
  D_Flip_Flop d_ff_58 (.D(d_ff_42_q), .clk(and_23_out), .Q(d_ff_58_q));  // open: Qn, preset, reset
  D_Flip_Flop d_ff_59 (.D(d_ff_43_q), .clk(and_25_out), .Q(d_ff_59_q));  // open: Qn, preset, reset
  D_Flip_Flop d_ff_60 (.D(d_ff_44_q), .clk(and_27_out), .Q(d_ff_60_q));  // open: Qn, preset, reset
  D_Flip_Flop d_ff_61 (.D(d_ff_45_q), .clk(and_29_out), .Q(d_ff_61_q));  // open: Qn, preset, reset
  D_Flip_Flop d_ff_62 (.D(d_ff_46_q), .clk(and_31_out), .Q(d_ff_62_q));  // open: Qn, preset, reset
  D_Flip_Flop d_ff_63 (.D(d_ff_47_q), .clk(and_33_out), .Q(d_ff_63_q));  // open: Qn, preset, reset
  D_Flip_Flop d_ff_64 (.D(d_ff_48_q), .clk(and_3_out), .Q(d_ff_64_q));  // open: Qn, preset, reset
  D_Flip_Flop d_ff_65 (.D(d_ff_49_q), .clk(and_5_out), .Q(d_ff_65_q));  // open: Qn, preset, reset
  D_Flip_Flop d_ff_66 (.D(d_ff_50_q), .clk(and_7_out), .Q(d_ff_66_q));  // open: Qn, preset, reset
  D_Flip_Flop d_ff_67 (.D(d_ff_51_q), .clk(and_9_out), .Q(d_ff_67_q));  // open: Qn, preset, reset
  D_Flip_Flop d_ff_68 (.D(d_ff_52_q), .clk(and_11_out), .Q(d_ff_68_q));  // open: Qn, preset, reset
  D_Flip_Flop d_ff_69 (.D(d_ff_53_q), .clk(and_13_out), .Q(d_ff_69_q));  // open: Qn, preset, reset
  D_Flip_Flop d_ff_70 (.D(d_ff_54_q), .clk(and_15_out), .Q(d_ff_70_q));  // open: Qn, preset, reset
  D_Flip_Flop d_ff_71 (.D(d_ff_55_q), .clk(and_17_out), .Q(d_ff_71_q));  // open: Qn, preset, reset
  D_Flip_Flop d_ff_72 (.D(d_ff_56_q), .clk(and_19_out), .Q(d_ff_72_q));  // open: Qn, preset, reset
  D_Flip_Flop d_ff_73 (.D(d_ff_57_q), .clk(and_21_out), .Q(d_ff_73_q));  // open: Qn, preset, reset
  D_Flip_Flop d_ff_74 (.D(d_ff_58_q), .clk(and_23_out), .Q(d_ff_74_q));  // open: Qn, preset, reset
  D_Flip_Flop d_ff_75 (.D(d_ff_59_q), .clk(and_25_out), .Q(d_ff_75_q));  // open: Qn, preset, reset
  D_Flip_Flop d_ff_76 (.D(d_ff_60_q), .clk(and_27_out), .Q(d_ff_76_q));  // open: Qn, preset, reset
  D_Flip_Flop d_ff_77 (.D(d_ff_61_q), .clk(and_29_out), .Q(d_ff_77_q));  // open: Qn, preset, reset
  D_Flip_Flop d_ff_78 (.D(d_ff_62_q), .clk(and_31_out), .Q(d_ff_78_q));  // open: Qn, preset, reset
  D_Flip_Flop d_ff_79 (.D(d_ff_63_q), .clk(and_33_out), .Q(d_ff_79_q));  // open: Qn, preset, reset
  D_Flip_Flop d_ff_80 (.D(d_ff_64_q), .clk(and_3_out), .Q(d_ff_80_q));  // open: Qn, preset, reset
  D_Flip_Flop d_ff_81 (.D(d_ff_65_q), .clk(and_5_out), .Q(d_ff_81_q));  // open: Qn, preset, reset
  D_Flip_Flop d_ff_82 (.D(d_ff_66_q), .clk(and_7_out), .Q(d_ff_82_q));  // open: Qn, preset, reset
  D_Flip_Flop d_ff_83 (.D(d_ff_67_q), .clk(and_9_out), .Q(d_ff_83_q));  // open: Qn, preset, reset
  D_Flip_Flop d_ff_84 (.D(d_ff_68_q), .clk(and_11_out), .Q(d_ff_84_q));  // open: Qn, preset, reset
  D_Flip_Flop d_ff_85 (.D(d_ff_69_q), .clk(and_13_out), .Q(d_ff_85_q));  // open: Qn, preset, reset
  D_Flip_Flop d_ff_86 (.D(d_ff_70_q), .clk(and_15_out), .Q(d_ff_86_q));  // open: Qn, preset, reset
  D_Flip_Flop d_ff_87 (.D(d_ff_71_q), .clk(and_17_out), .Q(d_ff_87_q));  // open: Qn, preset, reset
  D_Flip_Flop d_ff_88 (.D(d_ff_72_q), .clk(and_19_out), .Q(d_ff_88_q));  // open: Qn, preset, reset
  D_Flip_Flop d_ff_89 (.D(d_ff_73_q), .clk(and_21_out), .Q(d_ff_89_q));  // open: Qn, preset, reset
  D_Flip_Flop d_ff_90 (.D(d_ff_74_q), .clk(and_23_out), .Q(d_ff_90_q));  // open: Qn, preset, reset
  D_Flip_Flop d_ff_91 (.D(d_ff_75_q), .clk(and_25_out), .Q(d_ff_91_q));  // open: Qn, preset, reset
  D_Flip_Flop d_ff_92 (.D(d_ff_76_q), .clk(and_27_out), .Q(d_ff_92_q));  // open: Qn, preset, reset
  D_Flip_Flop d_ff_93 (.D(d_ff_77_q), .clk(and_29_out), .Q(d_ff_93_q));  // open: Qn, preset, reset
  D_Flip_Flop d_ff_94 (.D(d_ff_78_q), .clk(and_31_out), .Q(d_ff_94_q));  // open: Qn, preset, reset
  D_Flip_Flop d_ff_95 (.D(d_ff_79_q), .clk(and_33_out), .Q(d_ff_95_q));  // open: Qn, preset, reset
  D_Flip_Flop d_ff_96 (.D(d_ff_80_q), .clk(and_3_out), .Q(d_ff_96_q));  // open: Qn, preset, reset
  D_Flip_Flop d_ff_97 (.D(d_ff_81_q), .clk(and_5_out), .Q(d_ff_97_q));  // open: Qn, preset, reset
  D_Flip_Flop d_ff_98 (.D(d_ff_82_q), .clk(and_7_out), .Q(d_ff_98_q));  // open: Qn, preset, reset
  D_Flip_Flop d_ff_99 (.D(d_ff_83_q), .clk(and_9_out), .Q(d_ff_99_q));  // open: Qn, preset, reset
  D_Flip_Flop d_ff_100 (.D(d_ff_84_q), .clk(and_11_out), .Q(d_ff_100_q));  // open: Qn, preset, reset
  D_Flip_Flop d_ff_101 (.D(d_ff_85_q), .clk(and_13_out), .Q(d_ff_101_q));  // open: Qn, preset, reset
  D_Flip_Flop d_ff_102 (.D(d_ff_86_q), .clk(and_15_out), .Q(d_ff_102_q));  // open: Qn, preset, reset
  D_Flip_Flop d_ff_103 (.D(d_ff_87_q), .clk(and_17_out), .Q(d_ff_103_q));  // open: Qn, preset, reset
  D_Flip_Flop d_ff_104 (.D(d_ff_88_q), .clk(and_19_out), .Q(d_ff_104_q));  // open: Qn, preset, reset
  D_Flip_Flop d_ff_105 (.D(d_ff_89_q), .clk(and_21_out), .Q(d_ff_105_q));  // open: Qn, preset, reset
  D_Flip_Flop d_ff_106 (.D(d_ff_90_q), .clk(and_23_out), .Q(d_ff_106_q));  // open: Qn, preset, reset
  D_Flip_Flop d_ff_107 (.D(d_ff_91_q), .clk(and_25_out), .Q(d_ff_107_q));  // open: Qn, preset, reset
  D_Flip_Flop d_ff_108 (.D(d_ff_92_q), .clk(and_27_out), .Q(d_ff_108_q));  // open: Qn, preset, reset
  D_Flip_Flop d_ff_109 (.D(d_ff_93_q), .clk(and_29_out), .Q(d_ff_109_q));  // open: Qn, preset, reset
  D_Flip_Flop d_ff_110 (.D(d_ff_94_q), .clk(and_31_out), .Q(d_ff_110_q));  // open: Qn, preset, reset
  D_Flip_Flop d_ff_111 (.D(d_ff_95_q), .clk(and_33_out), .Q(d_ff_111_q));  // open: Qn, preset, reset
  D_Flip_Flop d_ff_112 (.D(d_ff_96_q), .clk(and_3_out), .Q(d_ff_112_q));  // open: Qn, preset, reset
  D_Flip_Flop d_ff_113 (.D(d_ff_97_q), .clk(and_5_out), .Q(d_ff_113_q));  // open: Qn, preset, reset
  D_Flip_Flop d_ff_114 (.D(d_ff_98_q), .clk(and_7_out), .Q(d_ff_114_q));  // open: Qn, preset, reset
  D_Flip_Flop d_ff_115 (.D(d_ff_99_q), .clk(and_9_out), .Q(d_ff_115_q));  // open: Qn, preset, reset
  D_Flip_Flop d_ff_116 (.D(d_ff_100_q), .clk(and_11_out), .Q(d_ff_116_q));  // open: Qn, preset, reset
  D_Flip_Flop d_ff_117 (.D(d_ff_101_q), .clk(and_13_out), .Q(d_ff_117_q));  // open: Qn, preset, reset
  D_Flip_Flop d_ff_118 (.D(d_ff_102_q), .clk(and_15_out), .Q(d_ff_118_q));  // open: Qn, preset, reset
  D_Flip_Flop d_ff_119 (.D(d_ff_103_q), .clk(and_17_out), .Q(d_ff_119_q));  // open: Qn, preset, reset
  D_Flip_Flop d_ff_120 (.D(d_ff_104_q), .clk(and_19_out), .Q(d_ff_120_q));  // open: Qn, preset, reset
  D_Flip_Flop d_ff_121 (.D(d_ff_105_q), .clk(and_21_out), .Q(d_ff_121_q));  // open: Qn, preset, reset
  D_Flip_Flop d_ff_122 (.D(d_ff_106_q), .clk(and_23_out), .Q(d_ff_122_q));  // open: Qn, preset, reset
  D_Flip_Flop d_ff_123 (.D(d_ff_107_q), .clk(and_25_out), .Q(d_ff_123_q));  // open: Qn, preset, reset
  D_Flip_Flop d_ff_124 (.D(d_ff_108_q), .clk(and_27_out), .Q(d_ff_124_q));  // open: Qn, preset, reset
  D_Flip_Flop d_ff_125 (.D(d_ff_109_q), .clk(and_29_out), .Q(d_ff_125_q));  // open: Qn, preset, reset
  D_Flip_Flop d_ff_126 (.D(d_ff_110_q), .clk(and_31_out), .Q(d_ff_126_q));  // open: Qn, preset, reset
  D_Flip_Flop d_ff_127 (.D(d_ff_111_q), .clk(and_33_out), .Q(d_ff_127_q));  // open: Qn, preset, reset
  D_Flip_Flop d_ff_128 (.D(d_ff_112_q), .clk(and_3_out), .Q(d_ff_128_q));  // open: Qn, preset, reset
  D_Flip_Flop d_ff_129 (.D(d_ff_113_q), .clk(and_5_out), .Q(d_ff_129_q));  // open: Qn, preset, reset
  D_Flip_Flop d_ff_130 (.D(d_ff_114_q), .clk(and_7_out), .Q(d_ff_130_q));  // open: Qn, preset, reset
  D_Flip_Flop d_ff_131 (.D(d_ff_115_q), .clk(and_9_out), .Q(d_ff_131_q));  // open: Qn, preset, reset
  D_Flip_Flop d_ff_132 (.D(d_ff_116_q), .clk(and_11_out), .Q(d_ff_132_q));  // open: Qn, preset, reset
  D_Flip_Flop d_ff_133 (.D(d_ff_117_q), .clk(and_13_out), .Q(d_ff_133_q));  // open: Qn, preset, reset
  D_Flip_Flop d_ff_134 (.D(d_ff_118_q), .clk(and_15_out), .Q(d_ff_134_q));  // open: Qn, preset, reset
  D_Flip_Flop d_ff_135 (.D(d_ff_119_q), .clk(and_17_out), .Q(d_ff_135_q));  // open: Qn, preset, reset
  D_Flip_Flop d_ff_136 (.D(d_ff_120_q), .clk(and_19_out), .Q(d_ff_136_q));  // open: Qn, preset, reset
  D_Flip_Flop d_ff_137 (.D(d_ff_121_q), .clk(and_21_out), .Q(d_ff_137_q));  // open: Qn, preset, reset
  D_Flip_Flop d_ff_138 (.D(d_ff_122_q), .clk(and_23_out), .Q(d_ff_138_q));  // open: Qn, preset, reset
  D_Flip_Flop d_ff_139 (.D(d_ff_123_q), .clk(and_25_out), .Q(d_ff_139_q));  // open: Qn, preset, reset
  D_Flip_Flop d_ff_140 (.D(d_ff_124_q), .clk(and_27_out), .Q(d_ff_140_q));  // open: Qn, preset, reset
  D_Flip_Flop d_ff_141 (.D(d_ff_125_q), .clk(and_29_out), .Q(d_ff_141_q));  // open: Qn, preset, reset
  D_Flip_Flop d_ff_142 (.D(d_ff_126_q), .clk(and_31_out), .Q(d_ff_142_q));  // open: Qn, preset, reset
  D_Flip_Flop d_ff_143 (.D(d_ff_127_q), .clk(and_33_out), .Q(d_ff_143_q));  // open: Qn, preset, reset
  D_Flip_Flop d_ff_144 (.D(d_ff_128_q), .clk(and_3_out), .Q(d_ff_144_q));  // open: Qn, preset, reset
  D_Flip_Flop d_ff_145 (.D(d_ff_129_q), .clk(and_5_out), .Q(d_ff_145_q));  // open: Qn, preset, reset
  D_Flip_Flop d_ff_146 (.D(d_ff_130_q), .clk(and_7_out), .Q(d_ff_146_q));  // open: Qn, preset, reset
  D_Flip_Flop d_ff_147 (.D(d_ff_131_q), .clk(and_9_out), .Q(d_ff_147_q));  // open: Qn, preset, reset
  D_Flip_Flop d_ff_148 (.D(d_ff_132_q), .clk(and_11_out), .Q(d_ff_148_q));  // open: Qn, preset, reset
  D_Flip_Flop d_ff_149 (.D(d_ff_133_q), .clk(and_13_out), .Q(d_ff_149_q));  // open: Qn, preset, reset
  D_Flip_Flop d_ff_150 (.D(d_ff_134_q), .clk(and_15_out), .Q(d_ff_150_q));  // open: Qn, preset, reset
  D_Flip_Flop d_ff_151 (.D(d_ff_135_q), .clk(and_17_out), .Q(d_ff_151_q));  // open: Qn, preset, reset
  D_Flip_Flop d_ff_152 (.D(d_ff_136_q), .clk(and_19_out), .Q(d_ff_152_q));  // open: Qn, preset, reset
  D_Flip_Flop d_ff_153 (.D(d_ff_137_q), .clk(and_21_out), .Q(d_ff_153_q));  // open: Qn, preset, reset
  D_Flip_Flop d_ff_154 (.D(d_ff_138_q), .clk(and_23_out), .Q(d_ff_154_q));  // open: Qn, preset, reset
  D_Flip_Flop d_ff_155 (.D(d_ff_139_q), .clk(and_25_out), .Q(d_ff_155_q));  // open: Qn, preset, reset
  D_Flip_Flop d_ff_156 (.D(d_ff_140_q), .clk(and_27_out), .Q(d_ff_156_q));  // open: Qn, preset, reset
  D_Flip_Flop d_ff_157 (.D(d_ff_141_q), .clk(and_29_out), .Q(d_ff_157_q));  // open: Qn, preset, reset
  D_Flip_Flop d_ff_158 (.D(d_ff_142_q), .clk(and_31_out), .Q(d_ff_158_q));  // open: Qn, preset, reset
  D_Flip_Flop d_ff_159 (.D(d_ff_143_q), .clk(and_33_out), .Q(d_ff_159_q));  // open: Qn, preset, reset
  D_Flip_Flop d_ff_160 (.D(d_ff_144_q), .clk(and_3_out), .Q(d_ff_160_q));  // open: Qn, preset, reset
  D_Flip_Flop d_ff_161 (.D(d_ff_145_q), .clk(and_5_out), .Q(d_ff_161_q));  // open: Qn, preset, reset
  D_Flip_Flop d_ff_162 (.D(d_ff_146_q), .clk(and_7_out), .Q(d_ff_162_q));  // open: Qn, preset, reset
  D_Flip_Flop d_ff_163 (.D(d_ff_147_q), .clk(and_9_out), .Q(d_ff_163_q));  // open: Qn, preset, reset
  D_Flip_Flop d_ff_164 (.D(d_ff_148_q), .clk(and_11_out), .Q(d_ff_164_q));  // open: Qn, preset, reset
  D_Flip_Flop d_ff_165 (.D(d_ff_149_q), .clk(and_13_out), .Q(d_ff_165_q));  // open: Qn, preset, reset
  D_Flip_Flop d_ff_166 (.D(d_ff_150_q), .clk(and_15_out), .Q(d_ff_166_q));  // open: Qn, preset, reset
  D_Flip_Flop d_ff_167 (.D(d_ff_151_q), .clk(and_17_out), .Q(d_ff_167_q));  // open: Qn, preset, reset
  D_Flip_Flop d_ff_168 (.D(d_ff_152_q), .clk(and_19_out), .Q(d_ff_168_q));  // open: Qn, preset, reset
  D_Flip_Flop d_ff_169 (.D(d_ff_153_q), .clk(and_21_out), .Q(d_ff_169_q));  // open: Qn, preset, reset
  D_Flip_Flop d_ff_170 (.D(d_ff_154_q), .clk(and_23_out), .Q(d_ff_170_q));  // open: Qn, preset, reset
  D_Flip_Flop d_ff_171 (.D(d_ff_155_q), .clk(and_25_out), .Q(d_ff_171_q));  // open: Qn, preset, reset
  D_Flip_Flop d_ff_172 (.D(d_ff_156_q), .clk(and_27_out), .Q(d_ff_172_q));  // open: Qn, preset, reset
  D_Flip_Flop d_ff_173 (.D(d_ff_157_q), .clk(and_29_out), .Q(d_ff_173_q));  // open: Qn, preset, reset
  D_Flip_Flop d_ff_174 (.D(d_ff_158_q), .clk(and_31_out), .Q(d_ff_174_q));  // open: Qn, preset, reset
  D_Flip_Flop d_ff_175 (.D(d_ff_159_q), .clk(and_33_out), .Q(d_ff_175_q));  // open: Qn, preset, reset
  D_Flip_Flop d_ff_176 (.D(d_ff_160_q), .clk(and_3_out), .Q(d_ff_176_q));  // open: Qn, preset, reset
  D_Flip_Flop d_ff_177 (.D(d_ff_161_q), .clk(and_5_out), .Q(d_ff_177_q));  // open: Qn, preset, reset
  D_Flip_Flop d_ff_178 (.D(d_ff_162_q), .clk(and_7_out), .Q(d_ff_178_q));  // open: Qn, preset, reset
  D_Flip_Flop d_ff_179 (.D(d_ff_163_q), .clk(and_9_out), .Q(d_ff_179_q));  // open: Qn, preset, reset
  D_Flip_Flop d_ff_180 (.D(d_ff_164_q), .clk(and_11_out), .Q(d_ff_180_q));  // open: Qn, preset, reset
  D_Flip_Flop d_ff_181 (.D(d_ff_165_q), .clk(and_13_out), .Q(d_ff_181_q));  // open: Qn, preset, reset
  D_Flip_Flop d_ff_182 (.D(d_ff_166_q), .clk(and_15_out), .Q(d_ff_182_q));  // open: Qn, preset, reset
  D_Flip_Flop d_ff_183 (.D(d_ff_167_q), .clk(and_17_out), .Q(d_ff_183_q));  // open: Qn, preset, reset
  D_Flip_Flop d_ff_184 (.D(d_ff_168_q), .clk(and_19_out), .Q(d_ff_184_q));  // open: Qn, preset, reset
  D_Flip_Flop d_ff_185 (.D(d_ff_169_q), .clk(and_21_out), .Q(d_ff_185_q));  // open: Qn, preset, reset
  D_Flip_Flop d_ff_186 (.D(d_ff_170_q), .clk(and_23_out), .Q(d_ff_186_q));  // open: Qn, preset, reset
  D_Flip_Flop d_ff_187 (.D(d_ff_171_q), .clk(and_25_out), .Q(d_ff_187_q));  // open: Qn, preset, reset
  D_Flip_Flop d_ff_188 (.D(d_ff_172_q), .clk(and_27_out), .Q(d_ff_188_q));  // open: Qn, preset, reset
  D_Flip_Flop d_ff_189 (.D(d_ff_173_q), .clk(and_29_out), .Q(d_ff_189_q));  // open: Qn, preset, reset
  D_Flip_Flop d_ff_190 (.D(d_ff_174_q), .clk(and_31_out), .Q(d_ff_190_q));  // open: Qn, preset, reset
  D_Flip_Flop d_ff_191 (.D(d_ff_175_q), .clk(and_33_out), .Q(d_ff_191_q));  // open: Qn, preset, reset
  D_Flip_Flop d_ff_192 (.D(d_ff_176_q), .clk(and_3_out), .Q(d_ff_192_q));  // open: Qn, preset, reset
  D_Flip_Flop d_ff_193 (.D(d_ff_177_q), .clk(and_5_out), .Q(d_ff_193_q));  // open: Qn, preset, reset
  D_Flip_Flop d_ff_194 (.D(d_ff_178_q), .clk(and_7_out), .Q(d_ff_194_q));  // open: Qn, preset, reset
  D_Flip_Flop d_ff_195 (.D(d_ff_179_q), .clk(and_9_out), .Q(d_ff_195_q));  // open: Qn, preset, reset
  D_Flip_Flop d_ff_196 (.D(d_ff_180_q), .clk(and_11_out), .Q(d_ff_196_q));  // open: Qn, preset, reset
  D_Flip_Flop d_ff_197 (.D(d_ff_181_q), .clk(and_13_out), .Q(d_ff_197_q));  // open: Qn, preset, reset
  D_Flip_Flop d_ff_198 (.D(d_ff_182_q), .clk(and_15_out), .Q(d_ff_198_q));  // open: Qn, preset, reset
  D_Flip_Flop d_ff_199 (.D(d_ff_183_q), .clk(and_17_out), .Q(d_ff_199_q));  // open: Qn, preset, reset
  D_Flip_Flop d_ff_200 (.D(d_ff_184_q), .clk(and_19_out), .Q(d_ff_200_q));  // open: Qn, preset, reset
  D_Flip_Flop d_ff_201 (.D(d_ff_185_q), .clk(and_21_out), .Q(d_ff_201_q));  // open: Qn, preset, reset
  D_Flip_Flop d_ff_202 (.D(d_ff_186_q), .clk(and_23_out), .Q(d_ff_202_q));  // open: Qn, preset, reset
  D_Flip_Flop d_ff_203 (.D(d_ff_187_q), .clk(and_25_out), .Q(d_ff_203_q));  // open: Qn, preset, reset
  D_Flip_Flop d_ff_204 (.D(d_ff_188_q), .clk(and_27_out), .Q(d_ff_204_q));  // open: Qn, preset, reset
  D_Flip_Flop d_ff_205 (.D(d_ff_189_q), .clk(and_29_out), .Q(d_ff_205_q));  // open: Qn, preset, reset
  D_Flip_Flop d_ff_206 (.D(d_ff_190_q), .clk(and_31_out), .Q(d_ff_206_q));  // open: Qn, preset, reset
  D_Flip_Flop d_ff_207 (.D(d_ff_191_q), .clk(and_33_out), .Q(d_ff_207_q));  // open: Qn, preset, reset
  D_Flip_Flop d_ff_208 (.D(d_ff_192_q), .clk(and_3_out), .Q(d_ff_208_q));  // open: Qn, preset, reset
  D_Flip_Flop d_ff_209 (.D(d_ff_193_q), .clk(and_5_out), .Q(d_ff_209_q));  // open: Qn, preset, reset
  D_Flip_Flop d_ff_210 (.D(d_ff_194_q), .clk(and_7_out), .Q(d_ff_210_q));  // open: Qn, preset, reset
  D_Flip_Flop d_ff_211 (.D(d_ff_195_q), .clk(and_9_out), .Q(d_ff_211_q));  // open: Qn, preset, reset
  D_Flip_Flop d_ff_212 (.D(d_ff_196_q), .clk(and_11_out), .Q(d_ff_212_q));  // open: Qn, preset, reset
  D_Flip_Flop d_ff_213 (.D(d_ff_197_q), .clk(and_13_out), .Q(d_ff_213_q));  // open: Qn, preset, reset
  D_Flip_Flop d_ff_214 (.D(d_ff_198_q), .clk(and_15_out), .Q(d_ff_214_q));  // open: Qn, preset, reset
  D_Flip_Flop d_ff_215 (.D(d_ff_199_q), .clk(and_17_out), .Q(d_ff_215_q));  // open: Qn, preset, reset
  D_Flip_Flop d_ff_216 (.D(d_ff_200_q), .clk(and_19_out), .Q(d_ff_216_q));  // open: Qn, preset, reset
  D_Flip_Flop d_ff_217 (.D(d_ff_201_q), .clk(and_21_out), .Q(d_ff_217_q));  // open: Qn, preset, reset
  D_Flip_Flop d_ff_218 (.D(d_ff_202_q), .clk(and_23_out), .Q(d_ff_218_q));  // open: Qn, preset, reset
  D_Flip_Flop d_ff_219 (.D(d_ff_203_q), .clk(and_25_out), .Q(d_ff_219_q));  // open: Qn, preset, reset
  D_Flip_Flop d_ff_220 (.D(d_ff_204_q), .clk(and_27_out), .Q(d_ff_220_q));  // open: Qn, preset, reset
  D_Flip_Flop d_ff_221 (.D(d_ff_205_q), .clk(and_29_out), .Q(d_ff_221_q));  // open: Qn, preset, reset
  D_Flip_Flop d_ff_222 (.D(d_ff_206_q), .clk(and_31_out), .Q(d_ff_222_q));  // open: Qn, preset, reset
  D_Flip_Flop d_ff_223 (.D(d_ff_207_q), .clk(and_33_out), .Q(d_ff_223_q));  // open: Qn, preset, reset
  D_Flip_Flop d_ff_224 (.D(d_ff_208_q), .clk(and_3_out), .Q(d_ff_224_q));  // open: Qn, preset, reset
  D_Flip_Flop d_ff_225 (.D(d_ff_209_q), .clk(and_5_out), .Q(d_ff_225_q));  // open: Qn, preset, reset
  D_Flip_Flop d_ff_226 (.D(d_ff_210_q), .clk(and_7_out), .Q(d_ff_226_q));  // open: Qn, preset, reset
  D_Flip_Flop d_ff_227 (.D(d_ff_211_q), .clk(and_9_out), .Q(d_ff_227_q));  // open: Qn, preset, reset
  D_Flip_Flop d_ff_228 (.D(d_ff_212_q), .clk(and_11_out), .Q(d_ff_228_q));  // open: Qn, preset, reset
  D_Flip_Flop d_ff_229 (.D(d_ff_213_q), .clk(and_13_out), .Q(d_ff_229_q));  // open: Qn, preset, reset
  D_Flip_Flop d_ff_230 (.D(d_ff_214_q), .clk(and_15_out), .Q(d_ff_230_q));  // open: Qn, preset, reset
  D_Flip_Flop d_ff_231 (.D(d_ff_215_q), .clk(and_17_out), .Q(d_ff_231_q));  // open: Qn, preset, reset
  D_Flip_Flop d_ff_232 (.D(d_ff_216_q), .clk(and_19_out), .Q(d_ff_232_q));  // open: Qn, preset, reset
  D_Flip_Flop d_ff_233 (.D(d_ff_217_q), .clk(and_21_out), .Q(d_ff_233_q));  // open: Qn, preset, reset
  D_Flip_Flop d_ff_234 (.D(d_ff_218_q), .clk(and_23_out), .Q(d_ff_234_q));  // open: Qn, preset, reset
  D_Flip_Flop d_ff_235 (.D(d_ff_219_q), .clk(and_25_out), .Q(d_ff_235_q));  // open: Qn, preset, reset
  D_Flip_Flop d_ff_236 (.D(d_ff_220_q), .clk(and_27_out), .Q(d_ff_236_q));  // open: Qn, preset, reset
  D_Flip_Flop d_ff_237 (.D(d_ff_221_q), .clk(and_29_out), .Q(d_ff_237_q));  // open: Qn, preset, reset
  D_Flip_Flop d_ff_238 (.D(d_ff_222_q), .clk(and_31_out), .Q(d_ff_238_q));  // open: Qn, preset, reset
  D_Flip_Flop d_ff_239 (.D(d_ff_223_q), .clk(and_33_out), .Q(d_ff_239_q));  // open: Qn, preset, reset
  D_Flip_Flop d_ff_240 (.D(d_ff_224_q), .clk(and_3_out));  // open: Q, Qn, preset, reset
  D_Flip_Flop d_ff_241 (.D(d_ff_225_q), .clk(and_5_out));  // open: Q, Qn, preset, reset
  D_Flip_Flop d_ff_242 (.D(d_ff_226_q), .clk(and_7_out));  // open: Q, Qn, preset, reset
  D_Flip_Flop d_ff_243 (.D(d_ff_227_q), .clk(and_9_out));  // open: Q, Qn, preset, reset
  D_Flip_Flop d_ff_244 (.D(d_ff_228_q), .clk(and_11_out));  // open: Q, Qn, preset, reset
  D_Flip_Flop d_ff_245 (.D(d_ff_229_q), .clk(and_13_out));  // open: Q, Qn, preset, reset
  D_Flip_Flop d_ff_246 (.D(d_ff_230_q), .clk(and_15_out));  // open: Q, Qn, preset, reset
  D_Flip_Flop d_ff_247 (.D(d_ff_231_q), .clk(and_17_out));  // open: Q, Qn, preset, reset
  D_Flip_Flop d_ff_248 (.D(d_ff_232_q), .clk(and_19_out));  // open: Q, Qn, preset, reset
  D_Flip_Flop d_ff_249 (.D(d_ff_233_q), .clk(and_21_out));  // open: Q, Qn, preset, reset
  D_Flip_Flop d_ff_250 (.D(d_ff_234_q), .clk(and_23_out));  // open: Q, Qn, preset, reset
  D_Flip_Flop d_ff_251 (.D(d_ff_235_q), .clk(and_25_out));  // open: Q, Qn, preset, reset
  D_Flip_Flop d_ff_252 (.D(d_ff_236_q), .clk(and_27_out));  // open: Q, Qn, preset, reset
  D_Flip_Flop d_ff_253 (.D(d_ff_237_q), .clk(and_29_out));  // open: Q, Qn, preset, reset
  D_Flip_Flop d_ff_254 (.D(d_ff_238_q), .clk(and_31_out));  // open: Q, Qn, preset, reset
  D_Flip_Flop d_ff_255 (.D(d_ff_239_q), .clk(and_33_out));  // open: Q, Qn, preset, reset
endmodule

module counter_14 (
  input  start,
  input  CLK,
  output CLK_A
);

  wire and_1_out, j_k_ff_1_q, j_k_ff_1_qn, j_k_ff_2_q, j_k_ff_2_qn, j_k_ff_3_q, j_k_ff_3_qn, j_k_ff_4_q,
       j_k_ff_4_qn, j_k_ff_5_q, j_k_ff_5_qn, j_k_ff_6_q, j_k_ff_6_qn, j_k_ff_7_q, j_k_ff_7_qn, j_k_ff_8_q,
       j_k_ff_8_qn, j_k_ff_9_q, j_k_ff_9_qn, j_k_ff_10_q, j_k_ff_10_qn, j_k_ff_11_q, j_k_ff_11_qn,
       j_k_ff_12_q, j_k_ff_12_qn, j_k_ff_13_q, j_k_ff_13_qn, j_k_ff_14_q, not_1_out, not_2_out;

  not not_1 (not_1_out, CLK_A);
  and and_1 (and_1_out, not_1_out, start);
  not not_2 (not_2_out, and_1_out);
  Transistor transistor_1 (.in(j_k_ff_1_q), .out(CLK_A), .gate(1'b0));
  J_K_Flip_Flop j_k_ff_1 (
    .J(and_1_out), .K(not_2_out), .clk(CLK), .Q(j_k_ff_1_q), .Qn(j_k_ff_1_qn));  // open: preset, reset
  Transistor transistor_2 (.in(j_k_ff_2_q), .out(CLK_A), .gate(1'b0));
  J_K_Flip_Flop j_k_ff_2 (
    .J(j_k_ff_1_q), .K(j_k_ff_1_qn), .clk(CLK), .Q(j_k_ff_2_q), .Qn(j_k_ff_2_qn));  // open: preset, reset
  Transistor transistor_3 (.in(j_k_ff_3_q), .out(CLK_A), .gate(1'b0));
  J_K_Flip_Flop j_k_ff_3 (
    .J(j_k_ff_2_q), .K(j_k_ff_2_qn), .clk(CLK), .Q(j_k_ff_3_q), .Qn(j_k_ff_3_qn));  // open: preset, reset
  Transistor transistor_4 (.in(j_k_ff_4_q), .out(CLK_A), .gate(1'b0));
  J_K_Flip_Flop j_k_ff_4 (
    .J(j_k_ff_3_q), .K(j_k_ff_3_qn), .clk(CLK), .Q(j_k_ff_4_q), .Qn(j_k_ff_4_qn));  // open: preset, reset
  Transistor transistor_5 (.in(j_k_ff_5_q), .out(CLK_A), .gate(1'b0));
  J_K_Flip_Flop j_k_ff_5 (
    .J(j_k_ff_4_q), .K(j_k_ff_4_qn), .clk(CLK), .Q(j_k_ff_5_q), .Qn(j_k_ff_5_qn));  // open: preset, reset
  Transistor transistor_6 (.in(j_k_ff_6_q), .out(CLK_A), .gate(1'b0));
  J_K_Flip_Flop j_k_ff_6 (
    .J(j_k_ff_5_q), .K(j_k_ff_5_qn), .clk(CLK), .Q(j_k_ff_6_q), .Qn(j_k_ff_6_qn));  // open: preset, reset
  Transistor transistor_7 (.in(j_k_ff_7_q), .out(CLK_A), .gate(1'b0));
  J_K_Flip_Flop j_k_ff_7 (
    .J(j_k_ff_6_q), .K(j_k_ff_6_qn), .clk(CLK), .Q(j_k_ff_7_q), .Qn(j_k_ff_7_qn));  // open: preset, reset
  J_K_Flip_Flop j_k_ff_8 (
    .J(j_k_ff_7_q), .K(j_k_ff_7_qn), .clk(CLK), .Q(j_k_ff_8_q), .Qn(j_k_ff_8_qn));  // open: preset, reset
  Transistor transistor_8 (.in(j_k_ff_8_q), .out(CLK_A), .gate(1'b0));
  J_K_Flip_Flop j_k_ff_9 (
    .J(j_k_ff_8_q), .K(j_k_ff_8_qn), .clk(CLK), .Q(j_k_ff_9_q), .Qn(j_k_ff_9_qn));  // open: preset, reset
  Transistor transistor_9 (.in(j_k_ff_9_q), .out(CLK_A), .gate(1'b0));
  J_K_Flip_Flop j_k_ff_10 (
    .J(j_k_ff_9_q), .K(j_k_ff_9_qn), .clk(CLK), .Q(j_k_ff_10_q), .Qn(j_k_ff_10_qn));  // open: preset, reset
  Transistor transistor_10 (.in(j_k_ff_10_q), .out(CLK_A), .gate(1'b0));
  J_K_Flip_Flop j_k_ff_11 (
    .J(j_k_ff_10_q), .K(j_k_ff_10_qn), .clk(CLK), .Q(j_k_ff_11_q), .Qn(j_k_ff_11_qn));  // open: preset, reset
  Transistor transistor_11 (.in(j_k_ff_11_q), .out(CLK_A), .gate(1'b0));
  J_K_Flip_Flop j_k_ff_12 (
    .J(j_k_ff_11_q), .K(j_k_ff_11_qn), .clk(CLK), .Q(j_k_ff_12_q), .Qn(j_k_ff_12_qn));  // open: preset, reset
  Transistor transistor_12 (.in(j_k_ff_12_q), .out(CLK_A), .gate(1'b0));
  J_K_Flip_Flop j_k_ff_13 (
    .J(j_k_ff_12_q), .K(j_k_ff_12_qn), .clk(CLK), .Q(j_k_ff_13_q), .Qn(j_k_ff_13_qn));  // open: preset, reset
  Transistor transistor_13 (.in(j_k_ff_13_q), .out(CLK_A), .gate(1'b0));
  J_K_Flip_Flop j_k_ff_14 (.J(j_k_ff_13_q), .K(j_k_ff_13_qn), .clk(CLK), .Q(j_k_ff_14_q));  // open: Qn, preset, reset
  Pull_Resistor pull_resistor_1 (.node(CLK_A));
  Transistor transistor_14 (.in(j_k_ff_14_q), .out(CLK_A), .gate(1'b0));
endmodule
